// Logisim project cpu21-riscv_8_流水线中断.circ as structural Verilog: 26 circuits, main circuit ◇单周期RISC-V
module \单周期RISC_V  (
  input  IR1,
  input  IR2,
  input  IR3,
  output RegWrite,
  output MemWrite,
  output [31:0] PC,
  output [31:0] IR,
  output [31:0] RDin,
  output [31:0] MDin,
  output [31:0] LedData
);

  wire alu_1_equal, alu_1_out_6, and_1_out, and_3_out, and_4_out, and_5_out, AUIPC, CLK, clock_1_out,
       comparator_1_eq, comparator_2_eq, comparator_2_lt, d_ff_1_q, ecall, Go, halt, IR1_t, IR2_t, IR3_t,
       IRA, IRB, IRC, isBranch, JAL, JALR, LHU, nand_1_out, not_1_out, not_2_out, or_1_out, or_2_out,
       or_7_out, RST, W1, W2, W3, \单周期硬布线控制器_1_alu_src , \单周期硬布线控制器_1_beq , \单周期硬布线控制器_1_bltu ,
       \单周期硬布线控制器_1_bne , \单周期硬布线控制器_1_memtoreg , \单周期硬布线控制器_1_s_type ;
  wire [3:0] \单周期硬布线控制器_1_alu_op ;
  wire [4:0] multiplexer_2_out, multiplexer_3_out;
  wire [11:0] multiplexer_4_out, shifter_1_out;
  wire [12:0] CNT_num;
  wire [15:0] multiplexer_8_out, \总周期数 ;
  wire [19:0] shifter_2_out;
  wire [31:0] adder_2_out, adder_3_out, alu_1_result, and_6_out, bit_extender_1_out, bit_extender_2_out,
       bit_extender_3_out, bit_extender_4_out, bit_extender_5_out, multiplexer_1_out, multiplexer_6_out,
       multiplexer_7_out, multiplexer_9_out, multiplexer_10_out, multiplexer_11_out, multiplexer_12_out,
       PC_4, R1, ram_1_data, shifter_3_out;

  Button \u_继续运行  (.out(Go));
  Button _1 (.out(IRA));
  Button _2 (.out(IRB));
  Button _3 (.out(IRC));
  LED #(.active("true")) led_1 (.in(W1));
  LED #(.active("true")) led_2 (.in(W2));
  LED #(.active("true")) led_3 (.in(W3));
  Hex_Digit_Display hex_digit_display_1 (.value(LedData[31:28]));  // open: dp
  not not_1 (not_1_out, halt);
  Hex_Digit_Display hex_digit_display_2 (.value(LedData[27:24]));  // open: dp
  Hex_Digit_Display hex_digit_display_3 (.value(LedData[23:20]));  // open: dp
  Multiplexer #(.select(1), .width(32), .disabled("Z"), .enable("false")) multiplexer_1 (
    .in0(PC_4), .in1(multiplexer_12_out), .out(multiplexer_1_out), .sel(or_1_out));
  or or_1 (or_1_out, JALR, JAL, isBranch);
  Counter #(.width(16), .max('hffff), .ongoal("wrap"), .trigger("rising"), .behavior("new")) counter_1 (
    .count(not_1_out), .Q(\总周期数 ), .clk(CLK));  // open: load, D, carry, clr, preset, down
  Hex_Digit_Display hex_digit_display_4 (.value(LedData[19:16]));  // open: dp
  Hex_Digit_Display hex_digit_display_5 (.value(LedData[15:12]));  // open: dp
  Comparator #(.width(32), .mode("twosComplement")) comparator_1 (
    .a(R1), .b(32'h22), .eq(comparator_1_eq));  // open: gt, lt
  Hex_Digit_Display hex_digit_display_6 (.value(LedData[7:4]));  // open: dp
  Hex_Digit_Display hex_digit_display_7 (.value(LedData[11:8]));  // open: dp
  // Probe on \总周期数 
  Button button_1 (.out(RST));
  or or_2 (or_2_out, Go, not_2_out);
  not not_2 (not_2_out, halt);
  and and_1 (and_1_out, ecall, comparator_1_eq);
  Hex_Digit_Display hex_digit_display_8 (.value(LedData[3:0]));  // open: dp
  Register #(.width(32), .trigger("rising"), .Select("low")) u_PC (
    .D(multiplexer_1_out), .en(or_2_out), .Q(PC), .clk(CLK), .clr(RST));
  and and_2 (halt, ecall, ~comparator_1_eq);  // AND_Gate
  Register #(.width(32), .trigger("rising"), .Select("low")) register_1 (
    .D(MDin), .en(and_1_out), .Q(LedData), .clk(CLK));  // open: clr
  Adder #(.width(32)) adder_1 (.a(PC), .b(32'h4), .out(PC_4));  // open: cin, cout
  or or_3 (IR1_t, IR1, IRA);
  or or_4 (IR2_t, IR2, IRB);
  // RiscV_Probe riscv_probe_1: pin names not known; wires that end beside it: IR
  ROM #(.addrWidth(10), .dataWidth(32), .Select("high")) rom_1 (.addr(PC[11:2]), .data(IR));
  or or_5 (IR3_t, IR3, IRC);
  \单周期硬布线控制器  \u_单周期硬布线控制器_1  (
    .Funct({IR[30], IR[25], IR[14:12]}), .OP(IR[6:2]), .ALU_OP(\单周期硬布线控制器_1_alu_op ),
    .MemToReg(\单周期硬布线控制器_1_memtoreg ), .MemWrite(MemWrite), .ALU_SRC(\单周期硬布线控制器_1_alu_src ),
    .RegWrite(RegWrite), .ecall(ecall), .S_type(\单周期硬布线控制器_1_s_type ), .Jalr(JALR), .Beq(\单周期硬布线控制器_1_beq ),
    .JAL(JAL), .Bne(\单周期硬布线控制器_1_bne ), .in_3(IR[21]), .AUIPC(AUIPC), .LHU(LHU), .BLTU(\单周期硬布线控制器_1_bltu ));  // open: uret, rs1_used, rs2_used, CSRRSI, CSRRCI
  Multiplexer #(.select(1), .width(5), .disabled("Z"), .enable("false")) multiplexer_2 (
    .in0(IR[19:15]), .in1(5'b10001), .out(multiplexer_2_out), .sel(ecall));
  assign bit_extender_1_out = {{12{IR[31]}}, IR[31:12]};  // Bit_Extender bit_extender_1
  Multiplexer #(.select(1), .width(5), .disabled("Z"), .enable("false")) multiplexer_3 (
    .in0(IR[24:20]), .in1(5'b01010), .out(multiplexer_3_out), .sel(ecall));
  Multiplexer #(.select(1), .width(12), .disabled("Z"), .enable("false")) multiplexer_4 (
    .in0(IR[31:20]), .in1({IR[31:25], IR[11:7]}), .out(multiplexer_4_out), .sel(\单周期硬布线控制器_1_s_type ));
  Shifter #(.width(12), .shift("ll")) shifter_1 (
    .in({IR[31], IR[7], IR[30:25], IR[11:8]}), .\dist (4'b0001), .out(shifter_1_out));
  Shifter #(.width(20), .shift("ll")) shifter_2 (
    .in({IR[31], IR[19:12], IR[20], IR[30:21]}), .\dist (5'b00001), .out(shifter_2_out));
  Shifter #(.width(32), .shift("ll")) shifter_3 (.in(bit_extender_1_out), .\dist (5'b01100), .out(shifter_3_out));
  assign bit_extender_2_out = {{20{multiplexer_4_out[11]}}, multiplexer_4_out};  // Bit_Extender bit_extender_2
  Multiplexer #(.select(1), .width(32), .disabled("Z"), .enable("false")) multiplexer_5 (
    .in0(multiplexer_9_out), .in1(bit_extender_5_out), .out(RDin), .sel(LHU));
  assign bit_extender_3_out = {{20{shifter_1_out[11]}}, shifter_1_out};  // Bit_Extender bit_extender_3
  assign bit_extender_4_out = {{12{shifter_2_out[19]}}, shifter_2_out};  // Bit_Extender bit_extender_4
  Regifile regifile_1 (
    .Din(RDin), .Clk(CLK), .R1(R1), .R2(MDin), .WE(RegWrite), .W_num(IR[11:7]), .R1_num(multiplexer_2_out),
    .R2_num(multiplexer_3_out));
  Adder #(.width(32)) adder_2 (.a(PC), .b(shifter_3_out), .out(adder_2_out));  // open: cin, cout
  Multiplexer #(.select(1), .width(32), .disabled("Z"), .enable("false")) multiplexer_6 (
    .in0(MDin), .in1(bit_extender_2_out), .out(multiplexer_6_out), .sel(\单周期硬布线控制器_1_alu_src ));
  assign bit_extender_5_out = {{16{1'b0}}, multiplexer_8_out};  // Bit_Extender bit_extender_5
  Multiplexer #(.select(1), .width(32), .disabled("Z"), .enable("false")) multiplexer_7 (
    .in0(bit_extender_3_out), .in1(bit_extender_4_out), .out(multiplexer_7_out), .sel(JAL));
  ALU alu_1 (
    .X(R1), .Y(multiplexer_6_out), .AluOP(\单周期硬布线控制器_1_alu_op ), .Equal(alu_1_equal), .Result(alu_1_result),
    .out_6(alu_1_out_6));  // open: Result_2, out_4
  Multiplexer #(.select(1), .width(16), .disabled("Z"), .enable("false")) multiplexer_8 (
    .in0(multiplexer_9_out[15:0]), .in1(multiplexer_9_out[31:16]), .out(multiplexer_8_out),
    .sel(alu_1_result[1]));
  Adder #(.width(32)) adder_3 (.a(PC), .b(multiplexer_7_out), .out(adder_3_out));  // open: cin, cout
  and and_3 (and_3_out, \单周期硬布线控制器_1_bltu , alu_1_out_6);
  and and_4 (and_4_out, alu_1_equal, \单周期硬布线控制器_1_beq );
  and and_5 (and_5_out, ~alu_1_equal, \单周期硬布线控制器_1_bne );  // AND_Gate
  Multiplexer #(.select(1), .width(32), .disabled("Z"), .enable("false")) multiplexer_9 (
    .in0(multiplexer_10_out), .in1(adder_2_out), .out(multiplexer_9_out), .sel(AUIPC));
  D_Flip_Flop #(.trigger("high"), .Pre_Clr_Positions("LEGACY"), .NegatePresetClear("false"), .enable("true"), .NewFFLayout("false")) d_ff_1 (.Q(d_ff_1_q));  // open: clk, D, Qn, preset, en, reset
  // Probe on 13'h8a
  Multiplexer #(.select(1), .width(32), .disabled("Z"), .enable("false")) multiplexer_10 (
    .in0(multiplexer_11_out), .in1(PC_4), .out(multiplexer_10_out), .sel(or_7_out));
  Comparator #(.width(13), .mode("twosComplement")) comparator_2 (
    .a(CNT_num), .b(13'h8a), .eq(comparator_2_eq), .lt(comparator_2_lt));  // open: gt
  Clock #(.highDuration(1), .lowDuration(1)) clock_1 (.out(clock_1_out));
  or or_6 (isBranch, and_3_out, and_4_out, and_5_out);
  RAM #(.addrWidth(10), .dataWidth(32), .bus("separate"), .Select("high")) ram_1 (
    .addr(alu_1_result[11:2]), .din(MDin), .data(ram_1_data), .str(MemWrite), .sel(1'b1), .clk(CLK),
    .ld(1'b1), .clr(RST));
  or or_7 (or_7_out, JALR, JAL);
  Counter #(.width(13), .max('h1fff), .ongoal("stay"), .trigger("rising"), .behavior("old")) counter_2 (
    .count(comparator_2_lt), .Q(CNT_num), .clk(clock_1_out));  // open: load, D, carry, clr, preset
  Multiplexer #(.select(1), .width(32), .disabled("Z"), .enable("false")) multiplexer_11 (
    .in0(alu_1_result), .in1(ram_1_data), .out(multiplexer_11_out), .sel(\单周期硬布线控制器_1_memtoreg ));
  assign and_6_out = multiplexer_11_out & 32'hfffffffe;  // AND_Gate and_6, 32 bits wide
  Multiplexer #(.select(1), .width(32), .disabled("Z"), .enable("false")) multiplexer_12 (
    .in0(adder_3_out), .in1(and_6_out), .out(multiplexer_12_out), .sel(JALR));
  nand nand_1 (nand_1_out, d_ff_1_q, comparator_2_eq);
  assign CLK = nand_1_out ? clock_1_out : 1'bz;  // Controlled_Buffer controlled_buffer_1
  Pull_Resistor #(.pull(1)) pull_resistor_1 (.node(CLK));

  // Notes on the sheet:
  //   中断源
  //   中断等待指示
  //   数码管输出应该用寄存器锁存，否则显示数据只能一闪而过
  //   数码管输出
  //   指令探针
  //   指令存储器
  //   contents of rom_1 (hex, n*v repeats v):
  //   100493 100006f 100493 200913 300993 100006f 100493 200913 300993 100006f 100493 200913 300993
  //   100006f 100493 200913 300993 41c000ef 100413 100493 1f49493 900533 2200893 73 24d493 48463 fedff06f
  //   900533 2200893 73 100493 249493 900533 2200893 73 48463 fedff06f 100493 1f49493 900533 2200893 73
  //   4034d493 900533 2200893 73 4044d493 900533 2200893 73 4044d493 900533 2200893 73 4044d493 900533
  //   2200893 73 4044d493 900533 2200893 73 4044d493 900533 2200893 73 4044d493 900533 2200893 73 4044d493
  //   900533 2200893 73 100413 1f41993 41f9d993 433 c00913 300b13 140413 f47413 800293 100313 499993
  //   89e9b3 1300533 2200893 73 406282b3 fe0294e3 140413 f00f93 1f47433 1c41413 800293 100313 49d993
  //   89e9b3 1300533 2200893 73 406282b3 fe0294e3 1c45413 406b0b33 b0463 f95ff06f 2b3 fff2c293 829293
  //   ff2e293 500533 2200893 73 fff00413 493 84a023 140413 448493 84a023 140413 448493 84a023 140413
  //   448493 84a023 140413 448493 84a023 140413 448493 84a023 140413 448493 84a023 140413 448493 84a023
  //   140413 448493 84a023 140413 448493 84a023 140413 448493 84a023 140413 448493 84a023 140413 448493
  //   84a023 140413 448493 84a023 140413 448493 84a023 140413 448493 84a023 140413 448493 140413 433
  //   3c00493 42983 4aa03 149a2b3 28663 134a023 1442023 ffc48493 fe9412e3 800533 2200893 73 440413 3c00493
  //   fc9416e3 3200893 73 fff00293 7700493 849493 7748493 900533 2200893 73 1000e13 54c4b3 900533 2200893
  //   73 fffe0e13 fe0e16e3 a00893 73 13 430497 900533 2200893 73 430497 900533 2200893 73 430497 900533
  //   2200893 73 430497 900533 2200893 73 430497 900533 2200893 73 430497 900533 2200893 73 430497 900533
  //   2200893 73 430497 900533 2200893 73 a00893 73 313 1000e13 8400493 849493 8348493 400913 891913
  //   490913 849493 8248493 849493 8148493 891913 490913 891913 490913 932023 12484b3 430313 fffe0e13
  //   fe0e18e3 2000e13 313 35483 900533 2200893 73 230313 fffe0e13 fe0e14e3 a00893 73 ff100493 900533
  //   2200893 73 148493 fe9068e3 900533 2200893 73 a00893 73 a00893 73 413 140413 800533 2200893 73 240413
  //   800533 2200893 73 340413 800533 2200893 73 440413 800533 2200893 73 540413 800533 2200893 73 640413
  //   800533 2200893 73 740413 800533 2200893 73 840413 800533 2200893 2200893 73 8067
  //   Beq,Bne,Bltu
  //   AUIPC
  //   指令字
  //   JAL
  //   JAL
  //   JALR
  //   Beq
  //   Bne
  //   MemToReg
  //   MemWrite
  //   AluOP
  //   AluSrcB
  //   RegWrite
  //   为方便自动评测，需要输出PC，IR，寄存器堆写如数据RDin
  //   RAM写使能MemWrite、RAM写入数据MDin等信号
  //   控制位
  //   暂停节拍，不能为0
  //   数据存储器
  //   戳工具置1进入计数暂停模式，ctrl+k时钟自动运行到对应节拍暂停
  //   ctrl+k关闭时钟连续运行，将控制位置零，进入单步调试模式调试
  //   用这个时钟源需要去掉电路中的其他时钟源
  //   可计数暂停的时钟源
endmodule

// 单周期硬布线控制器
module \单周期硬布线控制器  (
  input  [4:0] OP,
  input  [4:0] Funct,
  input  in_3,
  output [3:0] ALU_OP,
  output uret,
  output MemToReg,
  output ecall,
  output MemWrite,
  output ALU_SRC,
  output RegWrite,
  output S_type,
  output Beq,
  output Bne,
  output Jalr,
  output JAL,
  output AUIPC,
  output LHU,
  output BLTU,
  output rs1_used,
  output rs2_used,
  output CSRRSI,
  output CSRRCI
);

  wire \控制信号自动生成_1_ecall ;

  \运算控制器自动生成  \u_运算控制器自动生成_1  (
    .OP2(OP[0]), .OP3(OP[1]), .OP4(OP[2]), .OP5(OP[3]), .OP6(OP[4]), .F12(Funct[0]), .F13(Funct[1]),
    .F14(Funct[2]), .F25(Funct[3]), .F30(Funct[4]), .S0(ALU_OP[0]), .S1(ALU_OP[1]), .S2(ALU_OP[2]),
    .S3(ALU_OP[3]));
  \控制信号自动生成  \u_控制信号自动生成_1  (
    .OP2(OP[0]), .OP3(OP[1]), .OP4(OP[2]), .OP5(OP[3]), .MemToReg(MemToReg), .OP6(OP[4]), .F12(Funct[0]),
    .F13(Funct[1]), .F14(Funct[2]), .F25(Funct[3]), .F30(Funct[4]), .MemWrite(MemWrite), .ALU_SRC(ALU_SRC),
    .RegWrite(RegWrite), .ecall(\控制信号自动生成_1_ecall ), .S_Type(S_type), .BEQ(Beq), .BNE(Bne), .JALR(Jalr),
    .JAL(JAL), .AUIPC(AUIPC), .LHU(LHU), .BLTU(BLTU));
  R1_R2_used r1_r2_used_1 (
    .OP2(OP[0]), .OP3(OP[1]), .OP4(OP[2]), .OP5(OP[3]), .OP6(OP[4]), .F12(Funct[0]), .F13(Funct[1]),
    .F14(Funct[2]), .F25(Funct[3]), .F30(Funct[4]), .R1_used(rs1_used), .R2_used(rs2_used));
  \中断相关指令  \u_中断相关指令_1  (
    .OP2(OP[0]), .OP3(OP[1]), .OP4(OP[2]), .OP5(OP[3]), .OP6(OP[4]), .F12(Funct[0]), .F13(Funct[1]),
    .F14(Funct[2]), .F25(Funct[3]), .F30(Funct[4]), .CSRRSI(CSRRSI), .CSRRCI(CSRRCI));
  and and_1 (uret, in_3, \控制信号自动生成_1_ecall );
  and and_2 (ecall, ~in_3, \控制信号自动生成_1_ecall );  // AND_Gate

  // Other names for the same wires on the sheet: IR21 = in_3; OP_CODE[4:0] = OP

  // Notes on the sheet:
  //   运算器控制器，根据指令生成运算器功能选择信号
  //   控制信号生成，产生数据通路需要的其他控制信号
endmodule

// 运算器控制器
module \运算控制器自动生成  (
  input  OP2,
  input  OP3,
  input  OP4,
  input  OP5,
  input  OP6,
  input  F12,
  input  F13,
  input  F14,
  input  F25,
  input  F30,
  output S0,
  output S1,
  output S2,
  output S3
);

  wire and_1_out, and_2_out, and_3_out, and_4_out, and_5_out, and_6_out, and_7_out, and_8_out, and_9_out,
       and_10_out, and_11_out, and_12_out, and_13_out, and_14_out, and_15_out, and_16_out, and_17_out,
       and_18_out, and_19_out, and_20_out, and_21_out, and_22_out, and_23_out, and_24_out, and_25_out,
       and_26_out, and_27_out, and_28_out, and_29_out, and_30_out, and_31_out, and_32_out, and_33_out,
       and_34_out, and_35_out, and_36_out, and_37_out, and_38_out, not_1_out, not_2_out, not_3_out,
       not_4_out, not_5_out, not_6_out, not_7_out, not_8_out, not_9_out, not_10_out, not_11_out, not_12_out,
       not_13_out, not_14_out, not_15_out, not_16_out, not_17_out, not_18_out, not_19_out, not_20_out,
       not_21_out, not_22_out, not_23_out, not_24_out, not_25_out, not_26_out, not_27_out, not_28_out,
       not_29_out, not_30_out, not_31_out, not_32_out, not_33_out, not_34_out, not_35_out, not_36_out,
       not_37_out, not_38_out, not_39_out, not_40_out, not_41_out, not_42_out, not_43_out, not_44_out,
       not_45_out, not_46_out, not_47_out, not_48_out, not_49_out, not_50_out, not_51_out, not_52_out,
       not_53_out, not_54_out, not_55_out, not_56_out, not_57_out, not_58_out, not_59_out, not_60_out,
       not_61_out, not_62_out, not_63_out, not_64_out, not_65_out, not_66_out, not_67_out, not_68_out,
       not_69_out, not_70_out, not_71_out, not_72_out, not_73_out, not_74_out, not_75_out, not_76_out,
       not_77_out, not_78_out, not_79_out, not_80_out, not_81_out, not_82_out, not_83_out, not_84_out,
       not_85_out, not_86_out, not_87_out, not_88_out, not_89_out, not_90_out, not_91_out, not_92_out,
       not_93_out, not_94_out, not_95_out, not_96_out, not_97_out, not_98_out, not_99_out, not_100_out,
       not_101_out, not_102_out, not_103_out, not_104_out, not_105_out, not_106_out, not_107_out,
       not_108_out, not_109_out, not_110_out, not_111_out, not_112_out, not_113_out, not_114_out,
       not_115_out, not_116_out, not_117_out, not_118_out, not_119_out, not_120_out, not_121_out,
       not_122_out, not_123_out, not_124_out, not_125_out, not_126_out, not_127_out, not_128_out,
       not_129_out, not_130_out, not_131_out, not_132_out, not_133_out, not_134_out, not_135_out,
       not_136_out, not_137_out, not_138_out, not_139_out, not_140_out, not_141_out, not_142_out,
       not_143_out, not_144_out, not_145_out, not_146_out, not_147_out, not_148_out, not_149_out,
       not_150_out, not_151_out, not_152_out, not_153_out, not_154_out, not_155_out, not_156_out,
       not_157_out, not_158_out, not_159_out, not_160_out, not_161_out, not_162_out, not_163_out,
       not_164_out, not_165_out, not_166_out, not_167_out, not_168_out, not_169_out, not_170_out,
       not_171_out, not_172_out, not_173_out, not_174_out, not_175_out, not_176_out, not_177_out,
       not_178_out, not_179_out, not_180_out, not_181_out, not_182_out, not_183_out, not_184_out,
       not_185_out, not_186_out, not_187_out, not_188_out, not_189_out, not_190_out, not_191_out,
       not_192_out, not_193_out, not_194_out, not_195_out, not_196_out, not_197_out, not_198_out,
       not_199_out, not_200_out, not_201_out, not_202_out, not_203_out, not_204_out, not_205_out,
       not_206_out, not_207_out, not_208_out, not_209_out, not_210_out, not_211_out, not_212_out,
       not_213_out, not_214_out, not_215_out, not_216_out, not_217_out, not_218_out, not_219_out,
       not_220_out, not_221_out, not_222_out, not_223_out, not_224_out;

  not not_1 (not_1_out, F30);
  not not_2 (not_2_out, F25);
  not not_3 (not_3_out, F14);
  not not_4 (not_4_out, F13);
  not not_5 (not_5_out, F12);
  not not_6 (not_6_out, OP6);
  not not_7 (not_7_out, OP3);
  not not_8 (not_8_out, OP2);
  not not_9 (not_9_out, F30);
  not not_10 (not_10_out, F25);
  not not_11 (not_11_out, OP6);
  not not_12 (not_12_out, OP3);
  not not_13 (not_13_out, OP2);
  not not_14 (not_14_out, F30);
  not not_15 (not_15_out, F25);
  not not_16 (not_16_out, F14);
  not not_17 (not_17_out, F12);
  not not_18 (not_18_out, OP6);
  not not_19 (not_19_out, OP3);
  not not_20 (not_20_out, OP2);
  not not_21 (not_21_out, F14);
  not not_22 (not_22_out, F13);
  not not_23 (not_23_out, F12);
  not not_24 (not_24_out, OP6);
  not not_25 (not_25_out, OP5);
  not not_26 (not_26_out, OP3);
  not not_27 (not_27_out, OP2);
  not not_28 (not_28_out, OP6);
  not not_29 (not_29_out, OP5);
  not not_30 (not_30_out, OP3);
  not not_31 (not_31_out, OP2);
  not not_32 (not_32_out, F13);
  not not_33 (not_33_out, F12);
  not not_34 (not_34_out, OP6);
  not not_35 (not_35_out, OP5);
  not not_36 (not_36_out, OP3);
  not not_37 (not_37_out, OP2);
  not not_38 (not_38_out, F14);
  not not_39 (not_39_out, F12);
  not not_40 (not_40_out, OP6);
  not not_41 (not_41_out, OP5);
  not not_42 (not_42_out, OP3);
  not not_43 (not_43_out, OP2);
  not not_44 (not_44_out, F25);
  not not_45 (not_45_out, F13);
  not not_46 (not_46_out, OP6);
  not not_47 (not_47_out, OP5);
  not not_48 (not_48_out, OP3);
  not not_49 (not_49_out, OP2);
  not not_50 (not_50_out, F14);
  not not_51 (not_51_out, F13);
  not not_52 (not_52_out, F12);
  not not_53 (not_53_out, OP4);
  not not_54 (not_54_out, OP3);
  not not_55 (not_55_out, F30);
  not not_56 (not_56_out, F25);
  not not_57 (not_57_out, F13);
  not not_58 (not_58_out, F12);
  not not_59 (not_59_out, OP6);
  not not_60 (not_60_out, OP3);
  not not_61 (not_61_out, OP2);
  not not_62 (not_62_out, F13);
  not not_63 (not_63_out, OP6);
  not not_64 (not_64_out, OP5);
  not not_65 (not_65_out, OP4);
  not not_66 (not_66_out, OP3);
  not not_67 (not_67_out, OP2);
  not not_68 (not_68_out, F25);
  not not_69 (not_69_out, F14);
  not not_70 (not_70_out, F13);
  not not_71 (not_71_out, F12);
  not not_72 (not_72_out, OP6);
  not not_73 (not_73_out, OP3);
  not not_74 (not_74_out, OP2);
  not not_75 (not_75_out, F30);
  not not_76 (not_76_out, F25);
  not not_77 (not_77_out, OP6);
  not not_78 (not_78_out, OP3);
  not not_79 (not_79_out, OP2);
  not not_80 (not_80_out, F30);
  not not_81 (not_81_out, F25);
  not not_82 (not_82_out, F14);
  not not_83 (not_83_out, F12);
  not not_84 (not_84_out, OP6);
  not not_85 (not_85_out, OP3);
  not not_86 (not_86_out, OP2);
  not not_87 (not_87_out, OP6);
  not not_88 (not_88_out, OP5);
  not not_89 (not_89_out, OP3);
  not not_90 (not_90_out, OP2);
  not not_91 (not_91_out, F14);
  not not_92 (not_92_out, F12);
  not not_93 (not_93_out, OP6);
  not not_94 (not_94_out, OP5);
  not not_95 (not_95_out, OP3);
  not not_96 (not_96_out, OP2);
  not not_97 (not_97_out, F30);
  not not_98 (not_98_out, F25);
  not not_99 (not_99_out, F13);
  not not_100 (not_100_out, OP6);
  not not_101 (not_101_out, OP5);
  not not_102 (not_102_out, OP3);
  not not_103 (not_103_out, OP2);
  not not_104 (not_104_out, F14);
  not not_105 (not_105_out, F13);
  not not_106 (not_106_out, F12);
  not not_107 (not_107_out, OP4);
  not not_108 (not_108_out, OP3);
  not not_109 (not_109_out, OP2);
  not not_110 (not_110_out, F14);
  not not_111 (not_111_out, F13);
  not not_112 (not_112_out, OP4);
  not not_113 (not_113_out, OP3);
  not not_114 (not_114_out, OP2);
  not not_115 (not_115_out, F30);
  not not_116 (not_116_out, F25);
  not not_117 (not_117_out, F14);
  not not_118 (not_118_out, F13);
  not not_119 (not_119_out, F12);
  not not_120 (not_120_out, OP6);
  not not_121 (not_121_out, OP3);
  not not_122 (not_122_out, OP2);
  not not_123 (not_123_out, F25);
  not not_124 (not_124_out, F14);
  not not_125 (not_125_out, F13);
  not not_126 (not_126_out, F12);
  not not_127 (not_127_out, OP6);
  not not_128 (not_128_out, OP3);
  not not_129 (not_129_out, OP2);
  not not_130 (not_130_out, F30);
  not not_131 (not_131_out, F25);
  not not_132 (not_132_out, OP6);
  not not_133 (not_133_out, OP3);
  not not_134 (not_134_out, OP2);
  not not_135 (not_135_out, F30);
  not not_136 (not_136_out, F25);
  not not_137 (not_137_out, F14);
  not not_138 (not_138_out, OP6);
  not not_139 (not_139_out, OP3);
  not not_140 (not_140_out, OP2);
  not not_141 (not_141_out, F14);
  not not_142 (not_142_out, F13);
  not not_143 (not_143_out, F12);
  not not_144 (not_144_out, OP6);
  not not_145 (not_145_out, OP5);
  not not_146 (not_146_out, OP3);
  not not_147 (not_147_out, OP2);
  not not_148 (not_148_out, OP6);
  not not_149 (not_149_out, OP5);
  not not_150 (not_150_out, OP3);
  not not_151 (not_151_out, OP2);
  not not_152 (not_152_out, F14);
  not not_153 (not_153_out, F13);
  not not_154 (not_154_out, F12);
  not not_155 (not_155_out, OP4);
  not not_156 (not_156_out, OP3);
  not not_157 (not_157_out, OP2);
  not not_158 (not_158_out, F14);
  not not_159 (not_159_out, F13);
  not not_160 (not_160_out, OP4);
  not not_161 (not_161_out, OP3);
  not not_162 (not_162_out, OP2);
  not not_163 (not_163_out, F14);
  not not_164 (not_164_out, F13);
  not not_165 (not_165_out, F12);
  not not_166 (not_166_out, OP4);
  not not_167 (not_167_out, OP3);
  not not_168 (not_168_out, F13);
  not not_169 (not_169_out, OP6);
  not not_170 (not_170_out, OP5);
  not not_171 (not_171_out, OP4);
  not not_172 (not_172_out, OP3);
  not not_173 (not_173_out, OP2);
  not not_174 (not_174_out, F12);
  not not_175 (not_175_out, OP4);
  not not_176 (not_176_out, OP3);
  not not_177 (not_177_out, OP2);
  not not_178 (not_178_out, F30);
  not not_179 (not_179_out, F25);
  not not_180 (not_180_out, F12);
  not not_181 (not_181_out, OP6);
  not not_182 (not_182_out, OP3);
  not not_183 (not_183_out, OP2);
  not not_184 (not_184_out, F30);
  not not_185 (not_185_out, F25);
  not not_186 (not_186_out, F14);
  not not_187 (not_187_out, F12);
  not not_188 (not_188_out, OP6);
  not not_189 (not_189_out, OP3);
  not not_190 (not_190_out, OP2);
  not not_191 (not_191_out, F30);
  not not_192 (not_192_out, F25);
  not not_193 (not_193_out, F14);
  not not_194 (not_194_out, OP6);
  not not_195 (not_195_out, OP3);
  not not_196 (not_196_out, OP2);
  not not_197 (not_197_out, F12);
  not not_198 (not_198_out, OP6);
  not not_199 (not_199_out, OP5);
  not not_200 (not_200_out, OP3);
  not not_201 (not_201_out, OP2);
  not not_202 (not_202_out, F13);
  not not_203 (not_203_out, F12);
  not not_204 (not_204_out, OP6);
  not not_205 (not_205_out, OP5);
  not not_206 (not_206_out, OP3);
  not not_207 (not_207_out, OP2);
  not not_208 (not_208_out, F14);
  not not_209 (not_209_out, F12);
  not not_210 (not_210_out, OP6);
  not not_211 (not_211_out, OP5);
  not not_212 (not_212_out, OP3);
  not not_213 (not_213_out, OP2);
  not not_214 (not_214_out, F30);
  not not_215 (not_215_out, F25);
  not not_216 (not_216_out, F13);
  not not_217 (not_217_out, F12);
  not not_218 (not_218_out, OP6);
  not not_219 (not_219_out, OP3);
  not not_220 (not_220_out, OP2);
  not not_221 (not_221_out, F12);
  not not_222 (not_222_out, OP4);
  not not_223 (not_223_out, OP3);
  not not_224 (not_224_out, OP2);
  and and_1 (and_1_out, not_1_out, not_2_out, not_3_out, not_4_out, not_5_out, not_6_out, OP5, OP4, not_7_out, not_8_out);
  and and_2 (and_2_out, not_9_out, not_10_out, F14, F13, F12, not_11_out, OP5, OP4, not_12_out, not_13_out);
  and and_3 (and_3_out, not_14_out, not_15_out, not_16_out, F13, not_17_out, not_18_out, OP5, OP4, not_19_out, not_20_out);
  and and_4 (and_4_out, not_21_out, not_22_out, not_23_out, not_24_out, not_25_out, OP4, not_26_out, not_27_out);
  and and_5 (and_5_out, F14, F13, F12, not_28_out, not_29_out, OP4, not_30_out, not_31_out);
  and and_6 (and_6_out, F14, not_32_out, not_33_out, not_34_out, not_35_out, OP4, not_36_out, not_37_out);
  and and_7 (and_7_out, not_38_out, F13, not_39_out, not_40_out, not_41_out, OP4, not_42_out, not_43_out);
  and and_8 (and_8_out, F30, not_44_out, F14, not_45_out, F12, not_46_out, not_47_out, OP4, not_48_out, not_49_out);
  and and_9 (and_9_out, not_50_out, not_51_out, not_52_out, OP6, OP5, not_53_out, not_54_out, OP2);
  and and_10 (and_10_out, not_55_out, not_56_out, F14, not_57_out, not_58_out, not_59_out, OP5, OP4, not_60_out, not_61_out);
  and and_11 (and_11_out, F14, not_62_out, F12, not_63_out, not_64_out, not_65_out, not_66_out, not_67_out);
  and and_12 (and_12_out, F30, not_68_out, not_69_out, not_70_out, not_71_out, not_72_out, OP5, OP4, not_73_out, not_74_out);
  and and_13 (and_13_out, not_75_out, not_76_out, F14, F13, F12, not_77_out, OP5, OP4, not_78_out, not_79_out);
  and and_14 (and_14_out, not_80_out, not_81_out, not_82_out, F13, not_83_out, not_84_out, OP5, OP4, not_85_out, not_86_out);
  and and_15 (and_15_out, F14, F13, F12, not_87_out, not_88_out, OP4, not_89_out, not_90_out);
  and and_16 (and_16_out, not_91_out, F13, not_92_out, not_93_out, not_94_out, OP4, not_95_out, not_96_out);
  and and_17 (and_17_out, not_97_out, not_98_out, F14, not_99_out, F12, not_100_out, not_101_out, OP4, not_102_out, not_103_out);
  and and_18 (and_18_out, not_104_out, not_105_out, not_106_out, OP6, OP5, not_107_out, not_108_out, not_109_out);
  and and_19 (and_19_out, not_110_out, not_111_out, F12, OP6, OP5, not_112_out, not_113_out, not_114_out);
  and and_20 (and_20_out, not_115_out, not_116_out, not_117_out, not_118_out, not_119_out, not_120_out, OP5, OP4, not_121_out, not_122_out);
  and and_21 (and_21_out, F30, not_123_out, not_124_out, not_125_out, not_126_out, not_127_out, OP5, OP4, not_128_out, not_129_out);
  and and_22 (and_22_out, not_130_out, not_131_out, F14, F13, F12, not_132_out, OP5, OP4, not_133_out, not_134_out);
  and and_23 (and_23_out, not_135_out, not_136_out, not_137_out, F13, F12, not_138_out, OP5, OP4, not_139_out, not_140_out);
  and and_24 (and_24_out, not_141_out, not_142_out, not_143_out, not_144_out, not_145_out, OP4, not_146_out, not_147_out);
  and and_25 (and_25_out, F14, F13, F12, not_148_out, not_149_out, OP4, not_150_out, not_151_out);
  and and_26 (and_26_out, not_152_out, not_153_out, not_154_out, OP6, OP5, not_155_out, not_156_out, not_157_out);
  and and_27 (and_27_out, not_158_out, not_159_out, F12, OP6, OP5, not_160_out, not_161_out, not_162_out);
  and and_28 (and_28_out, not_163_out, not_164_out, not_165_out, OP6, OP5, not_166_out, not_167_out, OP2);
  and and_29 (and_29_out, F14, not_168_out, F12, not_169_out, not_170_out, not_171_out, not_172_out, not_173_out);
  and and_30 (and_30_out, F14, F13, not_174_out, OP6, OP5, not_175_out, not_176_out, not_177_out);
  and and_31 (and_31_out, not_178_out, not_179_out, F14, F13, not_180_out, not_181_out, OP5, OP4, not_182_out, not_183_out);
  and and_32 (and_32_out, not_184_out, not_185_out, not_186_out, F13, not_187_out, not_188_out, OP5, OP4, not_189_out, not_190_out);
  and and_33 (and_33_out, not_191_out, not_192_out, not_193_out, F13, F12, not_194_out, OP5, OP4, not_195_out, not_196_out);
  and and_34 (and_34_out, F14, F13, not_197_out, not_198_out, not_199_out, OP4, not_200_out, not_201_out);
  and and_35 (and_35_out, F14, not_202_out, not_203_out, not_204_out, not_205_out, OP4, not_206_out, not_207_out);
  and and_36 (and_36_out, not_208_out, F13, not_209_out, not_210_out, not_211_out, OP4, not_212_out, not_213_out);
  and and_37 (and_37_out, not_214_out, not_215_out, F14, not_216_out, not_217_out, not_218_out, OP5, OP4, not_219_out, not_220_out);
  and and_38 (and_38_out, F14, F13, not_221_out, OP6, OP5, not_222_out, not_223_out, not_224_out);
  or or_1 (S0, and_1_out, and_2_out, and_3_out, and_4_out, and_5_out, and_6_out, and_7_out, and_8_out, and_9_out, and_10_out, and_11_out);
  or or_2 (S1, and_12_out, and_13_out, and_14_out, and_15_out, and_16_out, and_17_out, and_18_out, and_19_out);
  or or_3 (S2, and_20_out, and_21_out, and_22_out, and_23_out, and_24_out, and_25_out, and_26_out, and_27_out, and_28_out, and_29_out, and_30_out);
  or or_4 (S3, and_31_out, and_32_out, and_33_out, and_34_out, and_35_out, and_36_out, and_37_out, and_38_out);
endmodule

// 控制信号生成
module \控制信号自动生成  (
  input  OP2,
  input  OP3,
  input  OP4,
  input  OP5,
  input  OP6,
  input  F12,
  input  F13,
  input  F14,
  input  F25,
  input  F30,
  output MemToReg,
  output MemWrite,
  output ALU_SRC,
  output RegWrite,
  output ecall,
  output S_Type,
  output BEQ,
  output BNE,
  output JALR,
  output JAL,
  output AUIPC,
  output LHU,
  output BLTU
);

  wire and_1_out, and_2_out, and_4_out, and_5_out, and_6_out, and_7_out, and_8_out, and_9_out, and_10_out,
       and_11_out, and_12_out, and_13_out, and_14_out, and_15_out, and_16_out, and_17_out, and_18_out,
       and_19_out, and_20_out, and_21_out, and_22_out, and_23_out, and_24_out, and_25_out, and_26_out,
       and_27_out, and_28_out, and_29_out, and_30_out, and_31_out, and_32_out, and_33_out, and_34_out,
       and_35_out, not_1_out, not_2_out, not_3_out, not_4_out, not_5_out, not_6_out, not_7_out, not_8_out,
       not_9_out, not_10_out, not_11_out, not_12_out, not_13_out, not_14_out, not_15_out, not_16_out,
       not_17_out, not_18_out, not_19_out, not_20_out, not_21_out, not_22_out, not_23_out, not_24_out,
       not_25_out, not_26_out, not_27_out, not_28_out, not_29_out, not_30_out, not_31_out, not_32_out,
       not_33_out, not_34_out, not_35_out, not_36_out, not_37_out, not_38_out, not_39_out, not_40_out,
       not_41_out, not_42_out, not_43_out, not_44_out, not_45_out, not_46_out, not_47_out, not_48_out,
       not_49_out, not_50_out, not_51_out, not_52_out, not_53_out, not_54_out, not_55_out, not_56_out,
       not_57_out, not_58_out, not_59_out, not_60_out, not_61_out, not_62_out, not_63_out, not_64_out,
       not_65_out, not_66_out, not_67_out, not_68_out, not_69_out, not_70_out, not_71_out, not_72_out,
       not_73_out, not_74_out, not_75_out, not_76_out, not_77_out, not_78_out, not_79_out, not_80_out,
       not_81_out, not_82_out, not_83_out, not_84_out, not_85_out, not_86_out, not_87_out, not_88_out,
       not_89_out, not_90_out, not_91_out, not_92_out, not_93_out, not_94_out, not_95_out, not_96_out,
       not_97_out, not_98_out, not_99_out, not_100_out, not_101_out, not_102_out, not_103_out, not_104_out,
       not_105_out, not_106_out, not_107_out, not_108_out, not_109_out, not_110_out, not_111_out,
       not_112_out, not_113_out, not_114_out, not_115_out, not_116_out, not_117_out, not_118_out,
       not_119_out, not_120_out, not_121_out, not_122_out, not_123_out, not_124_out, not_125_out,
       not_126_out, not_127_out, not_128_out, not_129_out, not_130_out, not_131_out, not_132_out,
       not_133_out, not_134_out, not_135_out, not_136_out, not_137_out, not_138_out, not_139_out,
       not_140_out, not_141_out, not_142_out, not_143_out, not_144_out, not_145_out, not_146_out,
       not_147_out, not_148_out, not_149_out, not_150_out, not_151_out, not_152_out, not_153_out,
       not_154_out, not_155_out, not_156_out, not_157_out, not_158_out, not_159_out, not_160_out,
       not_161_out, not_162_out, not_163_out, not_164_out, not_165_out, not_166_out, not_167_out,
       not_168_out, not_169_out, not_170_out, not_171_out, not_172_out, not_173_out, not_174_out,
       not_175_out, not_176_out, not_177_out, not_178_out, not_179_out, not_180_out, not_181_out,
       not_182_out, not_183_out, not_184_out, not_185_out, not_186_out, not_187_out, not_188_out,
       not_189_out, not_190_out, not_191_out, not_192_out, not_193_out, not_194_out, not_195_out,
       not_196_out, not_197_out, not_198_out, not_199_out, not_200_out, not_201_out, not_202_out,
       not_203_out, not_204_out, not_205_out, not_206_out, not_207_out, not_208_out, not_209_out,
       not_210_out, not_211_out, not_212_out, not_213_out, not_214_out, not_215_out, not_216_out,
       not_217_out, not_218_out, not_219_out, not_220_out, not_221_out, not_222_out, not_223_out,
       not_224_out, not_225_out, not_226_out, not_227_out, not_228_out, not_229_out, not_230_out,
       not_231_out, not_232_out, not_233_out, not_234_out, not_235_out, not_236_out, not_237_out,
       not_238_out, not_239_out, not_240_out, not_241_out, not_242_out, not_243_out, not_244_out,
       not_245_out, not_246_out, not_247_out, not_248_out, not_249_out, not_250_out, not_251_out, not_252_out;

  not not_1 (not_1_out, F14);
  not not_2 (not_2_out, F12);
  not not_3 (not_3_out, OP6);
  not not_4 (not_4_out, OP5);
  not not_5 (not_5_out, OP4);
  not not_6 (not_6_out, OP3);
  not not_7 (not_7_out, OP2);
  not not_8 (not_8_out, F13);
  not not_9 (not_9_out, OP6);
  not not_10 (not_10_out, OP5);
  not not_11 (not_11_out, OP4);
  not not_12 (not_12_out, OP3);
  not not_13 (not_13_out, OP2);
  not not_14 (not_14_out, F14);
  not not_15 (not_15_out, F12);
  not not_16 (not_16_out, OP6);
  not not_17 (not_17_out, OP4);
  not not_18 (not_18_out, OP3);
  not not_19 (not_19_out, OP2);
  not not_20 (not_20_out, F14);
  not not_21 (not_21_out, F13);
  not not_22 (not_22_out, F12);
  not not_23 (not_23_out, OP6);
  not not_24 (not_24_out, OP5);
  not not_25 (not_25_out, OP3);
  not not_26 (not_26_out, OP2);
  not not_27 (not_27_out, OP6);
  not not_28 (not_28_out, OP5);
  not not_29 (not_29_out, OP3);
  not not_30 (not_30_out, OP2);
  not not_31 (not_31_out, F12);
  not not_32 (not_32_out, OP6);
  not not_33 (not_33_out, OP5);
  not not_34 (not_34_out, OP3);
  not not_35 (not_35_out, OP2);
  not not_36 (not_36_out, F13);
  not not_37 (not_37_out, F12);
  not not_38 (not_38_out, OP6);
  not not_39 (not_39_out, OP5);
  not not_40 (not_40_out, OP3);
  not not_41 (not_41_out, OP2);
  not not_42 (not_42_out, F14);
  not not_43 (not_43_out, F12);
  not not_44 (not_44_out, OP6);
  not not_45 (not_45_out, OP5);
  not not_46 (not_46_out, OP3);
  not not_47 (not_47_out, OP2);
  not not_48 (not_48_out, F30);
  not not_49 (not_49_out, F25);
  not not_50 (not_50_out, F14);
  not not_51 (not_51_out, F13);
  not not_52 (not_52_out, OP6);
  not not_53 (not_53_out, OP5);
  not not_54 (not_54_out, OP3);
  not not_55 (not_55_out, OP2);
  not not_56 (not_56_out, F30);
  not not_57 (not_57_out, F25);
  not not_58 (not_58_out, F13);
  not not_59 (not_59_out, OP6);
  not not_60 (not_60_out, OP5);
  not not_61 (not_61_out, OP3);
  not not_62 (not_62_out, OP2);
  not not_63 (not_63_out, F25);
  not not_64 (not_64_out, F13);
  not not_65 (not_65_out, OP6);
  not not_66 (not_66_out, OP5);
  not not_67 (not_67_out, OP3);
  not not_68 (not_68_out, OP2);
  not not_69 (not_69_out, F14);
  not not_70 (not_70_out, F12);
  not not_71 (not_71_out, OP6);
  not not_72 (not_72_out, OP5);
  not not_73 (not_73_out, OP4);
  not not_74 (not_74_out, OP3);
  not not_75 (not_75_out, OP2);
  not not_76 (not_76_out, F14);
  not not_77 (not_77_out, F12);
  not not_78 (not_78_out, OP6);
  not not_79 (not_79_out, OP4);
  not not_80 (not_80_out, OP3);
  not not_81 (not_81_out, OP2);
  not not_82 (not_82_out, F14);
  not not_83 (not_83_out, F13);
  not not_84 (not_84_out, F12);
  not not_85 (not_85_out, OP4);
  not not_86 (not_86_out, OP3);
  not not_87 (not_87_out, F13);
  not not_88 (not_88_out, OP6);
  not not_89 (not_89_out, OP5);
  not not_90 (not_90_out, OP4);
  not not_91 (not_91_out, OP3);
  not not_92 (not_92_out, OP2);
  not not_93 (not_93_out, F30);
  not not_94 (not_94_out, F25);
  not not_95 (not_95_out, F14);
  not not_96 (not_96_out, F13);
  not not_97 (not_97_out, F12);
  not not_98 (not_98_out, OP6);
  not not_99 (not_99_out, OP3);
  not not_100 (not_100_out, OP2);
  not not_101 (not_101_out, F25);
  not not_102 (not_102_out, F14);
  not not_103 (not_103_out, F13);
  not not_104 (not_104_out, F12);
  not not_105 (not_105_out, OP6);
  not not_106 (not_106_out, OP3);
  not not_107 (not_107_out, OP2);
  not not_108 (not_108_out, F30);
  not not_109 (not_109_out, F25);
  not not_110 (not_110_out, OP6);
  not not_111 (not_111_out, OP3);
  not not_112 (not_112_out, OP2);
  not not_113 (not_113_out, F30);
  not not_114 (not_114_out, F25);
  not not_115 (not_115_out, F12);
  not not_116 (not_116_out, OP6);
  not not_117 (not_117_out, OP3);
  not not_118 (not_118_out, OP2);
  not not_119 (not_119_out, F30);
  not not_120 (not_120_out, F25);
  not not_121 (not_121_out, F14);
  not not_122 (not_122_out, F12);
  not not_123 (not_123_out, OP6);
  not not_124 (not_124_out, OP3);
  not not_125 (not_125_out, OP2);
  not not_126 (not_126_out, F30);
  not not_127 (not_127_out, F25);
  not not_128 (not_128_out, F14);
  not not_129 (not_129_out, OP6);
  not not_130 (not_130_out, OP3);
  not not_131 (not_131_out, OP2);
  not not_132 (not_132_out, F14);
  not not_133 (not_133_out, F13);
  not not_134 (not_134_out, F12);
  not not_135 (not_135_out, OP6);
  not not_136 (not_136_out, OP5);
  not not_137 (not_137_out, OP3);
  not not_138 (not_138_out, OP2);
  not not_139 (not_139_out, OP6);
  not not_140 (not_140_out, OP5);
  not not_141 (not_141_out, OP3);
  not not_142 (not_142_out, OP2);
  not not_143 (not_143_out, F12);
  not not_144 (not_144_out, OP6);
  not not_145 (not_145_out, OP5);
  not not_146 (not_146_out, OP3);
  not not_147 (not_147_out, OP2);
  not not_148 (not_148_out, F13);
  not not_149 (not_149_out, F12);
  not not_150 (not_150_out, OP6);
  not not_151 (not_151_out, OP5);
  not not_152 (not_152_out, OP3);
  not not_153 (not_153_out, OP2);
  not not_154 (not_154_out, F14);
  not not_155 (not_155_out, F12);
  not not_156 (not_156_out, OP6);
  not not_157 (not_157_out, OP5);
  not not_158 (not_158_out, OP3);
  not not_159 (not_159_out, OP2);
  not not_160 (not_160_out, F30);
  not not_161 (not_161_out, F25);
  not not_162 (not_162_out, F14);
  not not_163 (not_163_out, F13);
  not not_164 (not_164_out, OP6);
  not not_165 (not_165_out, OP5);
  not not_166 (not_166_out, OP3);
  not not_167 (not_167_out, OP2);
  not not_168 (not_168_out, F30);
  not not_169 (not_169_out, F25);
  not not_170 (not_170_out, F13);
  not not_171 (not_171_out, OP6);
  not not_172 (not_172_out, OP5);
  not not_173 (not_173_out, OP3);
  not not_174 (not_174_out, OP2);
  not not_175 (not_175_out, F25);
  not not_176 (not_176_out, F13);
  not not_177 (not_177_out, OP6);
  not not_178 (not_178_out, OP5);
  not not_179 (not_179_out, OP3);
  not not_180 (not_180_out, OP2);
  not not_181 (not_181_out, F14);
  not not_182 (not_182_out, F12);
  not not_183 (not_183_out, OP6);
  not not_184 (not_184_out, OP5);
  not not_185 (not_185_out, OP4);
  not not_186 (not_186_out, OP3);
  not not_187 (not_187_out, OP2);
  not not_188 (not_188_out, OP4);
  not not_189 (not_189_out, F14);
  not not_190 (not_190_out, F13);
  not not_191 (not_191_out, F12);
  not not_192 (not_192_out, OP4);
  not not_193 (not_193_out, OP3);
  not not_194 (not_194_out, F30);
  not not_195 (not_195_out, F25);
  not not_196 (not_196_out, F13);
  not not_197 (not_197_out, F12);
  not not_198 (not_198_out, OP6);
  not not_199 (not_199_out, OP3);
  not not_200 (not_200_out, OP2);
  not not_201 (not_201_out, OP6);
  not not_202 (not_202_out, OP5);
  not not_203 (not_203_out, OP3);
  not not_204 (not_204_out, F13);
  not not_205 (not_205_out, OP6);
  not not_206 (not_206_out, OP5);
  not not_207 (not_207_out, OP4);
  not not_208 (not_208_out, OP3);
  not not_209 (not_209_out, OP2);
  not not_210 (not_210_out, F30);
  not not_211 (not_211_out, F25);
  not not_212 (not_212_out, F14);
  not not_213 (not_213_out, F13);
  not not_214 (not_214_out, F12);
  not not_215 (not_215_out, OP3);
  not not_216 (not_216_out, OP2);
  not not_217 (not_217_out, F14);
  not not_218 (not_218_out, F12);
  not not_219 (not_219_out, OP6);
  not not_220 (not_220_out, OP4);
  not not_221 (not_221_out, OP3);
  not not_222 (not_222_out, OP2);
  not not_223 (not_223_out, F14);
  not not_224 (not_224_out, F13);
  not not_225 (not_225_out, F12);
  not not_226 (not_226_out, OP4);
  not not_227 (not_227_out, OP3);
  not not_228 (not_228_out, OP2);
  not not_229 (not_229_out, F14);
  not not_230 (not_230_out, F13);
  not not_231 (not_231_out, OP4);
  not not_232 (not_232_out, OP3);
  not not_233 (not_233_out, OP2);
  not not_234 (not_234_out, F14);
  not not_235 (not_235_out, F13);
  not not_236 (not_236_out, F12);
  not not_237 (not_237_out, OP4);
  not not_238 (not_238_out, OP3);
  not not_239 (not_239_out, OP4);
  not not_240 (not_240_out, OP6);
  not not_241 (not_241_out, OP5);
  not not_242 (not_242_out, OP3);
  not not_243 (not_243_out, F13);
  not not_244 (not_244_out, OP6);
  not not_245 (not_245_out, OP5);
  not not_246 (not_246_out, OP4);
  not not_247 (not_247_out, OP3);
  not not_248 (not_248_out, OP2);
  not not_249 (not_249_out, F12);
  not not_250 (not_250_out, OP4);
  not not_251 (not_251_out, OP3);
  not not_252 (not_252_out, OP2);
  and and_1 (and_1_out, not_1_out, F13, not_2_out, not_3_out, not_4_out, not_5_out, not_6_out, not_7_out);
  and and_2 (and_2_out, F14, not_8_out, F12, not_9_out, not_10_out, not_11_out, not_12_out, not_13_out);
  and and_3 (MemWrite, not_14_out, F13, not_15_out, not_16_out, OP5, not_17_out, not_18_out, not_19_out);
  and and_4 (and_4_out, not_20_out, not_21_out, not_22_out, not_23_out, not_24_out, OP4, not_25_out, not_26_out);
  and and_5 (and_5_out, F14, F13, F12, not_27_out, not_28_out, OP4, not_29_out, not_30_out);
  and and_6 (and_6_out, F14, F13, not_31_out, not_32_out, not_33_out, OP4, not_34_out, not_35_out);
  and and_7 (and_7_out, F14, not_36_out, not_37_out, not_38_out, not_39_out, OP4, not_40_out, not_41_out);
  and and_8 (and_8_out, not_42_out, F13, not_43_out, not_44_out, not_45_out, OP4, not_46_out, not_47_out);
  and and_9 (and_9_out, not_48_out, not_49_out, not_50_out, not_51_out, F12, not_52_out, not_53_out, OP4, not_54_out, not_55_out);
  and and_10 (and_10_out, not_56_out, not_57_out, F14, not_58_out, F12, not_59_out, not_60_out, OP4, not_61_out, not_62_out);
  and and_11 (and_11_out, F30, not_63_out, F14, not_64_out, F12, not_65_out, not_66_out, OP4, not_67_out, not_68_out);
  and and_12 (and_12_out, not_69_out, F13, not_70_out, not_71_out, not_72_out, not_73_out, not_74_out, not_75_out);
  and and_13 (and_13_out, not_76_out, F13, not_77_out, not_78_out, OP5, not_79_out, not_80_out, not_81_out);
  and and_14 (and_14_out, not_82_out, not_83_out, not_84_out, OP6, OP5, not_85_out, not_86_out, OP2);
  and and_15 (and_15_out, F14, not_87_out, F12, not_88_out, not_89_out, not_90_out, not_91_out, not_92_out);
  and and_16 (and_16_out, not_93_out, not_94_out, not_95_out, not_96_out, not_97_out, not_98_out, OP5, OP4, not_99_out, not_100_out);
  and and_17 (and_17_out, F30, not_101_out, not_102_out, not_103_out, not_104_out, not_105_out, OP5, OP4, not_106_out, not_107_out);
  and and_18 (and_18_out, not_108_out, not_109_out, F14, F13, F12, not_110_out, OP5, OP4, not_111_out, not_112_out);
  and and_19 (and_19_out, not_113_out, not_114_out, F14, F13, not_115_out, not_116_out, OP5, OP4, not_117_out, not_118_out);
  and and_20 (and_20_out, not_119_out, not_120_out, not_121_out, F13, not_122_out, not_123_out, OP5, OP4, not_124_out, not_125_out);
  and and_21 (and_21_out, not_126_out, not_127_out, not_128_out, F13, F12, not_129_out, OP5, OP4, not_130_out, not_131_out);
  and and_22 (and_22_out, not_132_out, not_133_out, not_134_out, not_135_out, not_136_out, OP4, not_137_out, not_138_out);
  and and_23 (and_23_out, F14, F13, F12, not_139_out, not_140_out, OP4, not_141_out, not_142_out);
  and and_24 (and_24_out, F14, F13, not_143_out, not_144_out, not_145_out, OP4, not_146_out, not_147_out);
  and and_25 (and_25_out, F14, not_148_out, not_149_out, not_150_out, not_151_out, OP4, not_152_out, not_153_out);
  and and_26 (and_26_out, not_154_out, F13, not_155_out, not_156_out, not_157_out, OP4, not_158_out, not_159_out);
  and and_27 (and_27_out, not_160_out, not_161_out, not_162_out, not_163_out, F12, not_164_out, not_165_out, OP4, not_166_out, not_167_out);
  and and_28 (and_28_out, not_168_out, not_169_out, F14, not_170_out, F12, not_171_out, not_172_out, OP4, not_173_out, not_174_out);
  and and_29 (and_29_out, F30, not_175_out, F14, not_176_out, F12, not_177_out, not_178_out, OP4, not_179_out, not_180_out);
  and and_30 (and_30_out, not_181_out, F13, not_182_out, not_183_out, not_184_out, not_185_out, not_186_out, not_187_out);
  and and_31 (and_31_out, OP6, OP5, not_188_out, OP3, OP2);
  and and_32 (and_32_out, not_189_out, not_190_out, not_191_out, OP6, OP5, not_192_out, not_193_out, OP2);
  and and_33 (and_33_out, not_194_out, not_195_out, F14, not_196_out, not_197_out, not_198_out, OP5, OP4, not_199_out, not_200_out);
  and and_34 (and_34_out, not_201_out, not_202_out, OP4, not_203_out, OP2);
  and and_35 (and_35_out, F14, not_204_out, F12, not_205_out, not_206_out, not_207_out, not_208_out, not_209_out);
  and and_36 (ecall, not_210_out, not_211_out, not_212_out, not_213_out, not_214_out, OP6, OP5, OP4, not_215_out, not_216_out);
  and and_37 (S_Type, not_217_out, F13, not_218_out, not_219_out, OP5, not_220_out, not_221_out, not_222_out);
  and and_38 (BEQ, not_223_out, not_224_out, not_225_out, OP6, OP5, not_226_out, not_227_out, not_228_out);
  and and_39 (BNE, not_229_out, not_230_out, F12, OP6, OP5, not_231_out, not_232_out, not_233_out);
  and and_40 (JALR, not_234_out, not_235_out, not_236_out, OP6, OP5, not_237_out, not_238_out, OP2);
  and and_41 (JAL, OP6, OP5, not_239_out, OP3, OP2);
  and and_42 (AUIPC, not_240_out, not_241_out, OP4, not_242_out, OP2);
  and and_43 (LHU, F14, not_243_out, F12, not_244_out, not_245_out, not_246_out, not_247_out, not_248_out);
  and and_44 (BLTU, F14, F13, not_249_out, OP6, OP5, not_250_out, not_251_out, not_252_out);
  or or_1 (MemToReg, and_1_out, and_2_out);
  or or_2 (ALU_SRC, and_4_out, and_5_out, and_6_out, and_7_out, and_8_out, and_9_out, and_10_out, and_11_out, and_12_out, and_13_out, and_14_out, and_15_out);
  or or_3 (RegWrite, and_16_out, and_17_out, and_18_out, and_19_out, and_20_out, and_21_out, and_22_out, and_23_out, and_24_out, and_25_out, and_26_out, and_27_out, and_28_out, and_29_out, and_30_out, and_31_out, and_32_out, and_33_out, and_34_out, and_35_out);
endmodule

// ALU
module ALU (
  input  [31:0] X,
  input  [31:0] Y,
  input  [3:0] AluOP,
  output out_4,
  output Equal,
  output out_6,
  output [31:0] Result,
  output [31:0] Result_2
);

  wire [0:0] comparator_1_lt, comparator_2_lt;
  wire [31:0] adder_1_out, AND_out, divider_1_out, divider_1_rem, multiplier_1_cout, multiplier_1_out,
       NOR_out, OR_out, shifter_1_out, shifter_2_out, shifter_3_out, subtractor_1_out, XOR_out;

  assign AND_out = X & Y;  // AND_Gate AND, 32 bits wide
  assign OR_out = X | Y;  // OR_Gate OR, 32 bits wide
  Shifter #(.width(32), .shift("ll")) shifter_1 (.in(X), .\dist (Y[4:0]), .out(shifter_1_out));
  Shifter #(.width(32), .shift("ar")) shifter_2 (.in(X), .\dist (Y[4:0]), .out(shifter_2_out));
  Shifter #(.width(32), .shift("lr")) shifter_3 (.in(X), .\dist (Y[4:0]), .out(shifter_3_out));
  Multiplier #(.width(32)) multiplier_1 (.a(X), .b(Y), .out(multiplier_1_out), .cout(multiplier_1_cout));  // open: cin
  Divider #(.width(32)) divider_1 (.a(X), .b(Y), .out(divider_1_out), .rem(divider_1_rem));  // open: upper
  Adder #(.width(32)) adder_1 (.a(X), .b(Y), .out(adder_1_out));  // open: cin, cout
  Subtractor #(.width(32)) subtractor_1 (.a(X), .b(Y), .out(subtractor_1_out));  // open: bin, bout
  assign XOR_out = X ^ Y;  // XOR_Gate XOR, 32 bits wide
  assign NOR_out = ~(X | Y);  // NOR_Gate NOR, 32 bits wide
  Comparator #(.width(32), .mode("twosComplement")) comparator_1 (
    .a(X), .b(Y), .eq(Equal), .lt(comparator_1_lt[0]));  // open: gt
  Comparator #(.width(32), .mode("unsigned")) comparator_2 (.a(X), .b(Y), .lt(comparator_2_lt[0]));  // open: gt, eq
  Multiplexer #(.select(4), .width(32), .disabled("Z"), .enable("false")) multiplexer_1 (
    .in0(shifter_1_out), .in1(shifter_2_out), .in2(shifter_3_out), .in3(multiplier_1_out),
    .in4(divider_1_out), .in5(adder_1_out), .in6(subtractor_1_out), .in7(AND_out), .in8(OR_out),
    .in9(XOR_out), .in10(NOR_out), .in11({{31{1'b0}}, comparator_1_lt[0]}),
    .in12({{31{1'b0}}, comparator_2_lt[0]}), .in13({32{1'b0}}), .in14({32{1'b0}}), .in15({32{1'b0}}),
    .out(Result), .sel(AluOP));
  Multiplexer #(.select(4), .width(32), .disabled("Z"), .enable("false")) multiplexer_2 (
    .in0({32{1'b0}}), .in1({32{1'b0}}), .in2({32{1'b0}}), .in3(multiplier_1_cout), .in4(divider_1_rem),
    .in5({32{1'b0}}), .in6({32{1'b0}}), .in7({32{1'b0}}), .in8({32{1'b0}}), .in9({32{1'b0}}),
    .in10({32{1'b0}}), .in11({32{1'b0}}), .in12({32{1'b0}}), .in13({32{1'b0}}), .in14({32{1'b0}}),
    .in15({32{1'b0}}), .out(Result_2), .sel(AluOP));
  Multiplexer #(.select(4), .width(1), .disabled("Z"), .enable("false")) multiplexer_3 (
    .in0(1'b0), .in1(1'b0), .in2(1'b0), .in3(1'b0), .in4(1'b0), .in5(1'b0), .in6(1'b0), .in7(1'b0),
    .in8(1'b0), .in9(1'b0), .in10(1'b0), .in11(comparator_1_lt[0]), .in12(comparator_2_lt[0]), .in13(1'b0),
    .in14(1'b0), .in15(1'b0), .out(out_6), .sel(AluOP));
  not not_1 (out_4, out_6);

  // Other names for the same wires on the sheet: Result2[31:0] = Result_2; S[3:0] = AluOP; tunnel = out_6;
  //   tunnel_t = out_4

  // Notes on the sheet:
  //   不要改变此引脚区域内容，也不要改变ALU封装形式
  //   输入引脚
  //   输出引脚
endmodule

module Regifile (
  input  [31:0] Din,
  input  Clk,
  input  WE,
  input  [4:0] R1_num,
  input  [4:0] W_num,
  input  [4:0] R2_num,
  output [31:0] R1,
  output [31:0] R2
);

  // RegisterFile registerfile_1: pin names not known; wires that end beside it: Din, Clk, WE, W_num, R1_num, R2_num, R1, R2
endmodule

module \理想流水线  (
  output RegWrite,
  output MemWrite,
  output [31:0] IF_PC,
  output [31:0] ID_PC,
  output [31:0] EX_PC,
  output [31:0] M_PC,
  output [31:0] WB_PC,
  output [31:0] RDin,
  output [31:0] MDin,
  output [31:0] LedData
);

  wire alu_1_equal, alu_1_out_6, and_1_out, and_2_out, and_3_out, and_4_out, and_7_out, AUIPC, CLK,
       clock_1_out, clock_2_out, comparator_1_eq, comparator_1_lt, comparator_2_eq, d_ff_1_q, EX_ecall,
       EX_halt, ex_mem_1_auipc_2, ex_mem_1_halt_2, ex_mem_1_jal_2, ex_mem_1_jalr_2, ex_mem_1_lhu_2,
       ex_mem_1_memtoreg_2, ex_mem_1_regwrie_2, Go, halt, id_ex_1_alusrcb_2, id_ex_1_auipc_2, id_ex_1_beq_2,
       id_ex_1_bltu_2, id_ex_1_bne_2, id_ex_1_jal_2, id_ex_1_jalr_2, id_ex_1_lhu_2, id_ex_1_memtoreg_2,
       id_ex_1_memwrite_2, id_ex_1_regwrie_2, IR1, IR2, IR3, isBranch, JAL, JALR, LHU, mem_wb_1_auipc_2,
       mem_wb_1_jal_2, mem_wb_1_jalr_2, mem_wb_1_lhu_2, mem_wb_1_memtoreg_2, nand_1_out, not_1_out,
       not_2_out, or_1_out, or_2_out, or_3_out, or_5_out, register_1_q, RST, W1, W2, W3,
       \单周期硬布线控制器_1_alu_src , \单周期硬布线控制器_1_beq , \单周期硬布线控制器_1_bltu , \单周期硬布线控制器_1_bne , \单周期硬布线控制器_1_ecall ,
       \单周期硬布线控制器_1_memtoreg , \单周期硬布线控制器_1_memwrite , \单周期硬布线控制器_1_regwrite , \单周期硬布线控制器_1_s_type ,
       \单周期硬布线控制器_1_uret ;
  wire [3:0] id_ex_1_aluop_2, \单周期硬布线控制器_1_alu_op ;
  wire [4:0] ex_mem_1_rd_2, id_ex_1_rd_2, multiplexer_2_out, multiplexer_3_out, WB_rd;
  wire [11:0] multiplexer_4_out;
  wire [12:0] CNT_num;
  wire [15:0] \LoadUse次数 , multiplexer_10_out, multiplexer_12_out, multiplexer_12_out_2, \总周期数 , \插入气泡数 ,
       \无条件分支数 , \条件分支成功数 ;
  wire [31:0] adder_2_out, adder_3_out, alu_1_result, and_5_out, bit_extender_1_out, bit_extender_2_out,
       bit_extender_3_out, bit_extender_4_out, bit_extender_5_out, branch, EX_IR, ex_mem_1_aluresult_2,
       ex_mem_1_auipc_addr_2, ex_mem_1_pc_4_2, id_ex_1_imm1_2, id_ex_1_imm2_2, id_ex_1_imm_20_2,
       id_ex_1_pc_4_2, ID_IR, if_id_1_pc_4_out, IF_IR, MEM_IR, mem_wb_1_aluresult_2, mem_wb_1_auipc_addr_2,
       mem_wb_1_pc_4_2, mem_wb_1_readdata_2, multiplexer_1_out, multiplexer_5_out, multiplexer_6_out,
       multiplexer_9_out, multiplexer_11_out, PC, PC_4, R1, R2, ram_1_data, regifile_1_r1, regifile_1_r2,
       shifter_1_out, shifter_2_out, WB_IR;

  Button \u_总复位  (.out(RST));
  Button _1 (.out(IR1));
  Button _2 (.out(IR2));
  Button _3 (.out(IR3));
  // Probe on \总周期数 
  // Probe on \总周期数 
  Button \u_继续运行  (.out(Go));
  LED #(.active("true")) led_1 (.in(W1));
  LED #(.active("true")) led_2 (.in(W2));
  LED #(.active("true")) led_3 (.in(W3));
  Hex_Digit_Display hex_digit_display_1 (.value(LedData[31:28]));  // open: dp
  // Probe on IF_PC[19:0]
  // RiscV_Probe riscv_probe_1: pin names not known; wires that end beside it: IF_IR
  Hex_Digit_Display hex_digit_display_2 (.value(LedData[23:20]));  // open: dp
  Hex_Digit_Display hex_digit_display_3 (.value(LedData[27:24]));  // open: dp
  // Probe on ID_PC[19:0]
  // RiscV_Probe riscv_probe_2: pin names not known; wires that end beside it: ID_IR
  Hex_Digit_Display hex_digit_display_4 (.value(LedData[19:16]));  // open: dp
  Hex_Digit_Display hex_digit_display_5 (.value(LedData[15:12]));  // open: dp
  Hex_Digit_Display hex_digit_display_6 (.value(LedData[7:4]));  // open: dp
  Hex_Digit_Display hex_digit_display_7 (.value(LedData[11:8]));  // open: dp
  Clock #(.highDuration(1), .lowDuration(1)) clock_1 (.out(clock_1_out));
  // Probe on EX_PC[19:0]
  // RiscV_Probe riscv_probe_3: pin names not known; wires that end beside it: clock_1_out, EX_IR, CLK
  Hex_Digit_Display hex_digit_display_8 (.value(LedData[3:0]));  // open: dp
  // Probe on \总周期数 
  // Probe on M_PC[19:0]
  // RiscV_Probe riscv_probe_4: pin names not known; wires that end beside it: MEM_IR
  // Probe on \总周期数 
  // Probe on \无条件分支数 
  // Probe on \条件分支成功数 
  // Probe on \插入气泡数 
  // Probe on \LoadUse次数 
  Multiplexer #(.select(1), .width(32), .disabled("Z"), .enable("false")) multiplexer_1 (
    .in0(PC_4), .in1(branch), .out(multiplexer_1_out), .sel(or_1_out));
  or or_1 (or_1_out, JALR, JAL, isBranch);
  // Probe on IF_PC[11:0]
  // Probe on WB_PC[19:0]
  // RiscV_Probe riscv_probe_5: pin names not known; wires that end beside it: WB_IR
  // Probe on ID_PC[11:0]
  // Probe on EX_PC[11:0]
  not not_1 (not_1_out, register_1_q);
  Register #(.width(1), .trigger("rising"), .Select("low")) register_1 (
    .D(halt), .Q(register_1_q), .clk(CLK), .clr(RST));  // open: en
  or or_2 (or_2_out, Go, not_2_out);
  not not_2 (not_2_out, halt);
  // Probe on M_PC[11:0]
  D_Flip_Flop #(.trigger("high"), .Pre_Clr_Positions("LEGACY"), .NegatePresetClear("false"), .enable("true"), .NewFFLayout("false")) d_ff_1 (.Q(d_ff_1_q));  // open: clk, D, Qn, preset, en, reset
  // Probe on 13'hc
  Counter #(.width(16), .max('hffff), .ongoal("wrap"), .trigger("rising"), .behavior("new")) counter_1 (
    .count(not_1_out), .Q(\总周期数 ), .clk(CLK));  // open: load, D, carry, clr, preset, down
  Register #(.width(32), .trigger("rising"), .Select("low")) u_PC (
    .D(multiplexer_1_out), .en(or_2_out), .Q(IF_PC), .clk(CLK), .clr(RST));
  // Probe on WB_PC[11:0]
  Comparator #(.width(13), .mode("twosComplement")) comparator_1 (
    .a(CNT_num), .b(13'hc), .eq(comparator_1_eq), .lt(comparator_1_lt));  // open: gt
  Clock #(.highDuration(1), .lowDuration(1)) clock_2 (.out(clock_2_out));
  Adder #(.width(32)) adder_1 (.a(IF_PC), .b(32'h4), .out(PC_4));  // open: cin, cout
  nand nand_1 (nand_1_out, d_ff_1_q, comparator_1_eq);
  Counter #(.width(13), .max('h1fff), .ongoal("stay"), .trigger("rising"), .behavior("old")) counter_2 (
    .count(comparator_1_lt), .Q(CNT_num), .clk(clock_2_out));  // open: load, D, carry, clr, preset
  assign CLK = nand_1_out ? clock_2_out : 1'bz;  // Controlled_Buffer controlled_buffer_1
  // RiscV_Probe riscv_probe_6: pin names not known; wires that end beside it: IF_IR
  ROM #(.addrWidth(10), .dataWidth(32), .Select("high")) rom_1 (.addr(IF_PC[11:2]), .data(IF_IR));
  Pull_Resistor #(.pull(1)) pull_resistor_1 (.node(CLK));
  and and_1 (and_1_out, 1'b1, ~halt);  // AND_Gate
  IF_ID if_id_1 (
    .IR_in(IF_IR), .PC_in(IF_PC), .PC_4_in(PC_4), .IR_out(ID_IR), .PC_out(ID_PC),
    .PC_4_out(if_id_1_pc_4_out), .RST(RST), .branchTaken(1'b0), .en(and_1_out), .clk(CLK));  // open: predictJump, predictJump_2, isBubble, isBubble_2
  or or_3 (or_3_out, JAL, JALR);
  Counter #(.width(16), .max('hffff), .ongoal("wrap"), .trigger("rising"), .behavior("new")) counter_3 (
    .count(or_3_out), .Q(\无条件分支数 ), .clk(CLK));  // open: load, D, carry, clr, preset, down
  Multiplexer #(.select(1), .width(5), .disabled("Z"), .enable("false")) multiplexer_2 (
    .in0(ID_IR[19:15]), .in1(5'b10001), .out(multiplexer_2_out), .sel(\单周期硬布线控制器_1_ecall ));
  \单周期硬布线控制器  \u_单周期硬布线控制器_1  (
    .Funct({ID_IR[30], ID_IR[25], ID_IR[14:12]}), .OP(ID_IR[6:2]), .ALU_OP(\单周期硬布线控制器_1_alu_op ),
    .MemToReg(\单周期硬布线控制器_1_memtoreg ), .MemWrite(\单周期硬布线控制器_1_memwrite ), .ALU_SRC(\单周期硬布线控制器_1_alu_src ),
    .RegWrite(\单周期硬布线控制器_1_regwrite ), .ecall(\单周期硬布线控制器_1_ecall ), .S_type(\单周期硬布线控制器_1_s_type ),
    .Jalr(JALR), .Beq(\单周期硬布线控制器_1_beq ), .JAL(JAL), .Bne(\单周期硬布线控制器_1_bne ), .in_3(ID_IR[21]),
    .uret(\单周期硬布线控制器_1_uret ), .AUIPC(AUIPC), .LHU(LHU), .BLTU(\单周期硬布线控制器_1_bltu ));  // open: rs1_used, rs2_used, CSRRSI, CSRRCI
  Multiplexer #(.select(1), .width(5), .disabled("Z"), .enable("false")) multiplexer_3 (
    .in0(ID_IR[24:20]), .in1(5'b01010), .out(multiplexer_3_out), .sel(\单周期硬布线控制器_1_ecall ));
  Multiplexer #(.select(1), .width(12), .disabled("Z"), .enable("false")) multiplexer_4 (
    .in0(ID_IR[31:20]), .in1({ID_IR[31:25], ID_IR[11:7]}), .out(multiplexer_4_out), .sel(\单周期硬布线控制器_1_s_type ));
  assign bit_extender_1_out = {{12{ID_IR[31]}}, ID_IR[31:12]};  // Bit_Extender bit_extender_1
  Shifter #(.width(32), .shift("ll")) shifter_1 (.in(bit_extender_1_out), .\dist (5'b01100), .out(shifter_1_out));
  Regifile regifile_1 (
    .Din(RDin), .Clk(CLK), .R1(regifile_1_r1), .R2(regifile_1_r2), .WE(RegWrite), .W_num(WB_rd),
    .R1_num(multiplexer_2_out), .R2_num(multiplexer_3_out));
  assign bit_extender_2_out = {{20{multiplexer_4_out[11]}}, multiplexer_4_out};  // Bit_Extender bit_extender_2
  assign bit_extender_3_out = {{20{ID_IR[31]}}, {ID_IR[31], ID_IR[7], ID_IR[30:25], ID_IR[11:8]}};  // Bit_Extender bit_extender_3
  assign bit_extender_4_out = {{12{ID_IR[31]}}, {ID_IR[31], ID_IR[19:12], ID_IR[20], ID_IR[30:21]}};  // Bit_Extender bit_extender_4
  Multiplexer #(.select(1), .width(32), .disabled("Z"), .enable("false")) multiplexer_5 (
    .in0(bit_extender_3_out), .in1(bit_extender_4_out), .out(multiplexer_5_out), .sel(JAL));
  ID_EX id_ex_1 (
    .Beq(\单周期硬布线控制器_1_beq ), .JAL(JAL), .Bne(\单周期硬布线控制器_1_bne ), .JALR(JALR),
    .MemToReg(\单周期硬布线控制器_1_memtoreg ), .AUIPC(AUIPC), .AluOp(\单周期硬布线控制器_1_alu_op ), .LHU(LHU),
    .AluSrcB(\单周期硬布线控制器_1_alu_src ), .BLTU(\单周期硬布线控制器_1_bltu ), .RegWrie(\单周期硬布线控制器_1_regwrite ),
    .ecall(\单周期硬布线控制器_1_ecall ), .uret(\单周期硬布线控制器_1_uret ), .R1(regifile_1_r1), .R2(regifile_1_r2),
    .rd(ID_IR[11:7]), .imm1(bit_extender_2_out), .imm2(multiplexer_5_out), .IR(ID_IR), .PC(ID_PC),
    .PC_4(if_id_1_pc_4_out), .Beq_2(id_ex_1_beq_2), .JAL_2(id_ex_1_jal_2), .Bne_2(id_ex_1_bne_2),
    .JALR_2(id_ex_1_jalr_2), .MemToReg_2(id_ex_1_memtoreg_2), .AUIPC_2(id_ex_1_auipc_2),
    .AluOp_2(id_ex_1_aluop_2), .LHU_2(id_ex_1_lhu_2), .AluSrcB_2(id_ex_1_alusrcb_2), .BLTU_2(id_ex_1_bltu_2),
    .RegWrie_2(id_ex_1_regwrie_2), .ecall_2(EX_ecall), .R1_2(R1), .R2_2(R2), .rd_2(id_ex_1_rd_2),
    .imm1_2(id_ex_1_imm1_2), .imm2_2(id_ex_1_imm2_2), .IR_2(EX_IR), .PC_2(EX_PC), .PC_4_2(id_ex_1_pc_4_2),
    .reset(RST), .flush(1'b0), .enable(and_1_out), .clk(CLK), .MemWrite(\单周期硬布线控制器_1_memwrite ),
    .MemWrite_2(id_ex_1_memwrite_2), .imm_20(shifter_1_out), .imm_20_2(id_ex_1_imm_20_2));  // open: uret_2, rs1_redirect, rs1_redirect_2, rs2_redirect_2, rs2_redirect, predictJump, predictJump_2, isBubblet, isBubble
  Multiplexer #(.select(1), .width(32), .disabled("Z"), .enable("false")) multiplexer_6 (
    .in0(R2), .in1(id_ex_1_imm1_2), .out(multiplexer_6_out), .sel(id_ex_1_alusrcb_2));
  Shifter #(.width(32), .shift("ll")) shifter_2 (.in(id_ex_1_imm2_2), .\dist (5'b00001), .out(shifter_2_out));
  or or_4 (isBranch, and_3_out, and_4_out, and_2_out);
  and and_2 (and_2_out, ~alu_1_equal, id_ex_1_bne_2);  // AND_Gate
  and and_3 (and_3_out, id_ex_1_bltu_2, alu_1_out_6);
  and and_4 (and_4_out, id_ex_1_beq_2, alu_1_equal);
  ALU alu_1 (
    .X(R1), .Y(multiplexer_6_out), .AluOP(id_ex_1_aluop_2), .Equal(alu_1_equal), .Result(alu_1_result),
    .out_6(alu_1_out_6));  // open: Result_2, out_4
  Adder #(.width(32)) adder_2 (.a(shifter_2_out), .b(EX_PC), .out(adder_2_out));  // open: cin, cout
  assign and_5_out = alu_1_result & 32'hfffffffe;  // AND_Gate and_5, 32 bits wide
  Comparator #(.width(32), .mode("twosComplement")) comparator_2 (
    .a(R1), .b(32'h22), .eq(comparator_2_eq));  // open: gt, lt
  Multiplexer #(.select(1), .width(32), .disabled("Z"), .enable("false")) multiplexer_7 (
    .in0(adder_2_out), .in1(and_5_out), .out(branch), .sel(id_ex_1_jalr_2));
  Adder #(.width(32)) adder_3 (.a(PC), .b(id_ex_1_imm_20_2), .out(adder_3_out));  // open: cin, cout
  and and_6 (EX_halt, EX_ecall, ~comparator_2_eq);  // AND_Gate
  and and_7 (and_7_out, EX_ecall, comparator_2_eq);
  Register #(.width(32), .trigger("rising"), .Select("low")) register_2 (
    .D(R2), .en(and_7_out), .Q(LedData), .clk(CLK));  // open: clr
  EX_MEM ex_mem_1 (
    .JAL(id_ex_1_jal_2), .JALR(id_ex_1_jalr_2), .MemToReg(id_ex_1_memtoreg_2), .AUIPC(id_ex_1_auipc_2),
    .MemWrite(id_ex_1_memwrite_2), .LHU(id_ex_1_lhu_2), .RegWrie(id_ex_1_regwrie_2), .halt(EX_halt),
    .ALUResult(alu_1_result), .Write(R2), .rd(id_ex_1_rd_2), .IR(EX_IR), .PC(EX_PC), .PC_4(id_ex_1_pc_4_2),
    .JAL_2(ex_mem_1_jal_2), .JALR_2(ex_mem_1_jalr_2), .MemToReg_2(ex_mem_1_memtoreg_2),
    .AUIPC_2(ex_mem_1_auipc_2), .MemWrite_2(MemWrite), .LHU_2(ex_mem_1_lhu_2),
    .RegWrie_2(ex_mem_1_regwrie_2), .halt_2(ex_mem_1_halt_2), .ALUResult_2(ex_mem_1_aluresult_2),
    .Write_2(MDin), .rd_2(ex_mem_1_rd_2), .IR_2(MEM_IR), .PC_2(M_PC), .PC_4_2(ex_mem_1_pc_4_2), .reset(RST),
    .enable(and_1_out), .clk(CLK), .AUIPC_addr(adder_3_out), .AUIPC_addr_2(ex_mem_1_auipc_addr_2));
  RAM #(.addrWidth(10), .dataWidth(32), .bus("separate"), .Select("high")) ram_1 (
    .addr(ex_mem_1_aluresult_2[11:2]), .din(MDin), .data(ram_1_data), .str(MemWrite), .sel(1'b1), .clk(CLK),
    .ld(1'b1), .clr(RST));
  MEM_WB mem_wb_1 (
    .JAL(ex_mem_1_jal_2), .JALR(ex_mem_1_jalr_2), .MemToReg(ex_mem_1_memtoreg_2), .AUIPC(ex_mem_1_auipc_2),
    .LHU(ex_mem_1_lhu_2), .RegWrie(ex_mem_1_regwrie_2), .halt(ex_mem_1_halt_2),
    .ALUResult(ex_mem_1_aluresult_2), .ReadData(ram_1_data), .IR(MEM_IR), .PC(M_PC), .PC_4(ex_mem_1_pc_4_2),
    .JAL_2(mem_wb_1_jal_2), .JALR_2(mem_wb_1_jalr_2), .MemToReg_2(mem_wb_1_memtoreg_2),
    .AUIPC_2(mem_wb_1_auipc_2), .LHU_2(mem_wb_1_lhu_2), .RegWrie_2(RegWrite), .halt_2(halt),
    .ALUResult_2(mem_wb_1_aluresult_2), .ReadData_2(mem_wb_1_readdata_2), .IR_2(WB_IR), .PC_2(WB_PC),
    .PC_4_2(mem_wb_1_pc_4_2), .reset(RST), .enable(and_1_out), .clk(CLK), .AUIPC_addr(ex_mem_1_auipc_addr_2),
    .AUIPC_addr_2(mem_wb_1_auipc_addr_2), .rd(ex_mem_1_rd_2), .rd_2(WB_rd));
  Multiplexer #(.select(1), .width(32), .disabled("Z"), .enable("false")) multiplexer_8 (
    .in0(multiplexer_9_out), .in1(bit_extender_5_out), .out(RDin), .sel(mem_wb_1_lhu_2));
  Multiplexer #(.select(1), .width(32), .disabled("Z"), .enable("false")) multiplexer_9 (
    .in0(multiplexer_11_out), .in1(mem_wb_1_auipc_addr_2), .out(multiplexer_9_out), .sel(mem_wb_1_auipc_2));
  assign bit_extender_5_out = {{16{1'b0}}, multiplexer_10_out};  // Bit_Extender bit_extender_5
  Multiplexer #(.select(1), .width(16), .disabled("Z"), .enable("false")) multiplexer_10 (
    .in0(multiplexer_12_out), .in1(multiplexer_12_out_2), .out(multiplexer_10_out),
    .sel(mem_wb_1_aluresult_2[1]));
  Multiplexer #(.select(1), .width(32), .disabled("Z"), .enable("false")) multiplexer_11 (
    .in0({multiplexer_12_out_2, multiplexer_12_out}), .in1(mem_wb_1_pc_4_2), .out(multiplexer_11_out),
    .sel(or_5_out));
  or or_5 (or_5_out, mem_wb_1_jalr_2, mem_wb_1_jal_2);
  Multiplexer #(.select(1), .width(32), .disabled("Z"), .enable("false")) multiplexer_12 (
    .in0(mem_wb_1_aluresult_2), .in1(mem_wb_1_readdata_2), .out({multiplexer_12_out_2, multiplexer_12_out}),
    .sel(mem_wb_1_memtoreg_2));

  // Other names for the same wires on the sheet: MEM_PC[31:0] = M_PC; WB_RegWrite = RegWrite

  // Notes on the sheet:
  //   中断源
  //   时空图监测，可删除
  //   中断等待指示
  //   数码管输出
  //   控制位
  //   流水调试日志用
  //   暂停节拍，不能为0
  //   戳工具置1进入计数暂停模式，ctrl+k时钟自动运行到对应节拍暂停
  //   ctrl+k关闭时钟连续运行，将控制位置零，进入单步调试模式调试
  //   用这个时钟源需要去掉电路中的其他时钟源
  //   指令存储器
  //   可计数暂停的时钟源
  //   指令探针
  //   contents of rom_1 (hex, n*v repeats v):
  //   413 493 913 993 46413 14e493 296913 39e993 842023 942223 1242423 1342623 a00893 493 913 993 73
  //   Beq,Bne,Bltu
  //   为方便自动评测，需要输出流水线各段保存的PC值，注意是PC不是PC+4，另外ID段寄存器写入信息，Mem段内存写入信息也要输出
  //   指令字
  //   JAL
  //   AUIPC
  //   JAL
  //   JALR
  //   Beq
  //   Bne
  //   MemToReg
  //   MemWrite
  //   AluOP
  //   AluSrcB
  //   RegWrite
  //   数据存储器
  //   LHU
  //   AUIPC
  //   JAL,JALR
endmodule

module \气泡流水线  (
  output RegWrite,
  output MemWrite,
  output [31:0] IF_PC,
  output [31:0] ID_PC,
  output [31:0] EX_PC,
  output [31:0] M_PC,
  output [31:0] WB_PC,
  output [31:0] RDin,
  output [31:0] MDin,
  output [31:0] LedData
);

  wire alu_1_equal, alu_1_out_6, and_1_out, and_2_out, and_3_out, and_4_out, and_5_out, and_6_out, and_7_out,
       and_9_out, AUIPC, Beq, Bltu, Bne, CLK, clock_1_out, clock_2_out, comparator_1_eq, comparator_1_lt,
       comparator_2_eq, d_ff_1_q, EX_ecall, EX_halt, Ex_isBubble, EX_JAL, EX_JALR, ex_mem_1_auipc_2,
       ex_mem_1_halt_2, ex_mem_1_jal_2, ex_mem_1_jalr_2, ex_mem_1_lhu_2, ex_mem_1_memtoreg_2, EX_RegWrite,
       Go, halt, hazzard, id_ex_1_alusrcb_2, id_ex_1_auipc_2, id_ex_1_beq_2, id_ex_1_bltu_2, id_ex_1_bne_2,
       id_ex_1_lhu_2, id_ex_1_memtoreg_2, id_ex_1_memwrite_2, if_id_1_isbubble_2, IR1, IR2, IR3, isBranch,
       JAL, JALR, LHU, MEM_RegWrite, mem_wb_1_auipc_2, mem_wb_1_jal_2, mem_wb_1_jalr_2, mem_wb_1_lhu_2,
       mem_wb_1_memtoreg_2, nand_1_out, not_1_out, not_2_out, not_3_out, not_4_out, or_1_out, or_2_out,
       or_3_out, or_4_out, or_5_out, or_6_out, or_7_out, or_9_out, or_10_out, or_11_out, register_1_q, RST,
       W1, W2, W3, \单周期硬布线控制器_1_alu_src , \单周期硬布线控制器_1_ecall , \单周期硬布线控制器_1_memtoreg ,
       \单周期硬布线控制器_1_memwrite , \单周期硬布线控制器_1_regwrite , \单周期硬布线控制器_1_rs1_used , \单周期硬布线控制器_1_rs2_used ,
       \单周期硬布线控制器_1_s_type , \单周期硬布线控制器_1_uret ;
  wire [3:0] id_ex_1_aluop_2, \单周期硬布线控制器_1_alu_op ;
  wire [4:0] EX_rd, MEM_rd, rs1, rs2, WB_rd;
  wire [11:0] multiplexer_4_out;
  wire [12:0] CNT_num;
  wire [15:0] multiplexer_10_out, multiplexer_12_out, multiplexer_12_out_2, \总周期数 , \插入气泡数 , \无条件分支数 ;
  wire [31:0] adder_2_out, adder_3_out, alu_1_result, and_8_out, bit_extender_1_out, bit_extender_2_out,
       bit_extender_3_out, bit_extender_4_out, bit_extender_5_out, branch, EX_IR, ex_mem_1_aluresult_2,
       ex_mem_1_auipc_addr_2, ex_mem_1_pc_4_2, id_ex_1_imm1_2, id_ex_1_imm2_2, id_ex_1_imm_20_2,
       id_ex_1_pc_4_2, ID_IR, if_id_1_pc_4_out, IF_IR, MEM_IR, mem_wb_1_aluresult_2, mem_wb_1_auipc_addr_2,
       mem_wb_1_pc_4_2, mem_wb_1_readdata_2, multiplexer_1_out, multiplexer_5_out, multiplexer_6_out,
       multiplexer_9_out, multiplexer_11_out, PC_4, R1, R2, ram_1_data, regifile_1_r1, regifile_1_r2,
       shifter_1_out, shifter_2_out, WB_IR;

  Button \u_总复位  (.out(RST));
  Button _1 (.out(IR1));
  Button _2 (.out(IR2));
  Button _3 (.out(IR3));
  // Probe on \总周期数 
  // Probe on \总周期数 
  Button \u_继续运行  (.out(Go));
  LED #(.active("true")) led_1 (.in(W1));
  LED #(.active("true")) led_2 (.in(W2));
  LED #(.active("true")) led_3 (.in(W3));
  Hex_Digit_Display hex_digit_display_1 (.value(LedData[31:28]));  // open: dp
  // Probe on IF_PC[19:0]
  // RiscV_Probe riscv_probe_1: pin names not known; wires that end beside it: IF_IR
  Hex_Digit_Display hex_digit_display_2 (.value(LedData[23:20]));  // open: dp
  Hex_Digit_Display hex_digit_display_3 (.value(LedData[27:24]));  // open: dp
  // Probe on ID_PC[19:0]
  // RiscV_Probe riscv_probe_2: pin names not known; wires that end beside it: ID_IR
  Hex_Digit_Display hex_digit_display_4 (.value(LedData[19:16]));  // open: dp
  Hex_Digit_Display hex_digit_display_5 (.value(LedData[15:12]));  // open: dp
  or or_1 (or_1_out, EX_JALR, EX_JAL, isBranch);
  Hex_Digit_Display hex_digit_display_6 (.value(LedData[7:4]));  // open: dp
  Hex_Digit_Display hex_digit_display_7 (.value(LedData[11:8]));  // open: dp
  Clock #(.highDuration(1), .lowDuration(1)) clock_1 (.out(clock_1_out));
  // Probe on EX_PC[19:0]
  // RiscV_Probe riscv_probe_3: pin names not known; wires that end beside it: clock_1_out, EX_IR, CLK
  Multiplexer #(.select(1), .width(32), .disabled("Z"), .enable("false")) multiplexer_1 (
    .in0(PC_4), .in1(branch), .out(multiplexer_1_out), .sel(or_1_out));
  Hex_Digit_Display hex_digit_display_8 (.value(LedData[3:0]));  // open: dp
  or or_2 (or_2_out, and_1_out, Go);
  and and_1 (and_1_out, not_1_out, not_2_out);
  not not_1 (not_1_out, hazzard);
  not not_2 (not_2_out, halt);
  // Probe on \总周期数 
  // Probe on M_PC[19:0]
  // RiscV_Probe riscv_probe_4: pin names not known; wires that end beside it: MEM_IR
  // Probe on \总周期数 
  // Probe on \无条件分支数 
  // Probe on {16{1'b0}}
  // Probe on \插入气泡数 
  // Probe on {16{1'b0}}
  Register #(.width(32), .trigger("rising"), .Select("low")) PC (
    .D(multiplexer_1_out), .en(or_2_out), .Q(IF_PC), .clk(CLK), .clr(RST));
  // Probe on IF_PC[11:0]
  // Probe on WB_PC[19:0]
  // RiscV_Probe riscv_probe_5: pin names not known; wires that end beside it: WB_IR
  Adder #(.width(32)) adder_1 (.a(IF_PC), .b(32'h4), .out(PC_4));  // open: cin, cout
  // Probe on ID_PC[11:0]
  // Probe on EX_PC[11:0]
  not not_3 (not_3_out, register_1_q);
  Register #(.width(1), .trigger("rising"), .Select("low")) register_1 (
    .D(halt), .Q(register_1_q), .clk(CLK), .clr(RST));  // open: en
  // RiscV_Probe riscv_probe_6: pin names not known; wires that end beside it: IF_IR
  // Probe on M_PC[11:0]
  D_Flip_Flop #(.trigger("high"), .Pre_Clr_Positions("LEGACY"), .NegatePresetClear("false"), .enable("true"), .NewFFLayout("false")) d_ff_1 (.Q(d_ff_1_q));  // open: clk, D, Qn, preset, en, reset
  // Probe on 13'h870
  Counter #(.width(16), .max('hffff), .ongoal("wrap"), .trigger("rising"), .behavior("new")) counter_1 (
    .count(not_3_out), .Q(\总周期数 ), .clk(CLK));  // open: load, D, carry, clr, preset, down
  ROM #(.addrWidth(10), .dataWidth(32), .Select("high")) rom_1 (.addr(IF_PC[11:2]), .data(IF_IR));
  or or_3 (or_3_out, ~halt, Go);  // OR_Gate
  // Probe on WB_PC[11:0]
  Comparator #(.width(13), .mode("twosComplement")) comparator_1 (
    .a(CNT_num), .b(13'h870), .eq(comparator_1_eq), .lt(comparator_1_lt));  // open: gt
  Clock #(.highDuration(1), .lowDuration(1)) clock_2 (.out(clock_2_out));
  or or_4 (or_4_out, EX_JALR, EX_JAL, isBranch);
  and and_2 (and_2_out, ~hazzard, or_3_out);  // AND_Gate
  Counter #(.width(13), .max('h1fff), .ongoal("stay"), .trigger("rising"), .behavior("old")) counter_2 (
    .count(comparator_1_lt), .Q(CNT_num), .clk(clock_2_out));  // open: load, D, carry, clr, preset
  nand nand_1 (nand_1_out, d_ff_1_q, comparator_1_eq);
  IF_ID if_id_1 (
    .IR_in(IF_IR), .PC_in(IF_PC), .PC_4_in(PC_4), .IR_out(ID_IR), .PC_out(ID_PC),
    .PC_4_out(if_id_1_pc_4_out), .RST(RST), .branchTaken(or_4_out), .en(and_2_out), .clk(CLK),
    .isBubble(1'b0), .isBubble_2(if_id_1_isbubble_2));  // open: predictJump, predictJump_2
  assign CLK = nand_1_out ? clock_2_out : 1'bz;  // Controlled_Buffer controlled_buffer_1
  Pull_Resistor #(.pull(1)) pull_resistor_1 (.node(CLK));
  \单周期硬布线控制器  \u_单周期硬布线控制器_1  (
    .Funct({ID_IR[30], ID_IR[25], ID_IR[14:12]}), .OP(ID_IR[6:2]), .ALU_OP(\单周期硬布线控制器_1_alu_op ),
    .MemToReg(\单周期硬布线控制器_1_memtoreg ), .MemWrite(\单周期硬布线控制器_1_memwrite ), .ALU_SRC(\单周期硬布线控制器_1_alu_src ),
    .RegWrite(\单周期硬布线控制器_1_regwrite ), .ecall(\单周期硬布线控制器_1_ecall ), .S_type(\单周期硬布线控制器_1_s_type ),
    .Jalr(JALR), .Beq(Beq), .JAL(JAL), .Bne(Bne), .in_3(ID_IR[21]), .uret(\单周期硬布线控制器_1_uret ), .AUIPC(AUIPC),
    .LHU(LHU), .BLTU(Bltu), .rs1_used(\单周期硬布线控制器_1_rs1_used ), .rs2_used(\单周期硬布线控制器_1_rs2_used ));  // open: CSRRSI, CSRRCI
  Multiplexer #(.select(1), .width(5), .disabled("Z"), .enable("false")) multiplexer_2 (
    .in0(ID_IR[19:15]), .in1(5'b10001), .out(rs1), .sel(\单周期硬布线控制器_1_ecall ));
  assign bit_extender_1_out = {{12{ID_IR[31]}}, ID_IR[31:12]};  // Bit_Extender bit_extender_1
  data_check data_check_1 (
    .rs1(rs1), .EX_RegWrite(EX_RegWrite), .ecall(\单周期硬布线控制器_1_ecall ), .rs2(rs2),
    .MEM_RegWrite(MEM_RegWrite), .EX_rd(EX_rd), .rs1_used(\单周期硬布线控制器_1_rs1_used ),
    .rs2_used(\单周期硬布线控制器_1_rs2_used ), .MEM_rd(MEM_rd), .hazzard(hazzard));
  Multiplexer #(.select(1), .width(5), .disabled("Z"), .enable("false")) multiplexer_3 (
    .in0(ID_IR[24:20]), .in1(5'b01010), .out(rs2), .sel(\单周期硬布线控制器_1_ecall ));
  Multiplexer #(.select(1), .width(12), .disabled("Z"), .enable("false")) multiplexer_4 (
    .in0(ID_IR[31:20]), .in1({ID_IR[31:25], ID_IR[11:7]}), .out(multiplexer_4_out), .sel(\单周期硬布线控制器_1_s_type ));
  Shifter #(.width(32), .shift("ll")) shifter_1 (.in(bit_extender_1_out), .\dist (5'b01100), .out(shifter_1_out));
  or or_5 (or_5_out, EX_JAL, EX_JALR);
  and and_3 (and_3_out, or_5_out, ~halt);  // AND_Gate
  assign bit_extender_2_out = {{20{multiplexer_4_out[11]}}, multiplexer_4_out};  // Bit_Extender bit_extender_2
  assign bit_extender_3_out = {{20{ID_IR[31]}}, {ID_IR[31], ID_IR[7], ID_IR[30:25], ID_IR[11:8]}};  // Bit_Extender bit_extender_3
  assign bit_extender_4_out = {{12{ID_IR[31]}}, {ID_IR[31], ID_IR[19:12], ID_IR[20], ID_IR[30:21]}};  // Bit_Extender bit_extender_4
  Counter #(.width(16), .max('hffff), .ongoal("wrap"), .trigger("rising"), .behavior("new")) counter_3 (
    .count(and_3_out), .Q(\无条件分支数 ), .clk(CLK));  // open: load, D, carry, clr, preset, down
  not not_4 (not_4_out, CLK);
  Regifile regifile_1 (
    .Din(RDin), .Clk(not_4_out), .R1(regifile_1_r1), .R2(regifile_1_r2), .WE(RegWrite), .W_num(WB_rd),
    .R1_num(rs1), .R2_num(rs2));
  Multiplexer #(.select(1), .width(32), .disabled("Z"), .enable("false")) multiplexer_5 (
    .in0(bit_extender_3_out), .in1(bit_extender_4_out), .out(multiplexer_5_out), .sel(JAL));
  or or_6 (or_6_out, ~halt, Go);  // OR_Gate
  or or_7 (or_7_out, or_4_out, hazzard);
  ID_EX id_ex_1 (
    .Beq(Beq), .JAL(JAL), .Bne(Bne), .JALR(JALR), .MemToReg(\单周期硬布线控制器_1_memtoreg ), .AUIPC(AUIPC),
    .AluOp(\单周期硬布线控制器_1_alu_op ), .LHU(LHU), .AluSrcB(\单周期硬布线控制器_1_alu_src ), .BLTU(Bltu),
    .RegWrie(\单周期硬布线控制器_1_regwrite ), .ecall(\单周期硬布线控制器_1_ecall ), .uret(\单周期硬布线控制器_1_uret ),
    .R1(regifile_1_r1), .R2(regifile_1_r2), .rd(ID_IR[11:7]), .imm1(bit_extender_2_out),
    .imm2(multiplexer_5_out), .IR(ID_IR), .PC(ID_PC), .PC_4(if_id_1_pc_4_out), .Beq_2(id_ex_1_beq_2),
    .JAL_2(EX_JAL), .Bne_2(id_ex_1_bne_2), .JALR_2(EX_JALR), .MemToReg_2(id_ex_1_memtoreg_2),
    .AUIPC_2(id_ex_1_auipc_2), .AluOp_2(id_ex_1_aluop_2), .LHU_2(id_ex_1_lhu_2),
    .AluSrcB_2(id_ex_1_alusrcb_2), .BLTU_2(id_ex_1_bltu_2), .RegWrie_2(EX_RegWrite), .ecall_2(EX_ecall),
    .R1_2(R1), .R2_2(R2), .rd_2(EX_rd), .imm1_2(id_ex_1_imm1_2), .imm2_2(id_ex_1_imm2_2), .IR_2(EX_IR),
    .PC_2(EX_PC), .PC_4_2(id_ex_1_pc_4_2), .reset(RST), .flush(or_7_out), .enable(or_6_out), .clk(CLK),
    .MemWrite(\单周期硬布线控制器_1_memwrite ), .MemWrite_2(id_ex_1_memwrite_2), .imm_20(shifter_1_out),
    .imm_20_2(id_ex_1_imm_20_2), .isBubblet(if_id_1_isbubble_2), .isBubble(Ex_isBubble));  // open: uret_2, rs1_redirect, rs1_redirect_2, rs2_redirect_2, rs2_redirect, predictJump, predictJump_2
  Shifter #(.width(32), .shift("ll")) shifter_2 (.in(id_ex_1_imm2_2), .\dist (5'b00001), .out(shifter_2_out));
  and and_4 (and_4_out, id_ex_1_bltu_2, alu_1_out_6);
  Multiplexer #(.select(1), .width(32), .disabled("Z"), .enable("false")) multiplexer_6 (
    .in0(R2), .in1(id_ex_1_imm1_2), .out(multiplexer_6_out), .sel(id_ex_1_alusrcb_2));
  and and_5 (and_5_out, Ex_isBubble, ~halt);  // AND_Gate
  Counter #(.width(16), .max('hffff), .ongoal("wrap"), .trigger("rising"), .behavior("new")) counter_4 (
    .count(and_5_out), .Q(\插入气泡数 ), .clk(CLK));  // open: load, D, carry, clr, preset, down
  or or_8 (isBranch, and_4_out, and_6_out, and_7_out);
  and and_6 (and_6_out, id_ex_1_beq_2, alu_1_equal);
  and and_7 (and_7_out, ~alu_1_equal, id_ex_1_bne_2);  // AND_Gate
  ALU alu_1 (
    .X(R1), .Y(multiplexer_6_out), .AluOP(id_ex_1_aluop_2), .Equal(alu_1_equal), .Result(alu_1_result),
    .out_6(alu_1_out_6));  // open: Result_2, out_4
  Adder #(.width(32)) adder_2 (.a(shifter_2_out), .b(EX_PC), .out(adder_2_out));  // open: cin, cout
  Comparator #(.width(32), .mode("twosComplement")) comparator_2 (
    .a(R1), .b(32'h22), .eq(comparator_2_eq));  // open: gt, lt
  assign and_8_out = alu_1_result & 32'hfffffffe;  // AND_Gate and_8, 32 bits wide
  and and_9 (and_9_out, EX_ecall, comparator_2_eq);
  Adder #(.width(32)) adder_3 (.a(EX_PC), .b(id_ex_1_imm_20_2), .out(adder_3_out));  // open: cin, cout
  and and_10 (EX_halt, EX_ecall, ~comparator_2_eq);  // AND_Gate
  Register #(.width(32), .trigger("rising"), .Select("low")) register_2 (
    .D(R2), .en(and_9_out), .Q(LedData), .clk(CLK));  // open: clr
  Multiplexer #(.select(1), .width(32), .disabled("Z"), .enable("false")) multiplexer_7 (
    .in0(adder_2_out), .in1(and_8_out), .out(branch), .sel(EX_JALR));
  or or_9 (or_9_out, ~halt, Go);  // OR_Gate
  EX_MEM ex_mem_1 (
    .JAL(EX_JAL), .JALR(EX_JALR), .MemToReg(id_ex_1_memtoreg_2), .AUIPC(id_ex_1_auipc_2),
    .MemWrite(id_ex_1_memwrite_2), .LHU(id_ex_1_lhu_2), .RegWrie(EX_RegWrite), .halt(EX_halt),
    .ALUResult(alu_1_result), .Write(R2), .rd(EX_rd), .IR(EX_IR), .PC(EX_PC), .PC_4(id_ex_1_pc_4_2),
    .JAL_2(ex_mem_1_jal_2), .JALR_2(ex_mem_1_jalr_2), .MemToReg_2(ex_mem_1_memtoreg_2),
    .AUIPC_2(ex_mem_1_auipc_2), .MemWrite_2(MemWrite), .LHU_2(ex_mem_1_lhu_2), .RegWrie_2(MEM_RegWrite),
    .halt_2(ex_mem_1_halt_2), .ALUResult_2(ex_mem_1_aluresult_2), .Write_2(MDin), .rd_2(MEM_rd),
    .IR_2(MEM_IR), .PC_2(M_PC), .PC_4_2(ex_mem_1_pc_4_2), .reset(RST), .enable(or_9_out), .clk(CLK),
    .AUIPC_addr(adder_3_out), .AUIPC_addr_2(ex_mem_1_auipc_addr_2));
  RAM #(.addrWidth(10), .dataWidth(32), .bus("separate"), .Select("high")) ram_1 (
    .addr(ex_mem_1_aluresult_2[11:2]), .din(MDin), .data(ram_1_data), .str(MemWrite), .sel(1'b1), .clk(CLK),
    .ld(1'b1), .clr(RST));
  or or_10 (or_10_out, ~halt, Go);  // OR_Gate
  MEM_WB mem_wb_1 (
    .JAL(ex_mem_1_jal_2), .JALR(ex_mem_1_jalr_2), .MemToReg(ex_mem_1_memtoreg_2), .AUIPC(ex_mem_1_auipc_2),
    .LHU(ex_mem_1_lhu_2), .RegWrie(MEM_RegWrite), .halt(ex_mem_1_halt_2), .ALUResult(ex_mem_1_aluresult_2),
    .ReadData(ram_1_data), .IR(MEM_IR), .PC(M_PC), .PC_4(ex_mem_1_pc_4_2), .JAL_2(mem_wb_1_jal_2),
    .JALR_2(mem_wb_1_jalr_2), .MemToReg_2(mem_wb_1_memtoreg_2), .AUIPC_2(mem_wb_1_auipc_2),
    .LHU_2(mem_wb_1_lhu_2), .RegWrie_2(RegWrite), .halt_2(halt), .ALUResult_2(mem_wb_1_aluresult_2),
    .ReadData_2(mem_wb_1_readdata_2), .IR_2(WB_IR), .PC_2(WB_PC), .PC_4_2(mem_wb_1_pc_4_2), .reset(RST),
    .enable(or_10_out), .clk(CLK), .AUIPC_addr(ex_mem_1_auipc_addr_2), .AUIPC_addr_2(mem_wb_1_auipc_addr_2),
    .rd(MEM_rd), .rd_2(WB_rd));
  Multiplexer #(.select(1), .width(32), .disabled("Z"), .enable("false")) multiplexer_8 (
    .in0(multiplexer_9_out), .in1(bit_extender_5_out), .out(RDin), .sel(mem_wb_1_lhu_2));
  assign bit_extender_5_out = {{16{1'b0}}, multiplexer_10_out};  // Bit_Extender bit_extender_5
  Multiplexer #(.select(1), .width(32), .disabled("Z"), .enable("false")) multiplexer_9 (
    .in0(multiplexer_11_out), .in1(mem_wb_1_auipc_addr_2), .out(multiplexer_9_out), .sel(mem_wb_1_auipc_2));
  Multiplexer #(.select(1), .width(16), .disabled("Z"), .enable("false")) multiplexer_10 (
    .in0(multiplexer_12_out), .in1(multiplexer_12_out_2), .out(multiplexer_10_out),
    .sel(mem_wb_1_aluresult_2[1]));
  or or_11 (or_11_out, mem_wb_1_jalr_2, mem_wb_1_jal_2);
  Multiplexer #(.select(1), .width(32), .disabled("Z"), .enable("false")) multiplexer_11 (
    .in0({multiplexer_12_out_2, multiplexer_12_out}), .in1(mem_wb_1_pc_4_2), .out(multiplexer_11_out),
    .sel(or_11_out));
  Multiplexer #(.select(1), .width(32), .disabled("Z"), .enable("false")) multiplexer_12 (
    .in0(mem_wb_1_aluresult_2), .in1(mem_wb_1_readdata_2), .out({multiplexer_12_out_2, multiplexer_12_out}),
    .sel(mem_wb_1_memtoreg_2));

  // Other names for the same wires on the sheet: MEM_PC[31:0] = M_PC; WB_RegWrite = RegWrite

  // Notes on the sheet:
  //   中断源
  //   时空图监测，可删除
  //   中断等待指示
  //   数码管输出
  //   指令探针
  //   指令存储器
  //   流水调试日志用
  //   控制位
  //   暂停节拍，不能为0
  //   contents of rom_1 (hex, n*v repeats v):
  //   100493 100006f 100493 200913 300993 100006f 100493 200913 300993 100006f 100493 200913 300993
  //   100006f 100493 200913 300993 41c000ef 100413 100493 1f49493 900533 2200893 73 24d493 48463 fedff06f
  //   900533 2200893 73 100493 249493 900533 2200893 73 48463 fedff06f 100493 1f49493 900533 2200893 73
  //   4034d493 900533 2200893 73 4044d493 900533 2200893 73 4044d493 900533 2200893 73 4044d493 900533
  //   2200893 73 4044d493 900533 2200893 73 4044d493 900533 2200893 73 4044d493 900533 2200893 73 4044d493
  //   900533 2200893 73 100413 1f41993 41f9d993 433 c00913 300b13 140413 f47413 800293 100313 499993
  //   89e9b3 1300533 2200893 73 406282b3 fe0294e3 140413 f00f93 1f47433 1c41413 800293 100313 49d993
  //   89e9b3 1300533 2200893 73 406282b3 fe0294e3 1c45413 406b0b33 b0463 f95ff06f 2b3 fff2c293 829293
  //   ff2e293 500533 2200893 73 fff00413 493 84a023 140413 448493 84a023 140413 448493 84a023 140413
  //   448493 84a023 140413 448493 84a023 140413 448493 84a023 140413 448493 84a023 140413 448493 84a023
  //   140413 448493 84a023 140413 448493 84a023 140413 448493 84a023 140413 448493 84a023 140413 448493
  //   84a023 140413 448493 84a023 140413 448493 84a023 140413 448493 84a023 140413 448493 140413 433
  //   3c00493 42983 4aa03 149a2b3 28663 134a023 1442023 ffc48493 fe9412e3 800533 2200893 73 440413 3c00493
  //   fc9416e3 3200893 73 fff00293 7700493 849493 7748493 900533 2200893 73 1000e13 54c4b3 900533 2200893
  //   73 fffe0e13 fe0e16e3 a00893 73 13 430497 900533 2200893 73 430497 900533 2200893 73 430497 900533
  //   2200893 73 430497 900533 2200893 73 430497 900533 2200893 73 430497 900533 2200893 73 430497 900533
  //   2200893 73 430497 900533 2200893 73 a00893 73 313 1000e13 8400493 849493 8348493 400913 891913
  //   490913 849493 8248493 849493 8148493 891913 490913 891913 490913 932023 12484b3 430313 fffe0e13
  //   fe0e18e3 2000e13 313 35483 900533 2200893 73 230313 fffe0e13 fe0e14e3 a00893 73 ff100493 900533
  //   2200893 73 148493 fe9068e3 900533 2200893 73 a00893 73 a00893 73 413 140413 800533 2200893 73 240413
  //   800533 2200893 73 340413 800533 2200893 73 440413 800533 2200893 73 540413 800533 2200893 73 640413
  //   800533 2200893 73 740413 800533 2200893 73 840413 800533 2200893 2200893 73 8067
  //   戳工具置1进入计数暂停模式，ctrl+k时钟自动运行到对应节拍暂停
  //   ctrl+k关闭时钟连续运行，将控制位置零，进入单步调试模式调试
  //   Beq,Bne,Bltu
  //   AUIPC
  //   可计数暂停的时钟源
  //   JAL
  //   JALR
  //   指令字
  //   JAL
  //   Beq
  //   Bne
  //   MemToReg
  //   MemWrite
  //   AluOP
  //   AluSrcB
  //   RegWrite
  //   为方便自动评测，需要输出流水线各段保存的PC值，注意是PC不是PC+4，另外ID段寄存器写入信息，Mem段内存写入信息也要输出
  //   数据存储器
  //   LHU
  //   AUIPC
  //   JAL,JALR
endmodule
module \重定向流水线  (
  output RegWrite,
  output MemWrite,
  output [31:0] IF_PC,
  output [31:0] ID_PC,
  output [31:0] EX_PC,
  output [31:0] M_PC,
  output [31:0] WB_PC,
  output [31:0] RDin,
  output [31:0] MDin,
  output [31:0] LedData
);

  wire alu_1_equal, alu_1_out_6, and_1_out, and_2_out, and_3_out, and_4_out, and_5_out, and_7_out, AUIPC,
       CLK, clock_1_out, clock_2_out, comparator_1_eq, comparator_1_lt, comparator_2_eq, d_ff_1_q, EX_ecall,
       EX_halt, Ex_isBubble, EX_JAL, EX_JALR, ex_mem_1_auipc_2, ex_mem_1_halt_2, ex_mem_1_jal_2,
       ex_mem_1_jalr_2, ex_mem_1_lhu_2, ex_mem_1_memtoreg_2, EX_MemToReg, EX_RegWrite, Go, halt,
       id_ex_1_alusrcb_2, id_ex_1_auipc_2, id_ex_1_beq_2, id_ex_1_bltu_2, id_ex_1_bne_2, id_ex_1_lhu_2,
       id_ex_1_memwrite_2, if_id_1_isbubble_2, IR1, IR2, IR3, isBranch, JAL, JALR, LHU, loadUse,
       MEM_RegWrite, mem_wb_1_auipc_2, mem_wb_1_jal_2, mem_wb_1_jalr_2, mem_wb_1_lhu_2, mem_wb_1_memtoreg_2,
       nand_1_out, not_1_out, not_2_out, not_3_out, not_4_out, or_1_out, or_2_out, or_3_out, or_4_out,
       or_5_out, or_6_out, or_7_out, or_9_out, or_10_out, or_11_out, register_1_q, RST, W1, W2, W3,
       \单周期硬布线控制器_1_alu_src , \单周期硬布线控制器_1_beq , \单周期硬布线控制器_1_bltu , \单周期硬布线控制器_1_bne , \单周期硬布线控制器_1_ecall ,
       \单周期硬布线控制器_1_memtoreg , \单周期硬布线控制器_1_memwrite , \单周期硬布线控制器_1_regwrite , \单周期硬布线控制器_1_rs1_used ,
       \单周期硬布线控制器_1_rs2_used , \单周期硬布线控制器_1_s_type , \单周期硬布线控制器_1_uret ;
  wire [1:0] id_ex_1_rs1_redirect_2, id_ex_1_rs2_redirect_2, redirect_1_rs1_redirect, redirect_1_rs2_redirect;
  wire [3:0] id_ex_1_aluop_2, \单周期硬布线控制器_1_alu_op ;
  wire [4:0] EX_rd, MEM_rd, rs1, rs2, WB_rd;
  wire [11:0] multiplexer_4_out;
  wire [12:0] CNT_num;
  wire [15:0] \LoadUse次数 , multiplexer_13_out, multiplexer_15_out, multiplexer_15_out_2, \总周期数 , \插入气泡数 ,
       \无条件分支数 ;
  wire [31:0] adder_2_out, adder_3_out, alu_1_result, and_6_out, bit_extender_1_out, bit_extender_2_out,
       bit_extender_3_out, bit_extender_4_out, bit_extender_5_out, branch, EX_IR, ex_mem_1_aluresult_2,
       ex_mem_1_auipc_addr_2, ex_mem_1_pc_4_2, id_ex_1_imm1_2, id_ex_1_imm2_2, id_ex_1_imm_20_2,
       id_ex_1_pc_4_2, id_ex_1_r1_2, id_ex_1_r2_2, ID_IR, if_id_1_pc_4_out, IF_IR, MEM_AluRes, MEM_IR,
       mem_wb_1_aluresult_2, mem_wb_1_auipc_addr_2, mem_wb_1_pc_4_2, mem_wb_1_readdata_2, multiplexer_1_out,
       multiplexer_5_out, multiplexer_6_out, multiplexer_12_out, multiplexer_14_out, PC_4, R1, R2,
       ram_1_data, regifile_1_r1, regifile_1_r2, shifter_1_out, shifter_2_out, WB_IR;

  Button \u_总复位  (.out(RST));
  Button _1 (.out(IR1));
  Button _2 (.out(IR2));
  Button _3 (.out(IR3));
  // Probe on \总周期数 
  // Probe on \总周期数 
  Button \u_继续运行  (.out(Go));
  LED #(.active("true")) led_1 (.in(W1));
  LED #(.active("true")) led_2 (.in(W2));
  LED #(.active("true")) led_3 (.in(W3));
  Hex_Digit_Display hex_digit_display_1 (.value(LedData[31:28]));  // open: dp
  // Probe on IF_PC[19:0]
  // RiscV_Probe riscv_probe_1: pin names not known; wires that end beside it: IF_IR
  Hex_Digit_Display hex_digit_display_2 (.value(LedData[23:20]));  // open: dp
  Hex_Digit_Display hex_digit_display_3 (.value(LedData[27:24]));  // open: dp
  // Probe on ID_PC[19:0]
  // RiscV_Probe riscv_probe_2: pin names not known; wires that end beside it: ID_IR
  Hex_Digit_Display hex_digit_display_4 (.value(LedData[19:16]));  // open: dp
  Hex_Digit_Display hex_digit_display_5 (.value(LedData[15:12]));  // open: dp
  Hex_Digit_Display hex_digit_display_6 (.value(LedData[7:4]));  // open: dp
  Hex_Digit_Display hex_digit_display_7 (.value(LedData[11:8]));  // open: dp
  Clock #(.highDuration(1), .lowDuration(1)) clock_1 (.out(clock_1_out));
  // Probe on EX_PC[19:0]
  // RiscV_Probe riscv_probe_3: pin names not known; wires that end beside it: clock_1_out, EX_IR, CLK
  or or_1 (or_1_out, EX_JALR, EX_JAL, isBranch);
  Hex_Digit_Display hex_digit_display_8 (.value(LedData[3:0]));  // open: dp
  Multiplexer #(.select(1), .width(32), .disabled("Z"), .enable("false")) multiplexer_1 (
    .in0(PC_4), .in1(branch), .out(multiplexer_1_out), .sel(or_1_out));
  // Probe on \总周期数 
  // Probe on M_PC[19:0]
  // RiscV_Probe riscv_probe_4: pin names not known; wires that end beside it: MEM_IR
  or or_2 (or_2_out, and_1_out, Go);
  and and_1 (and_1_out, not_1_out, not_2_out);
  not not_1 (not_1_out, loadUse);
  not not_2 (not_2_out, halt);
  // Probe on \总周期数 
  // Probe on \无条件分支数 
  // Probe on {16{1'b0}}
  // Probe on \插入气泡数 
  // Probe on \LoadUse次数 
  // Probe on IF_PC[11:0]
  // Probe on WB_PC[19:0]
  // RiscV_Probe riscv_probe_5: pin names not known; wires that end beside it: WB_IR
  Register #(.width(32), .trigger("rising"), .Select("low")) PC (
    .D(multiplexer_1_out), .en(or_2_out), .Q(IF_PC), .clk(CLK), .clr(RST));
  // Probe on ID_PC[11:0]
  // Probe on EX_PC[11:0]
  not not_3 (not_3_out, register_1_q);
  Register #(.width(1), .trigger("rising"), .Select("low")) register_1 (
    .D(halt), .Q(register_1_q), .clk(CLK), .clr(RST));  // open: en
  Adder #(.width(32)) adder_1 (.a(IF_PC), .b(32'h4), .out(PC_4));  // open: cin, cout
  // Probe on M_PC[11:0]
  D_Flip_Flop #(.trigger("high"), .Pre_Clr_Positions("LEGACY"), .NegatePresetClear("false"), .enable("true"), .NewFFLayout("false")) d_ff_1 (.Q(d_ff_1_q));  // open: clk, D, Qn, preset, en, reset
  // Probe on 13'hc
  Counter #(.width(16), .max('hffff), .ongoal("wrap"), .trigger("rising"), .behavior("new")) counter_1 (
    .count(not_3_out), .Q(\总周期数 ), .clk(CLK));  // open: load, D, carry, clr, preset, down
  // RiscV_Probe riscv_probe_6: pin names not known; wires that end beside it: IF_IR
  // Probe on WB_PC[11:0]
  Comparator #(.width(13), .mode("twosComplement")) comparator_1 (
    .a(CNT_num), .b(13'hc), .eq(comparator_1_eq), .lt(comparator_1_lt));  // open: gt
  Clock #(.highDuration(1), .lowDuration(1)) clock_2 (.out(clock_2_out));
  ROM #(.addrWidth(10), .dataWidth(32), .Select("high")) rom_1 (.addr(IF_PC[11:2]), .data(IF_IR));
  or or_3 (or_3_out, ~halt, Go);  // OR_Gate
  nand nand_1 (nand_1_out, d_ff_1_q, comparator_1_eq);
  Counter #(.width(13), .max('h1fff), .ongoal("stay"), .trigger("rising"), .behavior("old")) counter_2 (
    .count(comparator_1_lt), .Q(CNT_num), .clk(clock_2_out));  // open: load, D, carry, clr, preset
  or or_4 (or_4_out, EX_JALR, EX_JAL, isBranch);
  and and_2 (and_2_out, ~loadUse, or_3_out);  // AND_Gate
  assign CLK = nand_1_out ? clock_2_out : 1'bz;  // Controlled_Buffer controlled_buffer_1
  Pull_Resistor #(.pull(1)) pull_resistor_1 (.node(CLK));
  IF_ID if_id_1 (
    .IR_in(IF_IR), .PC_in(IF_PC), .PC_4_in(PC_4), .IR_out(ID_IR), .PC_out(ID_PC),
    .PC_4_out(if_id_1_pc_4_out), .RST(RST), .branchTaken(or_4_out), .en(and_2_out), .clk(CLK),
    .isBubble(1'b0), .isBubble_2(if_id_1_isbubble_2));  // open: predictJump, predictJump_2
  \单周期硬布线控制器  \u_单周期硬布线控制器_1  (
    .Funct({ID_IR[30], ID_IR[25], ID_IR[14:12]}), .OP(ID_IR[6:2]), .ALU_OP(\单周期硬布线控制器_1_alu_op ),
    .MemToReg(\单周期硬布线控制器_1_memtoreg ), .MemWrite(\单周期硬布线控制器_1_memwrite ), .ALU_SRC(\单周期硬布线控制器_1_alu_src ),
    .RegWrite(\单周期硬布线控制器_1_regwrite ), .ecall(\单周期硬布线控制器_1_ecall ), .S_type(\单周期硬布线控制器_1_s_type ),
    .Jalr(JALR), .Beq(\单周期硬布线控制器_1_beq ), .JAL(JAL), .Bne(\单周期硬布线控制器_1_bne ), .in_3(ID_IR[21]),
    .uret(\单周期硬布线控制器_1_uret ), .AUIPC(AUIPC), .LHU(LHU), .BLTU(\单周期硬布线控制器_1_bltu ),
    .rs1_used(\单周期硬布线控制器_1_rs1_used ), .rs2_used(\单周期硬布线控制器_1_rs2_used ));  // open: CSRRSI, CSRRCI
  Multiplexer #(.select(1), .width(5), .disabled("Z"), .enable("false")) multiplexer_2 (
    .in0(ID_IR[19:15]), .in1(5'b10001), .out(rs1), .sel(\单周期硬布线控制器_1_ecall ));
  assign bit_extender_1_out = {{12{ID_IR[31]}}, ID_IR[31:12]};  // Bit_Extender bit_extender_1
  or or_5 (or_5_out, EX_JAL, EX_JALR);
  redirect redirect_1 (
    .rs1(rs1), .EX_RegWrite(EX_RegWrite), .ecall(\单周期硬布线控制器_1_ecall ), .rs2(rs2),
    .MEM_RegWrite(MEM_RegWrite), .EX_MemToReg(EX_MemToReg), .EX_rd(EX_rd), .rs1_used(\单周期硬布线控制器_1_rs1_used ),
    .rs2_used(\单周期硬布线控制器_1_rs2_used ), .MEM_rd(MEM_rd), .loadUse(loadUse),
    .rs1_redirect(redirect_1_rs1_redirect), .rs2_redirect(redirect_1_rs2_redirect));
  Multiplexer #(.select(1), .width(5), .disabled("Z"), .enable("false")) multiplexer_3 (
    .in0(ID_IR[24:20]), .in1(5'b01010), .out(rs2), .sel(\单周期硬布线控制器_1_ecall ));
  Multiplexer #(.select(1), .width(12), .disabled("Z"), .enable("false")) multiplexer_4 (
    .in0(ID_IR[31:20]), .in1({ID_IR[31:25], ID_IR[11:7]}), .out(multiplexer_4_out), .sel(\单周期硬布线控制器_1_s_type ));
  Shifter #(.width(32), .shift("ll")) shifter_1 (.in(bit_extender_1_out), .\dist (5'b01100), .out(shifter_1_out));
  Counter #(.width(16), .max('hffff), .ongoal("wrap"), .trigger("rising"), .behavior("new")) counter_3 (
    .count(or_5_out), .Q(\无条件分支数 ), .clk(CLK));  // open: load, D, carry, clr, preset, down
  assign bit_extender_2_out = {{20{multiplexer_4_out[11]}}, multiplexer_4_out};  // Bit_Extender bit_extender_2
  assign bit_extender_3_out = {{20{ID_IR[31]}}, {ID_IR[31], ID_IR[7], ID_IR[30:25], ID_IR[11:8]}};  // Bit_Extender bit_extender_3
  assign bit_extender_4_out = {{12{ID_IR[31]}}, {ID_IR[31], ID_IR[19:12], ID_IR[20], ID_IR[30:21]}};  // Bit_Extender bit_extender_4
  not not_4 (not_4_out, CLK);
  Regifile regifile_1 (
    .Din(RDin), .Clk(not_4_out), .R1(regifile_1_r1), .R2(regifile_1_r2), .WE(RegWrite), .W_num(WB_rd),
    .R1_num(rs1), .R2_num(rs2));
  Multiplexer #(.select(1), .width(32), .disabled("Z"), .enable("false")) multiplexer_5 (
    .in0(bit_extender_3_out), .in1(bit_extender_4_out), .out(multiplexer_5_out), .sel(JAL));
  or or_6 (or_6_out, ~halt, Go);  // OR_Gate
  or or_7 (or_7_out, or_4_out, loadUse);
  ID_EX id_ex_1 (
    .Beq(\单周期硬布线控制器_1_beq ), .JAL(JAL), .Bne(\单周期硬布线控制器_1_bne ), .JALR(JALR),
    .MemToReg(\单周期硬布线控制器_1_memtoreg ), .AUIPC(AUIPC), .AluOp(\单周期硬布线控制器_1_alu_op ), .LHU(LHU),
    .AluSrcB(\单周期硬布线控制器_1_alu_src ), .BLTU(\单周期硬布线控制器_1_bltu ), .RegWrie(\单周期硬布线控制器_1_regwrite ),
    .ecall(\单周期硬布线控制器_1_ecall ), .uret(\单周期硬布线控制器_1_uret ), .R1(regifile_1_r1), .R2(regifile_1_r2),
    .rd(ID_IR[11:7]), .imm1(bit_extender_2_out), .imm2(multiplexer_5_out), .IR(ID_IR), .PC(ID_PC),
    .PC_4(if_id_1_pc_4_out), .Beq_2(id_ex_1_beq_2), .JAL_2(EX_JAL), .Bne_2(id_ex_1_bne_2), .JALR_2(EX_JALR),
    .MemToReg_2(EX_MemToReg), .AUIPC_2(id_ex_1_auipc_2), .AluOp_2(id_ex_1_aluop_2), .LHU_2(id_ex_1_lhu_2),
    .AluSrcB_2(id_ex_1_alusrcb_2), .BLTU_2(id_ex_1_bltu_2), .RegWrie_2(EX_RegWrite), .ecall_2(EX_ecall),
    .R1_2(id_ex_1_r1_2), .R2_2(id_ex_1_r2_2), .rd_2(EX_rd), .imm1_2(id_ex_1_imm1_2), .imm2_2(id_ex_1_imm2_2),
    .IR_2(EX_IR), .PC_2(EX_PC), .PC_4_2(id_ex_1_pc_4_2), .reset(RST), .flush(or_7_out), .enable(or_6_out),
    .clk(CLK), .MemWrite(\单周期硬布线控制器_1_memwrite ), .MemWrite_2(id_ex_1_memwrite_2), .imm_20(shifter_1_out),
    .imm_20_2(id_ex_1_imm_20_2), .rs1_redirect(redirect_1_rs1_redirect),
    .rs1_redirect_2(id_ex_1_rs1_redirect_2), .rs2_redirect_2(id_ex_1_rs2_redirect_2),
    .rs2_redirect(redirect_1_rs2_redirect), .isBubblet(if_id_1_isbubble_2), .isBubble(Ex_isBubble));  // open: uret_2, predictJump, predictJump_2
  Multiplexer #(.select(2), .width(32), .disabled("Z"), .enable("false")) multiplexer_6 (
    .in0(id_ex_1_r2_2), .in1(RDin), .in2(MEM_AluRes), .out(multiplexer_6_out), .sel(id_ex_1_rs2_redirect_2));  // open: in3
  Shifter #(.width(32), .shift("ll")) shifter_2 (.in(id_ex_1_imm2_2), .\dist (5'b00001), .out(shifter_2_out));
  Counter #(.width(16), .max('hffff), .ongoal("wrap"), .trigger("rising"), .behavior("new")) counter_4 (
    .count(Ex_isBubble), .Q(\插入气泡数 ), .clk(CLK));  // open: load, D, carry, clr, preset, down
  and and_3 (and_3_out, id_ex_1_bltu_2, alu_1_out_6);
  Multiplexer #(.select(2), .width(32), .disabled("Z"), .enable("false")) multiplexer_7 (
    .in0(id_ex_1_r1_2), .in1(RDin), .in2(MEM_AluRes), .out(R1), .sel(id_ex_1_rs1_redirect_2));  // open: in3
  Multiplexer #(.select(1), .width(32), .disabled("Z"), .enable("false")) multiplexer_8 (
    .in0(multiplexer_6_out), .in1(id_ex_1_imm1_2), .out(R2), .sel(id_ex_1_alusrcb_2));
  or or_8 (isBranch, and_3_out, and_4_out, and_5_out);
  and and_4 (and_4_out, id_ex_1_beq_2, alu_1_equal);
  and and_5 (and_5_out, ~alu_1_equal, id_ex_1_bne_2);  // AND_Gate
  ALU alu_1 (
    .X(R1), .Y(R2), .AluOP(id_ex_1_aluop_2), .Equal(alu_1_equal), .Result(alu_1_result), .out_6(alu_1_out_6));  // open: Result_2, out_4
  Adder #(.width(32)) adder_2 (.a(shifter_2_out), .b(EX_PC), .out(adder_2_out));  // open: cin, cout
  Comparator #(.width(32), .mode("twosComplement")) comparator_2 (
    .a(R1), .b(32'h22), .eq(comparator_2_eq));  // open: gt, lt
  assign and_6_out = alu_1_result & 32'hfffffffe;  // AND_Gate and_6, 32 bits wide
  and and_7 (and_7_out, EX_ecall, comparator_2_eq);
  Adder #(.width(32)) adder_3 (.a(EX_PC), .b(id_ex_1_imm_20_2), .out(adder_3_out));  // open: cin, cout
  and and_8 (EX_halt, EX_ecall, ~comparator_2_eq);  // AND_Gate
  Register #(.width(32), .trigger("rising"), .Select("low")) register_2 (
    .D(R2), .en(and_7_out), .Q(LedData), .clk(CLK));  // open: clr
  Counter #(.width(16), .max('hffff), .ongoal("wrap"), .trigger("rising"), .behavior("new")) counter_5 (
    .count(loadUse), .Q(\LoadUse次数 ), .clk(CLK));  // open: load, D, carry, clr, preset, down
  Multiplexer #(.select(1), .width(32), .disabled("Z"), .enable("false")) multiplexer_9 (
    .in0(adder_2_out), .in1(and_6_out), .out(branch), .sel(EX_JALR));
  or or_9 (or_9_out, ~halt, Go);  // OR_Gate
  EX_MEM ex_mem_1 (
    .JAL(EX_JAL), .JALR(EX_JALR), .MemToReg(EX_MemToReg), .AUIPC(id_ex_1_auipc_2),
    .MemWrite(id_ex_1_memwrite_2), .LHU(id_ex_1_lhu_2), .RegWrie(EX_RegWrite), .halt(EX_halt),
    .ALUResult(alu_1_result), .Write(multiplexer_6_out), .rd(EX_rd), .IR(EX_IR), .PC(EX_PC),
    .PC_4(id_ex_1_pc_4_2), .JAL_2(ex_mem_1_jal_2), .JALR_2(ex_mem_1_jalr_2),
    .MemToReg_2(ex_mem_1_memtoreg_2), .AUIPC_2(ex_mem_1_auipc_2), .MemWrite_2(MemWrite),
    .LHU_2(ex_mem_1_lhu_2), .RegWrie_2(MEM_RegWrite), .halt_2(ex_mem_1_halt_2),
    .ALUResult_2(ex_mem_1_aluresult_2), .Write_2(MDin), .rd_2(MEM_rd), .IR_2(MEM_IR), .PC_2(M_PC),
    .PC_4_2(ex_mem_1_pc_4_2), .reset(RST), .enable(or_9_out), .clk(CLK), .AUIPC_addr(adder_3_out),
    .AUIPC_addr_2(ex_mem_1_auipc_addr_2));
  Multiplexer #(.select(1), .width(32), .disabled("Z"), .enable("false")) multiplexer_10 (
    .in0(ex_mem_1_aluresult_2), .in1(ex_mem_1_auipc_addr_2), .out(MEM_AluRes), .sel(ex_mem_1_auipc_2));
  RAM #(.addrWidth(10), .dataWidth(32), .bus("separate"), .Select("high")) ram_1 (
    .addr(ex_mem_1_aluresult_2[11:2]), .din(MDin), .data(ram_1_data), .str(MemWrite), .sel(1'b1), .clk(CLK),
    .ld(1'b1), .clr(RST));
  or or_10 (or_10_out, ~halt, Go);  // OR_Gate
  MEM_WB mem_wb_1 (
    .JAL(ex_mem_1_jal_2), .JALR(ex_mem_1_jalr_2), .MemToReg(ex_mem_1_memtoreg_2), .AUIPC(ex_mem_1_auipc_2),
    .LHU(ex_mem_1_lhu_2), .RegWrie(MEM_RegWrite), .halt(ex_mem_1_halt_2), .ALUResult(ex_mem_1_aluresult_2),
    .ReadData(ram_1_data), .IR(MEM_IR), .PC(M_PC), .PC_4(ex_mem_1_pc_4_2), .JAL_2(mem_wb_1_jal_2),
    .JALR_2(mem_wb_1_jalr_2), .MemToReg_2(mem_wb_1_memtoreg_2), .AUIPC_2(mem_wb_1_auipc_2),
    .LHU_2(mem_wb_1_lhu_2), .RegWrie_2(RegWrite), .halt_2(halt), .ALUResult_2(mem_wb_1_aluresult_2),
    .ReadData_2(mem_wb_1_readdata_2), .IR_2(WB_IR), .PC_2(WB_PC), .PC_4_2(mem_wb_1_pc_4_2), .reset(RST),
    .enable(or_10_out), .clk(CLK), .AUIPC_addr(ex_mem_1_auipc_addr_2), .AUIPC_addr_2(mem_wb_1_auipc_addr_2),
    .rd(MEM_rd), .rd_2(WB_rd));
  Multiplexer #(.select(1), .width(32), .disabled("Z"), .enable("false")) multiplexer_11 (
    .in0(multiplexer_12_out), .in1(bit_extender_5_out), .out(RDin), .sel(mem_wb_1_lhu_2));
  assign bit_extender_5_out = {{16{1'b0}}, multiplexer_13_out};  // Bit_Extender bit_extender_5
  Multiplexer #(.select(1), .width(32), .disabled("Z"), .enable("false")) multiplexer_12 (
    .in0(multiplexer_14_out), .in1(mem_wb_1_auipc_addr_2), .out(multiplexer_12_out), .sel(mem_wb_1_auipc_2));
  Multiplexer #(.select(1), .width(16), .disabled("Z"), .enable("false")) multiplexer_13 (
    .in0(multiplexer_15_out), .in1(multiplexer_15_out_2), .out(multiplexer_13_out),
    .sel(mem_wb_1_aluresult_2[1]));
  or or_11 (or_11_out, mem_wb_1_jalr_2, mem_wb_1_jal_2);
  Multiplexer #(.select(1), .width(32), .disabled("Z"), .enable("false")) multiplexer_14 (
    .in0({multiplexer_15_out_2, multiplexer_15_out}), .in1(mem_wb_1_pc_4_2), .out(multiplexer_14_out),
    .sel(or_11_out));
  Multiplexer #(.select(1), .width(32), .disabled("Z"), .enable("false")) multiplexer_15 (
    .in0(mem_wb_1_aluresult_2), .in1(mem_wb_1_readdata_2), .out({multiplexer_15_out_2, multiplexer_15_out}),
    .sel(mem_wb_1_memtoreg_2));

  // Other names for the same wires on the sheet: MEM_PC[31:0] = M_PC; WB_RegWrite = RegWrite

  // Notes on the sheet:
  //   中断源
  //   时空图监测，可删除
  //   中断等待指示
  //   数码管输出
  //   控制位
  //   流水调试日志用
  //   暂停节拍，不能为0
  //   指令探针
  //   指令存储器
  //   戳工具置1进入计数暂停模式，ctrl+k时钟自动运行到对应节拍暂停
  //   ctrl+k关闭时钟连续运行，将控制位置零，进入单步调试模式调试
  //   contents of rom_1 (hex, n*v repeats v):
  //   100493 100006f 100493 200913 300993 100006f 100493 200913 300993 100006f 100493 200913 300993
  //   100006f 100493 200913 300993 41c000ef 100413 100493 1f49493 900533 2200893 73 24d493 48463 fedff06f
  //   900533 2200893 73 100493 249493 900533 2200893 73 48463 fedff06f 100493 1f49493 900533 2200893 73
  //   4034d493 900533 2200893 73 4044d493 900533 2200893 73 4044d493 900533 2200893 73 4044d493 900533
  //   2200893 73 4044d493 900533 2200893 73 4044d493 900533 2200893 73 4044d493 900533 2200893 73 4044d493
  //   900533 2200893 73 100413 1f41993 41f9d993 433 c00913 300b13 140413 f47413 800293 100313 499993
  //   89e9b3 1300533 2200893 73 406282b3 fe0294e3 140413 f00f93 1f47433 1c41413 800293 100313 49d993
  //   89e9b3 1300533 2200893 73 406282b3 fe0294e3 1c45413 406b0b33 b0463 f95ff06f 2b3 fff2c293 829293
  //   ff2e293 500533 2200893 73 fff00413 493 84a023 140413 448493 84a023 140413 448493 84a023 140413
  //   448493 84a023 140413 448493 84a023 140413 448493 84a023 140413 448493 84a023 140413 448493 84a023
  //   140413 448493 84a023 140413 448493 84a023 140413 448493 84a023 140413 448493 84a023 140413 448493
  //   84a023 140413 448493 84a023 140413 448493 84a023 140413 448493 84a023 140413 448493 140413 433
  //   3c00493 42983 4aa03 149a2b3 28663 134a023 1442023 ffc48493 fe9412e3 800533 2200893 73 440413 3c00493
  //   fc9416e3 3200893 73 fff00293 7700493 849493 7748493 900533 2200893 73 1000e13 54c4b3 900533 2200893
  //   73 fffe0e13 fe0e16e3 a00893 73 13 430497 900533 2200893 73 430497 900533 2200893 73 430497 900533
  //   2200893 73 430497 900533 2200893 73 430497 900533 2200893 73 430497 900533 2200893 73 430497 900533
  //   2200893 73 430497 900533 2200893 73 a00893 73 313 1000e13 8400493 849493 8348493 400913 891913
  //   490913 849493 8248493 849493 8148493 891913 490913 891913 490913 932023 12484b3 430313 fffe0e13
  //   fe0e18e3 2000e13 313 35483 900533 2200893 73 230313 fffe0e13 fe0e14e3 a00893 73 ff100493 900533
  //   2200893 73 148493 fe9068e3 900533 2200893 73 a00893 73 a00893 73 413 140413 800533 2200893 73 240413
  //   800533 2200893 73 340413 800533 2200893 73 440413 800533 2200893 73 540413 800533 2200893 73 640413
  //   800533 2200893 73 740413 800533 2200893 73 840413 800533 2200893 2200893 73 8067
  //   可计数暂停的时钟源
  //   Beq,Bne,Bltu
  //   AUIPC
  //   JAL
  //   JALR
  //   指令字
  //   JAL
  //   Beq
  //   Bne
  //   为方便自动评测，需要输出流水线各段保存的PC值，注意是PC不是PC+4，另外ID段寄存器写入信息，Mem段内存写入信息也要输出
  //   MemToReg
  //   MemWrite
  //   AluOP
  //   AluSrcB
  //   RegWrite
  //   数据存储器
  //   LHU
  //   AUIPC
  //   JAL,JALR
endmodule

module \中断按键参考电路  (
  input  \同步清零信号 ,
  output \与中断屏蔽位与 
);

  wire \_1号中断_out , and_1_out, clock_1_out, d_ff_1_q, or_1_out, or_2_out;

  Clock #(.highDuration(1), .lowDuration(1)) clock_1 (.out(clock_1_out));
  Button \_1号中断  (.out(\_1号中断_out ));
  LED #(.active("true")) \_1号中断等待指示灯  (.in(or_1_out));
  or or_1 (or_1_out, \与中断屏蔽位与 , d_ff_1_q);
  D_Flip_Flop #(.trigger("rising"), .Pre_Clr_Positions("LEGACY"), .NegatePresetClear("false"), .enable("true"), .NewFFLayout("false")) d_ff_1 (
    .clk(\_1号中断_out ), .D(1'b1), .Q(d_ff_1_q), .reset(\与中断屏蔽位与 ));  // open: Qn, preset, en
  or or_2 (or_2_out, d_ff_1_q, \与中断屏蔽位与 );
  and and_1 (and_1_out, or_2_out, ~\同步清零信号 );  // AND_Gate
  D_Flip_Flop #(.trigger("rising"), .Pre_Clr_Positions("LEGACY"), .NegatePresetClear("false"), .enable("true"), .NewFFLayout("false")) IR1 (
    .clk(clock_1_out), .D(and_1_out), .Q(\与中断屏蔽位与 ));  // open: Qn, preset, en, reset

  // Notes on the sheet:
  //   中断信号采样参考电路
  //   Reset 
endmodule

module \单周期_单级中断  (
  input  IR1,
  input  IR2,
  input  IR3,
  output RegWrite,
  output MemWrite,
  output [31:0] PC,
  output [31:0] IR,
  output [31:0] RDin,
  output [31:0] MDin,
  output [31:0] LedData
);

  wire alu_1_equal, alu_1_out_6, and_2_out, and_3_out, and_4_out, and_5_out, and_7_out, and_8_out, and_9_out,
       and_11_out, AUIPC, clear1, clear2, clear3, CLK, comparator_1_eq, comparator_2_eq, comparator_3_eq,
       comparator_4_eq, comparator_5_eq, decoder_1_out1, decoder_1_out2, decoder_1_out3, ecall, Go, halt, IE,
       INT, IR1_t, IR2_t, IR3_t, IRA, IRB, IRC, isBranch, JAL, JALR, LHU, not_1_out, not_2_out, or_1_out,
       or_2_out, or_5_out, or_8_out, or_9_out, or_10_out, or_11_out, or_13_out, or_15_out, or_17_out,
       priority_encoder_1_gs, register_2_q, register_3_q, register_4_q, register_5_q, register_6_q,
       register_7_q, RST, URET, W1, W2, W3, \单周期硬布线控制器_1_alu_src , \单周期硬布线控制器_1_beq , \单周期硬布线控制器_1_bltu ,
       \单周期硬布线控制器_1_bne , \单周期硬布线控制器_1_memtoreg , \单周期硬布线控制器_1_s_type ;
  wire [1:0] priority_encoder_1_out, register_8_q;
  wire [3:0] \单周期硬布线控制器_1_alu_op ;
  wire [4:0] multiplexer_4_out, multiplexer_5_out;
  wire [11:0] multiplexer_6_out, shifter_1_out;
  wire [15:0] multiplexer_10_out, \总周期数 ;
  wire [19:0] shifter_2_out;
  wire [31:0] adder_2_out, adder_3_out, alu_1_result, and_6_out, bit_extender_1_out, bit_extender_2_out,
       bit_extender_3_out, bit_extender_4_out, bit_extender_5_out, INT_PC, multiplexer_2_out,
       multiplexer_3_out, multiplexer_8_out, multiplexer_9_out, multiplexer_11_out, multiplexer_12_out,
       multiplexer_13_out, multiplexer_14_out, next_PC, PC_4, R1, ram_1_data, ret_PC, shifter_3_out;

  Clock #(.highDuration(1), .lowDuration(1)) clock_1 (.out(CLK));
  Button _1 ();  // open: out
  Button _2 ();  // open: out
  Button _3 ();  // open: out
  Button \u_继续运行  (.out(Go));
  LED #(.active("true")) led_1 (.in(W1));
  LED #(.active("true")) led_2 (.in(W2));
  LED #(.active("true")) led_3 (.in(W3));
  Hex_Digit_Display hex_digit_display_1 (.value(LedData[31:28]));  // open: dp
  Comparator #(.width(16), .mode("twosComplement")) comparator_1 (
    .a(16'h23b), .b(\总周期数 ), .eq(comparator_1_eq));  // open: gt, lt
  Comparator #(.width(16), .mode("twosComplement")) comparator_2 (
    .a(\总周期数 ), .b(16'h1), .eq(comparator_2_eq));  // open: gt, lt
  Comparator #(.width(16), .mode("twosComplement")) comparator_3 (
    .a(\总周期数 ), .b(16'h4), .eq(comparator_3_eq));  // open: gt, lt
  Comparator #(.width(16), .mode("twosComplement")) comparator_4 (
    .a(\总周期数 ), .b(16'h7), .eq(comparator_4_eq));  // open: gt, lt
  Hex_Digit_Display hex_digit_display_2 (.value(LedData[27:24]));  // open: dp
  Hex_Digit_Display hex_digit_display_3 (.value(LedData[23:20]));  // open: dp
  or or_1 (or_1_out, comparator_1_eq, comparator_2_eq);
  assign IRA = or_1_out ? ~CLK : 1'bz;  // Controlled_Inverter controlled_inverter_1
  assign IRB = comparator_3_eq ? ~CLK : 1'bz;  // Controlled_Inverter controlled_inverter_2
  assign IRC = comparator_4_eq ? ~CLK : 1'bz;  // Controlled_Inverter controlled_inverter_3
  Hex_Digit_Display hex_digit_display_4 (.value(LedData[19:16]));  // open: dp
  Hex_Digit_Display hex_digit_display_5 (.value(LedData[15:12]));  // open: dp
  Pull_Resistor #(.pull(0)) pull_resistor_1 (.node(IRA));
  Pull_Resistor #(.pull(0)) pull_resistor_2 (.node(IRB));
  Pull_Resistor #(.pull(0)) pull_resistor_3 (.node(IRC));
  Hex_Digit_Display hex_digit_display_6 (.value(LedData[7:4]));  // open: dp
  Hex_Digit_Display hex_digit_display_7 (.value(LedData[11:8]));  // open: dp
  // Probe on \总周期数 
  Hex_Digit_Display hex_digit_display_8 (.value(LedData[3:0]));  // open: dp
  Multiplexer #(.select(1), .width(32), .disabled("Z"), .enable("false")) multiplexer_1 (
    .in0(PC_4), .in1(multiplexer_14_out), .out(next_PC), .sel(or_2_out));
  or or_2 (or_2_out, JALR, JAL, isBranch);
  not not_1 (not_1_out, halt);
  Button button_1 (.out(RST));
  Counter #(.width(16), .max('hffff), .ongoal("wrap"), .trigger("rising"), .behavior("new")) counter_1 (
    .count(not_1_out), .Q(\总周期数 ), .clk(CLK));  // open: load, D, carry, clr, preset, down
  or or_3 (IR1_t, IR1, IRA);
  Multiplexer #(.select(1), .width(32), .disabled("Z"), .enable("false")) multiplexer_2 (
    .in0(next_PC), .in1(ret_PC), .out(multiplexer_2_out), .sel(URET));
  Multiplexer #(.select(1), .width(32), .disabled("Z"), .enable("false")) multiplexer_3 (
    .in0(multiplexer_2_out), .in1(INT_PC), .out(multiplexer_3_out), .sel(INT));
  Comparator #(.width(32), .mode("twosComplement")) comparator_5 (
    .a(R1), .b(32'h22), .eq(comparator_5_eq));  // open: gt, lt
  or or_4 (IR2_t, IR2, IRB);
  or or_5 (or_5_out, Go, not_2_out);
  not not_2 (not_2_out, halt);
  and and_1 (halt, ecall, ~comparator_5_eq);  // AND_Gate
  and and_2 (and_2_out, ecall, comparator_5_eq);
  Register #(.width(32), .trigger("rising"), .Select("low")) u_PC (
    .D(multiplexer_3_out), .en(or_5_out), .Q(PC), .clk(CLK), .clr(RST));
  Register #(.width(32), .trigger("rising"), .Select("low")) register_1 (
    .D(MDin), .en(and_2_out), .Q(LedData), .clk(CLK));  // open: clr
  or or_6 (IR3_t, IR3, IRC);
  Adder #(.width(32)) adder_1 (.a(PC), .b(32'h4), .out(PC_4));  // open: cin, cout
  // RiscV_Probe riscv_probe_1: pin names not known; wires that end beside it: IR
  ROM #(.addrWidth(10), .dataWidth(32), .Select("high")) rom_1 (.addr(PC[11:2]), .data(IR));
  \单周期硬布线控制器  \u_单周期硬布线控制器_1  (
    .Funct({IR[30], IR[25], IR[14:12]}), .OP(IR[6:2]), .ALU_OP(\单周期硬布线控制器_1_alu_op ),
    .MemToReg(\单周期硬布线控制器_1_memtoreg ), .MemWrite(MemWrite), .ALU_SRC(\单周期硬布线控制器_1_alu_src ),
    .RegWrite(RegWrite), .ecall(ecall), .S_type(\单周期硬布线控制器_1_s_type ), .Jalr(JALR), .Beq(\单周期硬布线控制器_1_beq ),
    .JAL(JAL), .Bne(\单周期硬布线控制器_1_bne ), .in_3(IR[21]), .uret(URET), .AUIPC(AUIPC), .LHU(LHU),
    .BLTU(\单周期硬布线控制器_1_bltu ));  // open: rs1_used, rs2_used, CSRRSI, CSRRCI
  Multiplexer #(.select(1), .width(5), .disabled("Z"), .enable("false")) multiplexer_4 (
    .in0(IR[19:15]), .in1(5'b10001), .out(multiplexer_4_out), .sel(ecall));
  Multiplexer #(.select(1), .width(5), .disabled("Z"), .enable("false")) multiplexer_5 (
    .in0(IR[24:20]), .in1(5'b01010), .out(multiplexer_5_out), .sel(ecall));
  assign bit_extender_1_out = {{12{IR[31]}}, IR[31:12]};  // Bit_Extender bit_extender_1
  Multiplexer #(.select(1), .width(12), .disabled("Z"), .enable("false")) multiplexer_6 (
    .in0(IR[31:20]), .in1({IR[31:25], IR[11:7]}), .out(multiplexer_6_out), .sel(\单周期硬布线控制器_1_s_type ));
  Multiplexer #(.select(1), .width(32), .disabled("Z"), .enable("false")) multiplexer_7 (
    .in0(multiplexer_11_out), .in1(bit_extender_5_out), .out(RDin), .sel(LHU));
  Shifter #(.width(12), .shift("ll")) shifter_1 (
    .in({IR[31], IR[7], IR[30:25], IR[11:8]}), .\dist (4'b0001), .out(shifter_1_out));
  Shifter #(.width(20), .shift("ll")) shifter_2 (
    .in({IR[31], IR[19:12], IR[20], IR[30:21]}), .\dist (5'b00001), .out(shifter_2_out));
  Shifter #(.width(32), .shift("ll")) shifter_3 (.in(bit_extender_1_out), .\dist (5'b01100), .out(shifter_3_out));
  Regifile regifile_1 (
    .Din(RDin), .Clk(CLK), .R1(R1), .R2(MDin), .WE(RegWrite), .W_num(IR[11:7]), .R1_num(multiplexer_4_out),
    .R2_num(multiplexer_5_out));
  assign bit_extender_2_out = {{20{multiplexer_6_out[11]}}, multiplexer_6_out};  // Bit_Extender bit_extender_2
  assign bit_extender_3_out = {{20{shifter_1_out[11]}}, shifter_1_out};  // Bit_Extender bit_extender_3
  assign bit_extender_4_out = {{12{shifter_2_out[19]}}, shifter_2_out};  // Bit_Extender bit_extender_4
  Adder #(.width(32)) adder_2 (.a(PC), .b(shifter_3_out), .out(adder_2_out));  // open: cin, cout
  Multiplexer #(.select(1), .width(32), .disabled("Z"), .enable("false")) multiplexer_8 (
    .in0(MDin), .in1(bit_extender_2_out), .out(multiplexer_8_out), .sel(\单周期硬布线控制器_1_alu_src ));
  Multiplexer #(.select(1), .width(32), .disabled("Z"), .enable("false")) multiplexer_9 (
    .in0(bit_extender_3_out), .in1(bit_extender_4_out), .out(multiplexer_9_out), .sel(JAL));
  assign bit_extender_5_out = {{16{1'b0}}, multiplexer_10_out};  // Bit_Extender bit_extender_5
  ALU alu_1 (
    .X(R1), .Y(multiplexer_8_out), .AluOP(\单周期硬布线控制器_1_alu_op ), .Equal(alu_1_equal), .Result(alu_1_result),
    .out_6(alu_1_out_6));  // open: Result_2, out_4
  Multiplexer #(.select(1), .width(16), .disabled("Z"), .enable("false")) multiplexer_10 (
    .in0(multiplexer_11_out[15:0]), .in1(multiplexer_11_out[31:16]), .out(multiplexer_10_out),
    .sel(alu_1_result[1]));
  Adder #(.width(32)) adder_3 (.a(PC), .b(multiplexer_9_out), .out(adder_3_out));  // open: cin, cout
  and and_3 (and_3_out, \单周期硬布线控制器_1_bltu , alu_1_out_6);
  and and_4 (and_4_out, alu_1_equal, \单周期硬布线控制器_1_beq );
  and and_5 (and_5_out, ~alu_1_equal, \单周期硬布线控制器_1_bne );  // AND_Gate
  Multiplexer #(.select(1), .width(32), .disabled("Z"), .enable("false")) multiplexer_11 (
    .in0(multiplexer_12_out), .in1(adder_2_out), .out(multiplexer_11_out), .sel(AUIPC));
  or or_7 (isBranch, and_3_out, and_4_out, and_5_out);
  RAM #(.addrWidth(10), .dataWidth(32), .bus("separate"), .Select("high")) ram_1 (
    .addr(alu_1_result[11:2]), .din(MDin), .data(ram_1_data), .str(MemWrite), .sel(1'b1), .clk(CLK),
    .ld(1'b1), .clr(RST));
  or or_8 (or_8_out, JALR, JAL);
  Multiplexer #(.select(1), .width(32), .disabled("Z"), .enable("false")) multiplexer_12 (
    .in0(multiplexer_13_out), .in1(PC_4), .out(multiplexer_12_out), .sel(or_8_out));
  Multiplexer #(.select(1), .width(32), .disabled("Z"), .enable("false")) multiplexer_13 (
    .in0(alu_1_result), .in1(ram_1_data), .out(multiplexer_13_out), .sel(\单周期硬布线控制器_1_memtoreg ));
  assign and_6_out = multiplexer_13_out & 32'hfffffffe;  // AND_Gate and_6, 32 bits wide
  Multiplexer #(.select(1), .width(32), .disabled("Z"), .enable("false")) multiplexer_14 (
    .in0(adder_3_out), .in1(and_6_out), .out(multiplexer_14_out), .sel(JALR));
  or or_9 (or_9_out, register_7_q, RST);
  Register #(.width(1), .trigger("rising"), .Select("low")) register_2 (
    .D(1'b1), .Q(register_2_q), .clk(IR1_t), .clr(or_10_out));  // open: en
  or or_10 (or_10_out, register_5_q, RST);
  Register #(.width(1), .trigger("rising"), .Select("low")) register_3 (
    .D(1'b1), .Q(register_3_q), .clk(IR2_t), .clr(or_11_out));  // open: en
  or or_11 (or_11_out, register_6_q, RST);
  or or_12 (W3, register_4_q, register_7_q);
  Register #(.width(1), .trigger("rising"), .Select("low")) register_4 (
    .D(1'b1), .Q(register_4_q), .clk(IR3_t), .clr(or_9_out));  // open: en
  or or_13 (or_13_out, register_4_q, register_7_q);
  or or_14 (W1, register_2_q, register_5_q);
  or or_15 (or_15_out, register_2_q, register_5_q);
  or or_16 (W2, register_3_q, register_6_q);
  or or_17 (or_17_out, register_3_q, register_6_q);
  and and_7 (and_7_out, or_13_out, ~clear3);  // AND_Gate
  and and_8 (and_8_out, or_15_out, ~clear1);  // AND_Gate
  and and_9 (and_9_out, or_17_out, ~clear2);  // AND_Gate
  Register #(.width(1), .trigger("rising"), .Select("low")) register_5 (
    .D(and_8_out), .Q(register_5_q), .clk(CLK), .clr(RST));  // open: en
  Register #(.width(1), .trigger("rising"), .Select("low")) register_6 (
    .D(and_9_out), .Q(register_6_q), .clk(CLK), .clr(RST));  // open: en
  Register #(.width(1), .trigger("rising"), .Select("low")) register_7 (
    .D(and_7_out), .Q(register_7_q), .clk(CLK), .clr(RST));  // open: en
  Priority_Encoder #(.select(2), .disabled("Z")) priority_encoder_1 (
    .in1(register_5_q), .in2(register_6_q), .in3(register_7_q), .out(priority_encoder_1_out),
    .gs(priority_encoder_1_gs));  // open: in0, en_out, en_in
  and and_10 (INT, priority_encoder_1_gs, IE);
  and and_11 (and_11_out, priority_encoder_1_gs, ~URET);  // AND_Gate
  Register #(.width(32), .trigger("falling"), .Select("low")) mEPC (
    .D(next_PC), .en(INT), .Q(ret_PC), .clk(CLK), .clr(RST));
  D_Flip_Flop #(.trigger("rising"), .Pre_Clr_Positions("LEGACY"), .NegatePresetClear("false"), .enable("true"), .NewFFLayout("false")) d_ff_1 (
    .clk(CLK), .D(and_11_out), .Qn(IE));  // open: Q, preset, en, reset
  Multiplexer #(.select(2), .width(32), .disabled("Z"), .enable("false")) multiplexer_15 (
    .in1(32'h30ac), .in2(32'h3150), .in3(32'h31f4), .out(INT_PC), .sel(priority_encoder_1_out));  // open: in0
  Register #(.width(2), .trigger("rising"), .Select("low")) register_8 (
    .D(priority_encoder_1_out), .en(INT), .Q(register_8_q), .clk(CLK), .clr(RST));
  Decoder #(.select(2), .tristate("false"), .disabled("Z"), .enable("false")) decoder_1 (
    .out1(decoder_1_out1), .out2(decoder_1_out2), .out3(decoder_1_out3), .sel(register_8_q));  // open: out0
  and and_12 (clear1, decoder_1_out1, URET);
  and and_13 (clear2, decoder_1_out2, URET);
  and and_14 (clear3, decoder_1_out3, URET);

  // Notes on the sheet:
  //   中断源
  //   中断等待指示
  //   总复位信号应将除ROM以外所有存储组件全部清零
  //   单级中断测试信号模拟器
  //   数码管输出
  //   数码管输出应该用寄存器锁存，否则显示数据只能一闪而过
  //   指令探针
  //   指令存储器
  //   指令字
  //   contents of rom_1 (hex, n*v repeats v):
  //   7d000113 100413 1f41993 41f9d993 433 c00913 800b13 140413 f47413 800293 100313 499993 89e9b3 1300533
  //   2200893 73 406282b3 fe0294e3 140413 f00f93 1f47433 1c41413 800293 100313 49d993 89e9b3 1300533
  //   2200893 73 406282b3 fe0294e3 1c45413 406b0b33 b0463 f95ff06f 2b3 fff2c293 1029293 fff2e293 500533
  //   2200893 73 f5dff06f 1112023 410113 a12023 410113 812023 410113 1312023 410113 1412023 410113 1512023
  //   410113 1612023 410113 100b13 300a13 100a93 1600433 441413 14469b3 1300533 2200893 73 fe0416e3
  //   415a0a33 fe0a10e3 ffc10113 12b03 ffc10113 12a83 ffc10113 12a03 ffc10113 12983 ffc10113 12403
  //   ffc10113 12503 ffc10113 12883 200073 1112023 410113 a12023 410113 812023 410113 1312023 410113
  //   1412023 410113 1512023 410113 1612023 410113 200b13 300a13 100a93 1600433 441413 14469b3 1300533
  //   2200893 73 fe0416e3 415a0a33 fe0a10e3 ffc10113 12b03 ffc10113 12a83 ffc10113 12a03 ffc10113 12983
  //   ffc10113 12403 ffc10113 12503 ffc10113 12883 200073 1112023 410113 a12023 410113 812023 410113
  //   1312023 410113 1412023 410113 1512023 410113 1612023 410113 300b13 300a13 100a93 1600433 441413
  //   14469b3 1300533 2200893 73 fe0416e3 415a0a33 fe0a10e3 ffc10113 12b03 ffc10113 12a83 ffc10113 12a03
  //   ffc10113 12983 ffc10113 12403 ffc10113 12503 ffc10113 12883 200073
  //   Beq,Bne,Bltu
  //   JAL
  //   AUIPC
  //   为方便自动评测，需要输出PC，IR，寄存器堆写如数据RDin
  //   JAL
  //   JALR
  //   RAM写使能MemWrite、RAM写入数据MDin等信号
  //   Beq
  //   Bne
  //   MemToReg
  //   MemWrite
  //   AluOP
  //   AluSrcB
  //   RegWrite
  //   数据存储器
endmodule

module \单周期_多级中断  (
  input  IR1,
  input  IR2,
  input  IR3,
  output RegWrite,
  output MemWrite,
  output [31:0] PC,
  output [31:0] IR,
  output [31:0] RDin,
  output [31:0] MDin,
  output [31:0] LedData
);

  wire alu_1_equal, alu_1_out_6, and_1_out, and_3_out, and_4_out, and_5_out, and_7_out, and_8_out, and_9_out,
       and_10_out, AUIPC, clear1, clear2, clear3, CLK, comparator_1_eq, comparator_2_eq, comparator_3_eq,
       comparator_4_eq, comparator_5_eq, comparator_6_eq, comparator_7_eq, CSRRCI, CSRRSI, decoder_1_out1,
       decoder_1_out2, decoder_1_out3, decoder_2_out0, decoder_2_out1, decoder_2_out2, decoder_3_out1,
       decoder_3_out2, decoder_3_out3, ecall, Go, halt, IE, INT, IR1_t, IR2_t, IR3_t, IRA, IRB, IRC, is_run,
       isBranch, JAL, JALR, LHU, multiplexer_15_out, multiplexer_20_out, new_INT, not_1_out, not_2_out,
       not_3_out, or_1_out, or_2_out, or_3_out, or_6_out, or_9_out, or_10_out, or_11_out, or_12_out,
       or_14_out, or_16_out, or_18_out, or_19_out, or_20_out, or_21_out, or_22_out, or_23_out, or_24_out,
       or_25_out, or_26_out, register_2_q, register_3_q, register_4_q, register_5_q, register_6_q,
       register_7_q, register_9_q, register_10_q, register_11_q, RST, status1_q, status2_q, status3_q, URET,
       W1, W2, W3, \单周期硬布线控制器_1_alu_src , \单周期硬布线控制器_1_beq , \单周期硬布线控制器_1_bltu , \单周期硬布线控制器_1_bne ,
       \单周期硬布线控制器_1_memtoreg , \单周期硬布线控制器_1_s_type ;
  wire [1:0] counter_2_q, INT_code, multiplexer_18_out, old_INT_code_q;
  wire [3:0] \单周期硬布线控制器_1_alu_op ;
  wire [4:0] multiplexer_4_out, multiplexer_5_out;
  wire [11:0] multiplexer_6_out, shifter_2_out;
  wire [15:0] multiplexer_10_out, \总周期数 ;
  wire [19:0] shifter_3_out;
  wire [31:0] adder_2_out, adder_3_out, alu_1_result, and_6_out, bit_extender_1_out, bit_extender_2_out,
       bit_extender_3_out, bit_extender_4_out, bit_extender_5_out, EPC0_q, EPC1_q, EPC2_q, INT_PC,
       multiplexer_2_out, multiplexer_3_out, multiplexer_8_out, multiplexer_9_out, multiplexer_11_out,
       multiplexer_12_out, multiplexer_13_out, multiplexer_14_out, next_PC, PC_4, R1, ram_1_data, ret_PC,
       shifter_1_out;

  Clock #(.highDuration(1), .lowDuration(1)) clock_1 (.out(CLK));
  Button _1 ();  // open: out
  Button _2 ();  // open: out
  Button _3 ();  // open: out
  Button \u_继续运行  (.out(Go));
  LED #(.active("true")) led_1 (.in(W1));
  LED #(.active("true")) led_2 (.in(W2));
  LED #(.active("true")) led_3 (.in(W3));
  Hex_Digit_Display hex_digit_display_1 (.value(LedData[31:28]));  // open: dp
  Comparator #(.width(16), .mode("twosComplement")) comparator_1 (
    .a(\总周期数 ), .b(16'h7), .eq(comparator_1_eq));  // open: gt, lt
  Comparator #(.width(16), .mode("twosComplement")) comparator_2 (
    .a(\总周期数 ), .b(16'h241), .eq(comparator_2_eq));  // open: gt, lt
  Button button_1 (.out(RST));
  Hex_Digit_Display hex_digit_display_2 (.value(LedData[27:24]));  // open: dp
  Hex_Digit_Display hex_digit_display_3 (.value(LedData[23:20]));  // open: dp
  Comparator #(.width(16), .mode("twosComplement")) comparator_3 (
    .a(16'h258), .b(\总周期数 ), .eq(comparator_3_eq));  // open: gt, lt
  or or_1 (or_1_out, comparator_3_eq, comparator_4_eq);
  Comparator #(.width(16), .mode("twosComplement")) comparator_4 (
    .a(\总周期数 ), .b(16'h1), .eq(comparator_4_eq));  // open: gt, lt
  Comparator #(.width(16), .mode("twosComplement")) comparator_5 (
    .a(\总周期数 ), .b(16'h4), .eq(comparator_5_eq));  // open: gt, lt
  or or_2 (or_2_out, comparator_1_eq, comparator_2_eq);
  Hex_Digit_Display hex_digit_display_4 (.value(LedData[15:12]));  // open: dp
  Hex_Digit_Display hex_digit_display_5 (.value(LedData[19:16]));  // open: dp
  Pull_Resistor #(.pull(0)) pull_resistor_1 (.node(IRA));
  assign IRA = or_1_out ? ~CLK : 1'bz;  // Controlled_Inverter controlled_inverter_1
  Pull_Resistor #(.pull(0)) pull_resistor_2 (.node(IRB));
  assign IRB = comparator_5_eq ? ~CLK : 1'bz;  // Controlled_Inverter controlled_inverter_2
  Pull_Resistor #(.pull(0)) pull_resistor_3 (.node(IRC));
  assign IRC = or_2_out ? ~CLK : 1'bz;  // Controlled_Inverter controlled_inverter_3
  Hex_Digit_Display hex_digit_display_6 (.value(LedData[11:8]));  // open: dp
  Hex_Digit_Display hex_digit_display_7 (.value(LedData[7:4]));  // open: dp
  // Probe on \总周期数 
  Hex_Digit_Display hex_digit_display_8 (.value(LedData[3:0]));  // open: dp
  not not_1 (not_1_out, halt);
  Multiplexer #(.select(1), .width(32), .disabled("Z"), .enable("false")) multiplexer_1 (
    .in0(PC_4), .in1(multiplexer_14_out), .out(next_PC), .sel(or_3_out));
  or or_3 (or_3_out, JALR, JAL, isBranch);
  Counter #(.width(16), .max('hffff), .ongoal("wrap"), .trigger("rising"), .behavior("new")) counter_1 (
    .count(not_1_out), .Q(\总周期数 ), .clk(CLK));  // open: load, D, carry, clr, preset, down
  or or_4 (IR1_t, IR1, IRA);
  Multiplexer #(.select(1), .width(32), .disabled("Z"), .enable("false")) multiplexer_2 (
    .in0(next_PC), .in1(ret_PC), .out(multiplexer_2_out), .sel(URET));
  Comparator #(.width(32), .mode("twosComplement")) comparator_6 (
    .a(R1), .b(32'h22), .eq(comparator_6_eq));  // open: gt, lt
  or or_5 (IR2_t, IR2, IRB);
  Multiplexer #(.select(1), .width(32), .disabled("Z"), .enable("false")) multiplexer_3 (
    .in0(multiplexer_2_out), .in1(INT_PC), .out(multiplexer_3_out), .sel(INT));
  or or_6 (or_6_out, Go, not_2_out);
  not not_2 (not_2_out, halt);
  and and_1 (and_1_out, ecall, comparator_6_eq);
  Register #(.width(32), .trigger("rising"), .Select("low")) u_PC (
    .D(multiplexer_3_out), .en(or_6_out), .Q(PC), .clk(CLK), .clr(RST));
  and and_2 (halt, ecall, ~comparator_6_eq);  // AND_Gate
  or or_7 (IR3_t, IR3, IRC);
  Adder #(.width(32)) adder_1 (.a(PC), .b(32'h4), .out(PC_4));  // open: cin, cout
  Register #(.width(32), .trigger("rising"), .Select("low")) register_1 (
    .D(MDin), .en(and_1_out), .Q(LedData), .clk(CLK));  // open: clr
  // Probe on PC[11:2]
  // RiscV_Probe riscv_probe_1: pin names not known; wires that end beside it: IR
  ROM #(.addrWidth(10), .dataWidth(32), .Select("high")) rom_1 (.addr(PC[11:2]), .data(IR));
  Multiplexer #(.select(1), .width(5), .disabled("Z"), .enable("false")) multiplexer_4 (
    .in0(IR[19:15]), .in1(5'b10001), .out(multiplexer_4_out), .sel(ecall));
  assign bit_extender_1_out = {{12{IR[31]}}, IR[31:12]};  // Bit_Extender bit_extender_1
  \单周期硬布线控制器  \u_单周期硬布线控制器_1  (
    .Funct({IR[30], IR[25], IR[14:12]}), .OP(IR[6:2]), .ALU_OP(\单周期硬布线控制器_1_alu_op ),
    .MemToReg(\单周期硬布线控制器_1_memtoreg ), .MemWrite(MemWrite), .ALU_SRC(\单周期硬布线控制器_1_alu_src ),
    .RegWrite(RegWrite), .ecall(ecall), .S_type(\单周期硬布线控制器_1_s_type ), .Jalr(JALR), .Beq(\单周期硬布线控制器_1_beq ),
    .JAL(JAL), .Bne(\单周期硬布线控制器_1_bne ), .in_3(IR[21]), .uret(URET), .AUIPC(AUIPC), .LHU(LHU),
    .BLTU(\单周期硬布线控制器_1_bltu ), .CSRRSI(CSRRSI), .CSRRCI(CSRRCI));  // open: rs1_used, rs2_used
  Multiplexer #(.select(1), .width(5), .disabled("Z"), .enable("false")) multiplexer_5 (
    .in0(IR[24:20]), .in1(5'b01010), .out(multiplexer_5_out), .sel(ecall));
  Multiplexer #(.select(1), .width(12), .disabled("Z"), .enable("false")) multiplexer_6 (
    .in0(IR[31:20]), .in1({IR[31:25], IR[11:7]}), .out(multiplexer_6_out), .sel(\单周期硬布线控制器_1_s_type ));
  Shifter #(.width(32), .shift("ll")) shifter_1 (.in(bit_extender_1_out), .\dist (5'b01100), .out(shifter_1_out));
  Multiplexer #(.select(1), .width(32), .disabled("Z"), .enable("false")) multiplexer_7 (
    .in0(multiplexer_11_out), .in1(bit_extender_5_out), .out(RDin), .sel(LHU));
  Shifter #(.width(12), .shift("ll")) shifter_2 (
    .in({IR[31], IR[7], IR[30:25], IR[11:8]}), .\dist (4'b0001), .out(shifter_2_out));
  Shifter #(.width(20), .shift("ll")) shifter_3 (
    .in({IR[31], IR[19:12], IR[20], IR[30:21]}), .\dist (5'b00001), .out(shifter_3_out));
  Regifile regifile_1 (
    .Din(RDin), .Clk(CLK), .R1(R1), .R2(MDin), .WE(RegWrite), .W_num(IR[11:7]), .R1_num(multiplexer_4_out),
    .R2_num(multiplexer_5_out));
  assign bit_extender_2_out = {{20{multiplexer_6_out[11]}}, multiplexer_6_out};  // Bit_Extender bit_extender_2
  assign bit_extender_3_out = {{20{shifter_2_out[11]}}, shifter_2_out};  // Bit_Extender bit_extender_3
  assign bit_extender_4_out = {{12{shifter_3_out[19]}}, shifter_3_out};  // Bit_Extender bit_extender_4
  Adder #(.width(32)) adder_2 (.a(PC), .b(shifter_1_out), .out(adder_2_out));  // open: cin, cout
  Multiplexer #(.select(1), .width(32), .disabled("Z"), .enable("false")) multiplexer_8 (
    .in0(MDin), .in1(bit_extender_2_out), .out(multiplexer_8_out), .sel(\单周期硬布线控制器_1_alu_src ));
  assign bit_extender_5_out = {{16{1'b0}}, multiplexer_10_out};  // Bit_Extender bit_extender_5
  Multiplexer #(.select(1), .width(32), .disabled("Z"), .enable("false")) multiplexer_9 (
    .in0(bit_extender_3_out), .in1(bit_extender_4_out), .out(multiplexer_9_out), .sel(JAL));
  ALU alu_1 (
    .X(R1), .Y(multiplexer_8_out), .AluOP(\单周期硬布线控制器_1_alu_op ), .Equal(alu_1_equal), .Result(alu_1_result),
    .out_6(alu_1_out_6));  // open: Result_2, out_4
  Multiplexer #(.select(1), .width(16), .disabled("Z"), .enable("false")) multiplexer_10 (
    .in0(multiplexer_11_out[15:0]), .in1(multiplexer_11_out[31:16]), .out(multiplexer_10_out),
    .sel(alu_1_result[1]));
  and and_3 (and_3_out, \单周期硬布线控制器_1_bltu , alu_1_out_6);
  and and_4 (and_4_out, alu_1_equal, \单周期硬布线控制器_1_beq );
  and and_5 (and_5_out, ~alu_1_equal, \单周期硬布线控制器_1_bne );  // AND_Gate
  Multiplexer #(.select(1), .width(32), .disabled("Z"), .enable("false")) multiplexer_11 (
    .in0(multiplexer_12_out), .in1(adder_2_out), .out(multiplexer_11_out), .sel(AUIPC));
  Adder #(.width(32)) adder_3 (.a(PC), .b(multiplexer_9_out), .out(adder_3_out));  // open: cin, cout
  Multiplexer #(.select(1), .width(32), .disabled("Z"), .enable("false")) multiplexer_12 (
    .in0(multiplexer_13_out), .in1(PC_4), .out(multiplexer_12_out), .sel(or_9_out));
  or or_8 (isBranch, and_3_out, and_4_out, and_5_out);
  RAM #(.addrWidth(10), .dataWidth(32), .bus("separate"), .Select("high")) ram_1 (
    .addr(alu_1_result[11:2]), .din(MDin), .data(ram_1_data), .str(MemWrite), .sel(1'b1), .clk(CLK),
    .ld(1'b1), .clr(RST));
  or or_9 (or_9_out, JALR, JAL);
  Multiplexer #(.select(1), .width(32), .disabled("Z"), .enable("false")) multiplexer_13 (
    .in0(alu_1_result), .in1(ram_1_data), .out(multiplexer_13_out), .sel(\单周期硬布线控制器_1_memtoreg ));
  Multiplexer #(.select(1), .width(32), .disabled("Z"), .enable("false")) multiplexer_14 (
    .in0(adder_3_out), .in1(and_6_out), .out(multiplexer_14_out), .sel(JALR));
  assign and_6_out = multiplexer_13_out & 32'hfffffffe;  // AND_Gate and_6, 32 bits wide
  Register #(.width(1), .trigger("rising"), .Select("low")) register_2 (
    .D(1'b1), .Q(register_2_q), .clk(IR1_t), .clr(or_10_out));  // open: en
  or or_10 (or_10_out, register_5_q, RST);
  Register #(.width(1), .trigger("rising"), .Select("low")) register_3 (
    .D(1'b1), .Q(register_3_q), .clk(IR2_t), .clr(or_11_out));  // open: en
  or or_11 (or_11_out, register_6_q, RST);
  Register #(.width(1), .trigger("rising"), .Select("low")) register_4 (
    .D(1'b1), .Q(register_4_q), .clk(IR3_t), .clr(or_12_out));  // open: en
  or or_12 (or_12_out, register_7_q, RST);
  Decoder #(.select(2), .tristate("false"), .disabled("Z"), .enable("false")) decoder_1 (
    .out1(decoder_1_out1), .out2(decoder_1_out2), .out3(decoder_1_out3), .sel(INT_code));  // open: out0
  or or_13 (W1, register_2_q, register_5_q);
  or or_14 (or_14_out, register_2_q, register_5_q);
  or or_15 (W2, register_3_q, register_6_q);
  or or_16 (or_16_out, register_3_q, register_6_q);
  or or_17 (W3, register_4_q, register_7_q);
  or or_18 (or_18_out, register_4_q, register_7_q);
  or or_19 (or_19_out, INT, URET);
  and and_7 (and_7_out, or_14_out, ~clear1);  // AND_Gate
  and and_8 (and_8_out, or_16_out, ~clear2);  // AND_Gate
  and and_9 (and_9_out, or_18_out, ~clear3);  // AND_Gate
  Decoder #(.select(2), .tristate("false"), .disabled("Z"), .enable("false")) decoder_2 (
    .out0(decoder_2_out0), .out1(decoder_2_out1), .out2(decoder_2_out2), .sel(counter_2_q));  // open: out3
  Counter #(.width(2), .max('h3), .ongoal("wrap"), .trigger("rising"), .behavior("new")) counter_2 (
    .count(or_19_out), .Q(counter_2_q), .clk(CLK), .clr(RST), .down(URET));  // open: load, D, carry, preset
  Register #(.width(1), .trigger("rising"), .Select("low")) register_5 (
    .D(and_7_out), .Q(register_5_q), .clk(CLK), .clr(RST));  // open: en
  Register #(.width(1), .trigger("rising"), .Select("low")) register_6 (
    .D(and_8_out), .Q(register_6_q), .clk(CLK), .clr(RST));  // open: en
  Register #(.width(1), .trigger("rising"), .Select("low")) register_7 (
    .D(and_9_out), .Q(register_7_q), .clk(CLK), .clr(RST));  // open: en
  Register #(.width(1), .trigger("rising"), .Select("low")) status1 (
    .D(1'b1), .en(decoder_1_out1), .Q(status1_q), .clk(INT), .clr(or_20_out));
  or or_20 (or_20_out, clear1, RST);
  Register #(.width(1), .trigger("rising"), .Select("low")) status2 (
    .D(1'b1), .en(decoder_1_out2), .Q(status2_q), .clk(INT), .clr(or_21_out));
  or or_21 (or_21_out, clear2, RST);
  Register #(.width(1), .trigger("rising"), .Select("low")) status3 (
    .D(1'b1), .en(decoder_1_out3), .Q(status3_q), .clk(INT), .clr(or_22_out));
  or or_22 (or_22_out, clear3, RST);
  Register #(.width(32), .trigger("rising"), .Select("low")) EPC1 (
    .D(next_PC), .en(decoder_2_out1), .Q(EPC1_q), .clk(CLK), .clr(RST));
  Priority_Encoder #(.select(2), .disabled("Z")) priority_encoder_1 (
    .in0(1'b1), .in1(register_5_q), .in2(register_6_q), .in3(register_7_q), .out(INT_code));  // open: gs, en_out, en_in
  Register #(.width(1), .trigger("rising"), .Select("low")) register_8 (
    .D(1'b1), .Q(INT), .clk(new_INT), .clr(or_23_out));  // open: en
  Register #(.width(1), .trigger("rising"), .Select("low")) register_9 (
    .D(1'b1), .Q(register_9_q), .clk(multiplexer_15_out), .clr(or_24_out));  // open: en
  Multiplexer #(.select(1), .width(1), .disabled("Z"), .enable("false")) multiplexer_15 (
    .in0(1'b1), .in1(CLK), .out(multiplexer_15_out), .sel(INT));
  Register #(.width(32), .trigger("rising"), .Select("low")) EPC0 (
    .D(next_PC), .en(decoder_2_out0), .Q(EPC0_q), .clk(CLK), .clr(RST));
  Register #(.width(32), .trigger("rising"), .Select("low")) EPC2 (
    .D(next_PC), .en(decoder_2_out2), .Q(EPC2_q), .clk(CLK), .clr(RST));
  or or_23 (or_23_out, RST, register_9_q);
  or or_24 (or_24_out, register_9_q, RST);
  Multiplexer #(.select(2), .width(1), .disabled("Z"), .enable("false")) multiplexer_16 (
    .in0(1'b1), .in1(status1_q), .in2(status2_q), .in3(status3_q), .out(is_run), .sel(INT_code));
  Multiplexer #(.select(2), .width(32), .disabled("Z"), .enable("false")) multiplexer_17 (
    .in1(32'h30ac), .in2(32'h3158), .in3(32'h3204), .out(INT_PC), .sel(INT_code));  // open: in0
  Multiplexer #(.select(1), .width(2), .disabled("Z"), .enable("false")) multiplexer_18 (
    .in0(multiplexer_18_out), .in1(INT_code), .out(multiplexer_18_out), .sel(IE));
  Multiplexer #(.select(2), .width(32), .disabled("Z"), .enable("false")) multiplexer_19 (
    .in1(EPC0_q), .in2(EPC1_q), .in3(EPC2_q), .out(ret_PC), .sel(counter_2_q));  // open: in0
  Register #(.width(2), .trigger("rising"), .Select("low")) old_INT_code (
    .D(multiplexer_18_out), .Q(old_INT_code_q), .clk(CLK), .clr(RST));  // open: en
  Register #(.width(1), .trigger("falling"), .Select("low")) register_10 (
    .D(1'b0), .Q(register_10_q), .clk(CLK), .clr(RST), .preset(URET));  // open: en, cs
  Comparator #(.width(2), .mode("unsigned")) comparator_7 (
    .a(old_INT_code_q), .b(multiplexer_18_out), .eq(comparator_7_eq));  // open: gt, lt
  Register #(.width(1), .trigger("falling"), .Select("low")) register_11 (
    .D(register_10_q), .Q(register_11_q), .clk(CLK), .clr(RST));  // open: en
  and and_10 (and_10_out, ~CSRRSI, ~URET);  // AND_Gate
  Decoder #(.select(2), .tristate("false"), .disabled("Z"), .enable("false")) decoder_3 (
    .out1(decoder_3_out1), .out2(decoder_3_out2), .out3(decoder_3_out3), .sel(old_INT_code_q));  // open: out0
  not not_3 (not_3_out, comparator_7_eq);
  or or_25 (or_25_out, register_10_q, register_11_q);
  D_Flip_Flop #(.trigger("rising"), .Pre_Clr_Positions("LEGACY"), .NegatePresetClear("false"), .enable("true"), .NewFFLayout("false")) d_ff_1 (
    .clk(and_10_out), .D(1'b0), .Qn(IE), .preset(or_26_out), .reset(RST));  // open: Q, en
  or or_26 (or_26_out, CSRRCI, INT);
  Multiplexer #(.select(1), .width(1), .disabled("Z"), .enable("false")) multiplexer_20 (
    .in0(not_3_out), .in1(multiplexer_20_out), .out(multiplexer_20_out), .sel(or_25_out));
  and and_11 (clear1, decoder_3_out1, URET);
  and and_12 (clear2, decoder_3_out2, URET);
  and and_13 (clear3, decoder_3_out3, URET);
  Multiplexer #(.select(1), .width(1), .disabled("Z"), .enable("false")) multiplexer_21 (
    .in0(not_3_out), .in1(multiplexer_20_out), .out(new_INT), .sel(is_run));

  // Notes on the sheet:
  //   中断源
  //   中断等待指示
  //   总复位信号应将除ROM以外所有存储组件全部清零
  //   多级中断测试信号模拟器
  //   数码管输出
  //   数码管输出应该用寄存器锁存，否则显示数据只能一闪而过
  //   指令探针
  //   指令存储器
  //   Beq,Bne,Bltu
  //   为方便自动评测，需要输出PC，IR，寄存器堆写如数据RDin
  //   指令字
  //   contents of rom_1 (hex, n*v repeats v):
  //   7d000113 100413 1f41993 41f9d993 433 c00913 800b13 140413 f47413 800293 100313 499993 89e9b3 1300533
  //   2200893 73 406282b3 fe0294e3 140413 f00f93 1f47433 1c41413 800293 100313 49d993 89e9b3 1300533
  //   2200893 73 406282b3 fe0294e3 1c45413 406b0b33 b0463 f95ff06f 2b3 fff2c293 1029293 fff2e293 500533
  //   2200893 73 f5dff06f 1112023 410113 a12023 410113 812023 410113 1312023 410113 1412023 410113 1512023
  //   410113 1612023 410113 40e073 100b13 300a13 100a93 1600433 441413 14469b3 1300533 2200893 73 fe0416e3
  //   415a0a33 fe0a10e3 40f073 ffc10113 12b03 ffc10113 12a83 ffc10113 12a03 ffc10113 12983 ffc10113 12403
  //   ffc10113 12503 ffc10113 12883 200073 1112023 410113 a12023 410113 812023 410113 1312023 410113
  //   1412023 410113 1512023 410113 1612023 410113 40e073 200b13 300a13 100a93 1600433 441413 14469b3
  //   1300533 2200893 73 fe0416e3 415a0a33 fe0a10e3 40f073 ffc10113 12b03 ffc10113 12a83 ffc10113 12a03
  //   ffc10113 12983 ffc10113 12403 ffc10113 12503 ffc10113 12883 200073 1112023 410113 a12023 410113
  //   812023 410113 1312023 410113 1412023 410113 1512023 410113 1612023 410113 40e073 300b13 300a13
  //   100a93 1600433 441413 14469b3 1300533 2200893 73 fe0416e3 415a0a33 fe0a10e3 40f073 ffc10113 12b03
  //   ffc10113 12a83 ffc10113 12a03 ffc10113 12983 ffc10113 12403 ffc10113 12503 ffc10113 12883 200073
  //   JAL
  //   AUIPC
  //   RAM写使能MemWrite、RAM写入数据MDin等信号
  //   JAL
  //   JALR
  //   Beq
  //   Bne
  //   MemToReg
  //   MemWrite
  //   AluOP
  //   AluSrcB
  //   RegWrite
  //   数据存储器
endmodule

module \封装正确性测试  (
);

  wire IR1, IR2, IR3, MemW, RegW;
  wire [31:0] EX_PC, ID_PC, IF_PC, IR, LED, MDin, MDinr, MEM_PC, PC, RDin, RDinr, WB_PC;

  \单周期RISC_V  \u_单周期risc_v_1  (
    .IR1(IR1), .IR2(IR2), .IR3(IR3), .RegWrite(RegW), .MemWrite(MemW), .PC(PC), .IR(IR), .RDin(RDin),
    .MDin(MDin), .LedData(LED));
  \气泡流水线  \u_气泡流水线_1  (
    .RegWrite(RegW), .MemWrite(MemW), .IF_PC(IF_PC), .ID_PC(ID_PC), .EX_PC(EX_PC), .M_PC(MEM_PC),
    .WB_PC(WB_PC), .RDin(RDinr), .MDin(MDinr), .LedData(LED));
  \单周期_单级中断  \u_单周期_单级中断_1  (
    .IR1(IR1), .IR2(IR2), .IR3(IR3), .RegWrite(RegW), .MemWrite(MemW), .PC(PC), .IR(IR), .RDin(RDin),
    .MDin(MDin), .LedData(LED));
  \理想流水线  \u_理想流水线_1  (
    .RegWrite(RegW), .MemWrite(MemW), .IF_PC(IF_PC), .ID_PC(ID_PC), .EX_PC(EX_PC), .M_PC(MEM_PC),
    .WB_PC(WB_PC), .RDin(RDinr), .MDin(MDinr), .LedData(LED));
  \重定向流水线  \u_重定向流水线_1  (
    .RegWrite(RegW), .MemWrite(MemW), .IF_PC(IF_PC), .ID_PC(ID_PC), .EX_PC(EX_PC), .M_PC(MEM_PC),
    .WB_PC(WB_PC), .RDin(RDinr), .MDin(MDinr), .LedData(LED));
  \单周期_多级中断  \u_单周期_多级中断_1  (
    .IR1(IR1), .IR2(IR2), .IR3(IR3), .RegWrite(RegW), .MemWrite(MemW), .PC(PC), .IR(IR), .RDin(RDin),
    .MDin(MDin), .LedData(LED));

  // Notes on the sheet:
  //   单周期封装测试
  //   气泡流水封装测试
  //   单周期+单级中断封装测试
  //   请检查上面封装有无位宽不匹配，引脚标签是否和连接的标签相对应，否则无法在educoder平台上正确测试
  //   理想流水封装测试
  //   重定向流水封装测试
  //   单周期+多级中断封装测试
endmodule

module \重定向流水线中断  (
  input  IR1,
  input  IR2,
  input  IR3,
  output RegWrite,
  output MemWrite,
  output [31:0] PC,
  output [31:0] IR,
  output [31:0] RDin,
  output [31:0] MDin,
  output [31:0] LedData
);

  wire alu_1_equal, alu_1_out_6, and_1_out, and_2_out, and_4_out, and_5_out, and_6_out, and_8_out,
       and_10_out, and_11_out, and_12_out, and_13_out, AUIPC, BranchTaken, BTBefore1, BTBefore2, clear1,
       clear2, clear3, CLK, comparator_1_eq, comparator_2_eq, comparator_3_eq, comparator_4_eq,
       comparator_5_eq, comparator_6_eq, comparator_7_eq, decoder_1_out1, decoder_1_out2, decoder_1_out3,
       EX_ecall, EX_halt, EX_JAL, EX_JALR, ex_mem_1_auipc_2, ex_mem_1_halt_2, ex_mem_1_jal_2,
       ex_mem_1_jalr_2, ex_mem_1_lhu_2, ex_mem_1_memtoreg_2, EX_MemToReg, EX_RegWrite, EX_uret, Go, halt,
       id_ex_1_alusrcb_2, id_ex_1_auipc_2, id_ex_1_beq_2, id_ex_1_bltu_2, id_ex_1_bne_2, id_ex_1_lhu_2,
       id_ex_1_memwrite_2, IE, IF_uret, INT, IR1_t, IR2_t, IR3_t, IRA, IRB, IRC, isBranch, JAL, JALR, LHU,
       loadUseBefore1, MEM_RegWrite, mem_wb_1_auipc_2, mem_wb_1_jal_2, mem_wb_1_jalr_2, mem_wb_1_lhu_2,
       mem_wb_1_memtoreg_2, not_1_out, not_2_out, not_3_out, not_4_out, or_1_out, or_2_out, or_5_out,
       or_8_out, or_9_out, or_10_out, or_11_out, or_12_out, or_14_out, or_15_out, or_16_out, or_17_out,
       or_18_out, or_19_out, or_21_out, or_23_out, or_25_out, priority_encoder_1_gs, register_2_q,
       register_3_q, register_4_q, register_5_q, register_6_q, register_7_q, RST, stall, W1, W2, W3,
       \单周期硬布线控制器_1_alu_src , \单周期硬布线控制器_1_beq , \单周期硬布线控制器_1_bltu , \单周期硬布线控制器_1_bne , \单周期硬布线控制器_1_ecall ,
       \单周期硬布线控制器_1_memtoreg , \单周期硬布线控制器_1_memwrite , \单周期硬布线控制器_1_regwrite , \单周期硬布线控制器_1_rs1_used ,
       \单周期硬布线控制器_1_rs2_used , \单周期硬布线控制器_1_s_type , \单周期硬布线控制器_1_uret ;
  wire [1:0] id_ex_1_rs1_redirect_2, id_ex_1_rs2_redirect_2, priority_encoder_1_out, redirect_1_rs1_redirect,
       redirect_1_rs2_redirect, register_11_q;
  wire [3:0] id_ex_1_aluop_2, \单周期硬布线控制器_1_alu_op ;
  wire [4:0] EX_rd, MEM_rd, rs1, rs2, WB_rd;
  wire [11:0] multiplexer_6_out;
  wire [15:0] multiplexer_15_out, multiplexer_17_out, multiplexer_17_out_2, \总周期数 , \无条件分支数 ;
  wire [31:0] adder_2_out, adder_3_out, alu_1_result, and_7_out, bit_extender_1_out, bit_extender_2_out,
       bit_extender_3_out, bit_extender_4_out, bit_extender_5_out, branch, EX_IR, ex_mem_1_aluresult_2,
       ex_mem_1_auipc_addr_2, ex_mem_1_pc_4_2, EX_PC, EX_PC_4, id_ex_1_imm1_2, id_ex_1_imm2_2,
       id_ex_1_imm_20_2, id_ex_1_r1_2, id_ex_1_r2_2, ID_IR, ID_PC, if_id_1_pc_4_out, IF_IR, IF_PC, INT_PC,
       MEM_AluRes, MEM_IR, MEM_PC, mem_wb_1_aluresult_2, mem_wb_1_auipc_addr_2, mem_wb_1_pc_4_2,
       mem_wb_1_readdata_2, multiplexer_1_out, multiplexer_2_out, multiplexer_3_out, multiplexer_7_out,
       multiplexer_9_out, multiplexer_14_out, multiplexer_16_out, PC_4, R1, R2, ram_1_data, regifile_1_r1,
       regifile_1_r2, ret_PC, save_PC, shifter_1_out, shifter_2_out, WB_IR, WB_PC;

  Clock #(.highDuration(1), .lowDuration(1)) clock_1 (.out(CLK));
  Button _1 ();  // open: out
  Button _2 ();  // open: out
  Button _3 ();  // open: out
  Button \u_继续运行  (.out(Go));
  LED #(.active("true")) led_1 (.in(W1));
  LED #(.active("true")) led_2 (.in(W2));
  LED #(.active("true")) led_3 (.in(W3));
  Hex_Digit_Display hex_digit_display_1 (.value(LedData[31:28]));  // open: dp
  // Probe on \总周期数 
  // Probe on \总周期数 
  Hex_Digit_Display hex_digit_display_2 (.value(LedData[23:20]));  // open: dp
  Hex_Digit_Display hex_digit_display_3 (.value(LedData[27:24]));  // open: dp
  Comparator #(.width(16), .mode("twosComplement")) comparator_1 (
    .a(16'h23b), .b(\总周期数 ), .eq(comparator_1_eq));  // open: gt, lt
  or or_1 (or_1_out, comparator_1_eq, comparator_2_eq);
  Comparator #(.width(16), .mode("twosComplement")) comparator_2 (
    .a(\总周期数 ), .b(16'h1), .eq(comparator_2_eq));  // open: gt, lt
  Comparator #(.width(16), .mode("twosComplement")) comparator_3 (
    .a(\总周期数 ), .b(16'h4), .eq(comparator_3_eq));  // open: gt, lt
  Comparator #(.width(16), .mode("twosComplement")) comparator_4 (
    .a(\总周期数 ), .b(16'h7), .eq(comparator_4_eq));  // open: gt, lt
  Hex_Digit_Display hex_digit_display_4 (.value(LedData[19:16]));  // open: dp
  Hex_Digit_Display hex_digit_display_5 (.value(LedData[15:12]));  // open: dp
  Pull_Resistor #(.pull(0)) pull_resistor_1 (.node(IRA));
  assign IRA = or_1_out ? ~CLK : 1'bz;  // Controlled_Inverter controlled_inverter_1
  Pull_Resistor #(.pull(0)) pull_resistor_2 (.node(IRB));
  assign IRB = comparator_3_eq ? ~CLK : 1'bz;  // Controlled_Inverter controlled_inverter_2
  Pull_Resistor #(.pull(0)) pull_resistor_3 (.node(IRC));
  assign IRC = comparator_4_eq ? ~CLK : 1'bz;  // Controlled_Inverter controlled_inverter_3
  // Probe on IF_PC[19:0]
  // RiscV_Probe riscv_probe_1: pin names not known; wires that end beside it: IF_IR
  Hex_Digit_Display hex_digit_display_6 (.value(LedData[7:4]));  // open: dp
  Hex_Digit_Display hex_digit_display_7 (.value(LedData[11:8]));  // open: dp
  // Probe on \总周期数 
  // Probe on ID_PC[19:0]
  // RiscV_Probe riscv_probe_2: pin names not known; wires that end beside it: ID_IR
  Hex_Digit_Display hex_digit_display_8 (.value(LedData[3:0]));  // open: dp
  Multiplexer #(.select(1), .width(32), .disabled("Z"), .enable("false")) multiplexer_1 (
    .in0(PC_4), .in1(branch), .out(multiplexer_1_out), .sel(or_2_out));
  or or_2 (or_2_out, EX_JALR, EX_JAL, isBranch);
  // Probe on EX_PC[19:0]
  // RiscV_Probe riscv_probe_3: pin names not known; wires that end beside it: EX_IR
  or or_3 (IR1_t, IR1, IRA);
  Button button_1 (.out(RST));
  Multiplexer #(.select(1), .width(32), .disabled("Z"), .enable("false")) multiplexer_2 (
    .in0(multiplexer_1_out), .in1(INT_PC), .out(multiplexer_2_out), .sel(INT));
  or or_4 (IR2_t, IR2, IRB);
  // Probe on MEM_PC[19:0]
  // RiscV_Probe riscv_probe_4: pin names not known; wires that end beside it: MEM_IR
  Multiplexer #(.select(1), .width(32), .disabled("Z"), .enable("false")) multiplexer_3 (
    .in0(multiplexer_2_out), .in1(ret_PC), .out(multiplexer_3_out), .sel(EX_uret));
  or or_5 (or_5_out, and_1_out, Go);
  and and_1 (and_1_out, not_1_out, not_2_out);
  not not_1 (not_1_out, stall);
  not not_2 (not_2_out, halt);
  or or_6 (IR3_t, IR3, IRC);
  // Probe on WB_PC[19:0]
  // RiscV_Probe riscv_probe_5: pin names not known; wires that end beside it: WB_IR
  Register #(.width(32), .trigger("rising"), .Select("low")) u_PC (
    .D(multiplexer_3_out), .en(or_5_out), .Q(IF_PC), .clk(CLK), .clr(RST));
  not not_3 (not_3_out, halt);
  Adder #(.width(32)) adder_1 (.a(IF_PC), .b(32'h4), .out(PC_4));  // open: cin, cout
  Counter #(.width(16), .max('hffff), .ongoal("wrap"), .trigger("rising"), .behavior("new")) counter_1 (
    .count(not_3_out), .Q(\总周期数 ), .clk(CLK));  // open: load, D, carry, clr, preset, down
  // RiscV_Probe riscv_probe_6: pin names not known; wires that end beside it: IF_IR
  Comparator #(.width(5), .mode("unsigned")) comparator_5 (
    .a(IF_IR[6:2]), .b(5'b11100), .eq(comparator_5_eq));  // open: gt, lt
  Comparator #(.width(5), .mode("unsigned")) comparator_6 (
    .a({5{1'b0}}), .b({IF_IR[30], IF_IR[25], IF_IR[14:12]}), .eq(comparator_6_eq));  // open: gt, lt
  or or_7 (BranchTaken, EX_JALR, EX_JAL, isBranch);
  ROM #(.addrWidth(10), .dataWidth(32), .Select("high")) rom_1 (.addr(IF_PC[11:2]), .data(IF_IR));
  or or_8 (or_8_out, ~halt, Go);  // OR_Gate
  and and_2 (and_2_out, ~stall, or_8_out);  // AND_Gate
  and and_3 (IF_uret, comparator_5_eq, IF_IR[21], comparator_6_eq);
  or or_9 (or_9_out, BranchTaken, INT);
  IF_ID if_id_1 (
    .IR_in(IF_IR), .PC_in(IF_PC), .PC_4_in(PC_4), .IR_out(ID_IR), .PC_out(ID_PC),
    .PC_4_out(if_id_1_pc_4_out), .RST(RST), .branchTaken(or_9_out), .en(and_2_out), .clk(CLK));  // open: predictJump, predictJump_2, isBubble, isBubble_2
  \单周期硬布线控制器  \u_单周期硬布线控制器_1  (
    .Funct({ID_IR[30], ID_IR[25], ID_IR[14:12]}), .OP(ID_IR[6:2]), .ALU_OP(\单周期硬布线控制器_1_alu_op ),
    .MemToReg(\单周期硬布线控制器_1_memtoreg ), .MemWrite(\单周期硬布线控制器_1_memwrite ), .ALU_SRC(\单周期硬布线控制器_1_alu_src ),
    .RegWrite(\单周期硬布线控制器_1_regwrite ), .ecall(\单周期硬布线控制器_1_ecall ), .S_type(\单周期硬布线控制器_1_s_type ),
    .Jalr(JALR), .Beq(\单周期硬布线控制器_1_beq ), .JAL(JAL), .Bne(\单周期硬布线控制器_1_bne ), .in_3(ID_IR[21]),
    .uret(\单周期硬布线控制器_1_uret ), .AUIPC(AUIPC), .LHU(LHU), .BLTU(\单周期硬布线控制器_1_bltu ),
    .rs1_used(\单周期硬布线控制器_1_rs1_used ), .rs2_used(\单周期硬布线控制器_1_rs2_used ));  // open: CSRRSI, CSRRCI
  Multiplexer #(.select(1), .width(5), .disabled("Z"), .enable("false")) multiplexer_4 (
    .in0(ID_IR[19:15]), .in1(5'b10001), .out(rs1), .sel(\单周期硬布线控制器_1_ecall ));
  Multiplexer #(.select(1), .width(5), .disabled("Z"), .enable("false")) multiplexer_5 (
    .in0(ID_IR[24:20]), .in1(5'b01010), .out(rs2), .sel(\单周期硬布线控制器_1_ecall ));
  assign bit_extender_1_out = {{12{ID_IR[31]}}, ID_IR[31:12]};  // Bit_Extender bit_extender_1
  redirect redirect_1 (
    .rs1(rs1), .EX_RegWrite(EX_RegWrite), .ecall(\单周期硬布线控制器_1_ecall ), .rs2(rs2),
    .MEM_RegWrite(MEM_RegWrite), .EX_MemToReg(EX_MemToReg), .EX_rd(EX_rd), .rs1_used(\单周期硬布线控制器_1_rs1_used ),
    .rs2_used(\单周期硬布线控制器_1_rs2_used ), .MEM_rd(MEM_rd), .loadUse(stall),
    .rs1_redirect(redirect_1_rs1_redirect), .rs2_redirect(redirect_1_rs2_redirect));
  Multiplexer #(.select(1), .width(12), .disabled("Z"), .enable("false")) multiplexer_6 (
    .in0(ID_IR[31:20]), .in1({ID_IR[31:25], ID_IR[11:7]}), .out(multiplexer_6_out), .sel(\单周期硬布线控制器_1_s_type ));
  Shifter #(.width(32), .shift("ll")) shifter_1 (.in(bit_extender_1_out), .\dist (5'b01100), .out(shifter_1_out));
  or or_10 (or_10_out, JAL, JALR);
  Counter #(.width(16), .max('hffff), .ongoal("wrap"), .trigger("rising"), .behavior("new")) counter_2 (
    .count(or_10_out), .Q(\无条件分支数 ), .clk(CLK));  // open: load, D, carry, clr, preset, down
  assign bit_extender_2_out = {{20{multiplexer_6_out[11]}}, multiplexer_6_out};  // Bit_Extender bit_extender_2
  assign bit_extender_3_out = {{20{ID_IR[31]}}, {ID_IR[31], ID_IR[7], ID_IR[30:25], ID_IR[11:8]}};  // Bit_Extender bit_extender_3
  assign bit_extender_4_out = {{12{ID_IR[31]}}, {ID_IR[31], ID_IR[19:12], ID_IR[20], ID_IR[30:21]}};  // Bit_Extender bit_extender_4
  not not_4 (not_4_out, CLK);
  Regifile regifile_1 (
    .Din(RDin), .Clk(not_4_out), .R1(regifile_1_r1), .R2(regifile_1_r2), .WE(RegWrite), .W_num(WB_rd),
    .R1_num(rs1), .R2_num(rs2));
  Multiplexer #(.select(1), .width(32), .disabled("Z"), .enable("false")) multiplexer_7 (
    .in0(bit_extender_3_out), .in1(bit_extender_4_out), .out(multiplexer_7_out), .sel(JAL));
  or or_11 (or_11_out, ~halt, Go);  // OR_Gate
  or or_12 (or_12_out, BranchTaken, INT, stall);
  ID_EX id_ex_1 (
    .Beq(\单周期硬布线控制器_1_beq ), .JAL(JAL), .Bne(\单周期硬布线控制器_1_bne ), .JALR(JALR),
    .MemToReg(\单周期硬布线控制器_1_memtoreg ), .AUIPC(AUIPC), .AluOp(\单周期硬布线控制器_1_alu_op ), .LHU(LHU),
    .AluSrcB(\单周期硬布线控制器_1_alu_src ), .BLTU(\单周期硬布线控制器_1_bltu ), .RegWrie(\单周期硬布线控制器_1_regwrite ),
    .ecall(\单周期硬布线控制器_1_ecall ), .uret(\单周期硬布线控制器_1_uret ), .R1(regifile_1_r1), .R2(regifile_1_r2),
    .rd(ID_IR[11:7]), .imm1(bit_extender_2_out), .imm2(multiplexer_7_out), .IR(ID_IR), .PC(ID_PC),
    .PC_4(if_id_1_pc_4_out), .Beq_2(id_ex_1_beq_2), .JAL_2(EX_JAL), .Bne_2(id_ex_1_bne_2), .JALR_2(EX_JALR),
    .MemToReg_2(EX_MemToReg), .AUIPC_2(id_ex_1_auipc_2), .AluOp_2(id_ex_1_aluop_2), .LHU_2(id_ex_1_lhu_2),
    .AluSrcB_2(id_ex_1_alusrcb_2), .BLTU_2(id_ex_1_bltu_2), .RegWrie_2(EX_RegWrite), .ecall_2(EX_ecall),
    .uret_2(EX_uret), .R1_2(id_ex_1_r1_2), .R2_2(id_ex_1_r2_2), .rd_2(EX_rd), .imm1_2(id_ex_1_imm1_2),
    .imm2_2(id_ex_1_imm2_2), .IR_2(EX_IR), .PC_2(EX_PC), .PC_4_2(EX_PC_4), .reset(RST), .flush(or_12_out),
    .enable(or_11_out), .clk(CLK), .MemWrite(\单周期硬布线控制器_1_memwrite ), .MemWrite_2(id_ex_1_memwrite_2),
    .imm_20(shifter_1_out), .imm_20_2(id_ex_1_imm_20_2), .rs1_redirect(redirect_1_rs1_redirect),
    .rs1_redirect_2(id_ex_1_rs1_redirect_2), .rs2_redirect_2(id_ex_1_rs2_redirect_2),
    .rs2_redirect(redirect_1_rs2_redirect));  // open: predictJump, predictJump_2, isBubblet, isBubble
  Multiplexer #(.select(2), .width(32), .disabled("Z"), .enable("false")) multiplexer_8 (
    .in0(id_ex_1_r1_2), .in1(RDin), .in2(MEM_AluRes), .out(R1), .sel(id_ex_1_rs1_redirect_2));  // open: in3
  Multiplexer #(.select(2), .width(32), .disabled("Z"), .enable("false")) multiplexer_9 (
    .in0(id_ex_1_r2_2), .in1(RDin), .in2(MEM_AluRes), .out(multiplexer_9_out), .sel(id_ex_1_rs2_redirect_2));  // open: in3
  Shifter #(.width(32), .shift("ll")) shifter_2 (.in(id_ex_1_imm2_2), .\dist (5'b00001), .out(shifter_2_out));
  and and_4 (and_4_out, id_ex_1_bltu_2, alu_1_out_6);
  Multiplexer #(.select(1), .width(32), .disabled("Z"), .enable("false")) multiplexer_10 (
    .in0(multiplexer_9_out), .in1(id_ex_1_imm1_2), .out(R2), .sel(id_ex_1_alusrcb_2));
  or or_13 (isBranch, and_4_out, and_6_out, and_5_out);
  and and_5 (and_5_out, ~alu_1_equal, id_ex_1_bne_2);  // AND_Gate
  and and_6 (and_6_out, id_ex_1_beq_2, alu_1_equal);
  ALU alu_1 (
    .X(R1), .Y(R2), .AluOP(id_ex_1_aluop_2), .Equal(alu_1_equal), .Result(alu_1_result), .out_6(alu_1_out_6));  // open: Result_2, out_4
  Adder #(.width(32)) adder_2 (.a(shifter_2_out), .b(EX_PC), .out(adder_2_out));  // open: cin, cout
  Comparator #(.width(32), .mode("twosComplement")) comparator_7 (
    .a(R1), .b(32'h22), .eq(comparator_7_eq));  // open: gt, lt
  assign and_7_out = alu_1_result & 32'hfffffffe;  // AND_Gate and_7, 32 bits wide
  and and_8 (and_8_out, EX_ecall, comparator_7_eq);
  Adder #(.width(32)) adder_3 (.a(EX_PC), .b(id_ex_1_imm_20_2), .out(adder_3_out));  // open: cin, cout
  and and_9 (EX_halt, EX_ecall, ~comparator_7_eq);  // AND_Gate
  Register #(.width(32), .trigger("rising"), .Select("low")) register_1 (
    .D(R2), .en(and_8_out), .Q(LedData), .clk(CLK));  // open: clr
  Multiplexer #(.select(1), .width(32), .disabled("Z"), .enable("false")) multiplexer_11 (
    .in0(adder_2_out), .in1(and_7_out), .out(branch), .sel(EX_JALR));
  or or_14 (or_14_out, ~halt, Go);  // OR_Gate
  EX_MEM ex_mem_1 (
    .JAL(EX_JAL), .JALR(EX_JALR), .MemToReg(EX_MemToReg), .AUIPC(id_ex_1_auipc_2),
    .MemWrite(id_ex_1_memwrite_2), .LHU(id_ex_1_lhu_2), .RegWrie(EX_RegWrite), .halt(EX_halt),
    .ALUResult(alu_1_result), .Write(multiplexer_9_out), .rd(EX_rd), .IR(EX_IR), .PC(EX_PC), .PC_4(EX_PC_4),
    .JAL_2(ex_mem_1_jal_2), .JALR_2(ex_mem_1_jalr_2), .MemToReg_2(ex_mem_1_memtoreg_2),
    .AUIPC_2(ex_mem_1_auipc_2), .MemWrite_2(MemWrite), .LHU_2(ex_mem_1_lhu_2), .RegWrie_2(MEM_RegWrite),
    .halt_2(ex_mem_1_halt_2), .ALUResult_2(ex_mem_1_aluresult_2), .Write_2(MDin), .rd_2(MEM_rd),
    .IR_2(MEM_IR), .PC_2(MEM_PC), .PC_4_2(ex_mem_1_pc_4_2), .reset(RST), .enable(or_14_out), .clk(CLK),
    .AUIPC_addr(adder_3_out), .AUIPC_addr_2(ex_mem_1_auipc_addr_2));
  Multiplexer #(.select(1), .width(32), .disabled("Z"), .enable("false")) multiplexer_12 (
    .in0(ex_mem_1_aluresult_2), .in1(ex_mem_1_auipc_addr_2), .out(MEM_AluRes), .sel(ex_mem_1_auipc_2));
  RAM #(.addrWidth(10), .dataWidth(32), .bus("separate"), .Select("high")) ram_1 (
    .addr(ex_mem_1_aluresult_2[11:2]), .din(MDin), .data(ram_1_data), .str(MemWrite), .sel(1'b1), .clk(CLK),
    .ld(1'b1), .clr(RST));
  MEM_WB mem_wb_1 (
    .JAL(ex_mem_1_jal_2), .JALR(ex_mem_1_jalr_2), .MemToReg(ex_mem_1_memtoreg_2), .AUIPC(ex_mem_1_auipc_2),
    .LHU(ex_mem_1_lhu_2), .RegWrie(MEM_RegWrite), .halt(ex_mem_1_halt_2), .ALUResult(ex_mem_1_aluresult_2),
    .ReadData(ram_1_data), .IR(MEM_IR), .PC(MEM_PC), .PC_4(ex_mem_1_pc_4_2), .JAL_2(mem_wb_1_jal_2),
    .JALR_2(mem_wb_1_jalr_2), .MemToReg_2(mem_wb_1_memtoreg_2), .AUIPC_2(mem_wb_1_auipc_2),
    .LHU_2(mem_wb_1_lhu_2), .RegWrie_2(RegWrite), .halt_2(halt), .ALUResult_2(mem_wb_1_aluresult_2),
    .ReadData_2(mem_wb_1_readdata_2), .IR_2(WB_IR), .PC_2(WB_PC), .PC_4_2(mem_wb_1_pc_4_2), .reset(RST),
    .enable(or_15_out), .clk(CLK), .AUIPC_addr(ex_mem_1_auipc_addr_2), .AUIPC_addr_2(mem_wb_1_auipc_addr_2),
    .rd(MEM_rd), .rd_2(WB_rd));
  or or_15 (or_15_out, ~halt, Go);  // OR_Gate
  Multiplexer #(.select(1), .width(32), .disabled("Z"), .enable("false")) multiplexer_13 (
    .in0(multiplexer_14_out), .in1(bit_extender_5_out), .out(RDin), .sel(mem_wb_1_lhu_2));
  assign bit_extender_5_out = {{16{1'b0}}, multiplexer_15_out};  // Bit_Extender bit_extender_5
  Multiplexer #(.select(1), .width(32), .disabled("Z"), .enable("false")) multiplexer_14 (
    .in0(multiplexer_16_out), .in1(mem_wb_1_auipc_addr_2), .out(multiplexer_14_out), .sel(mem_wb_1_auipc_2));
  Multiplexer #(.select(1), .width(16), .disabled("Z"), .enable("false")) multiplexer_15 (
    .in0(multiplexer_17_out), .in1(multiplexer_17_out_2), .out(multiplexer_15_out),
    .sel(mem_wb_1_aluresult_2[1]));
  or or_16 (or_16_out, mem_wb_1_jalr_2, mem_wb_1_jal_2);
  Multiplexer #(.select(1), .width(32), .disabled("Z"), .enable("false")) multiplexer_16 (
    .in0({multiplexer_17_out_2, multiplexer_17_out}), .in1(mem_wb_1_pc_4_2), .out(multiplexer_16_out),
    .sel(or_16_out));
  Multiplexer #(.select(1), .width(32), .disabled("Z"), .enable("false")) multiplexer_17 (
    .in0(mem_wb_1_aluresult_2), .in1(mem_wb_1_readdata_2), .out({multiplexer_17_out_2, multiplexer_17_out}),
    .sel(mem_wb_1_memtoreg_2));
  Register #(.width(1), .trigger("rising"), .Select("low")) register_2 (
    .D(1'b1), .Q(register_2_q), .clk(IR1_t), .clr(or_17_out));  // open: en
  or or_17 (or_17_out, register_5_q, RST);
  Register #(.width(1), .trigger("rising"), .Select("low")) register_3 (
    .D(1'b1), .Q(register_3_q), .clk(IR2_t), .clr(or_18_out));  // open: en
  or or_18 (or_18_out, register_6_q, RST);
  Register #(.width(1), .trigger("rising"), .Select("low")) register_4 (
    .D(1'b1), .Q(register_4_q), .clk(IR3_t), .clr(or_19_out));  // open: en
  or or_19 (or_19_out, register_7_q, RST);
  or or_20 (W1, register_2_q, register_5_q);
  or or_21 (or_21_out, register_2_q, register_5_q);
  or or_22 (W2, register_3_q, register_6_q);
  or or_23 (or_23_out, register_3_q, register_6_q);
  or or_24 (W3, register_4_q, register_7_q);
  or or_25 (or_25_out, register_4_q, register_7_q);
  and and_10 (and_10_out, or_21_out, ~clear1);  // AND_Gate
  and and_11 (and_11_out, or_23_out, ~clear2);  // AND_Gate
  and and_12 (and_12_out, or_25_out, ~clear3);  // AND_Gate
  Register #(.width(1), .trigger("rising"), .Select("low")) register_5 (
    .D(and_10_out), .Q(register_5_q), .clk(CLK), .clr(RST));  // open: en
  Register #(.width(1), .trigger("rising"), .Select("low")) register_6 (
    .D(and_11_out), .Q(register_6_q), .clk(CLK), .clr(RST));  // open: en
  Register #(.width(1), .trigger("rising"), .Select("low")) register_7 (
    .D(and_12_out), .Q(register_7_q), .clk(CLK), .clr(RST));  // open: en
  Priority_Encoder #(.select(2), .disabled("Z")) priority_encoder_1 (
    .in1(register_5_q), .in2(register_6_q), .in3(register_7_q), .out(priority_encoder_1_out),
    .gs(priority_encoder_1_gs));  // open: in0, en_out, en_in
  and and_13 (and_13_out, priority_encoder_1_gs, ~EX_uret);  // AND_Gate
  and and_14 (INT, priority_encoder_1_gs, IE);
  D_Flip_Flop #(.trigger("rising"), .Pre_Clr_Positions("LEGACY"), .NegatePresetClear("false"), .enable("true"), .NewFFLayout("false")) d_ff_1 (
    .clk(CLK), .D(and_13_out), .Qn(IE));  // open: Q, preset, en, reset
  Register #(.width(32), .trigger("falling"), .Select("low")) mEPC (
    .D(save_PC), .en(INT), .Q(ret_PC), .clk(CLK), .clr(RST));
  Register #(.width(1), .trigger("rising"), .Select("low")) register_8 (
    .D(BranchTaken), .Q(BTBefore1), .clk(CLK), .clr(RST));  // open: en
  Register #(.width(1), .trigger("rising"), .Select("low")) register_9 (
    .D(stall), .Q(loadUseBefore1), .clk(CLK), .clr(RST));  // open: en
  Multiplexer #(.select(2), .width(32), .disabled("Z"), .enable("false")) multiplexer_18 (
    .in1(32'h30ac), .in2(32'h3150), .in3(32'h31f4), .out(INT_PC), .sel(priority_encoder_1_out));  // open: in0
  Register #(.width(1), .trigger("rising"), .Select("low")) register_10 (
    .D(BTBefore1), .Q(BTBefore2), .clk(CLK), .clr(RST));  // open: en
  Register #(.width(2), .trigger("rising"), .Select("low")) register_11 (
    .D(priority_encoder_1_out), .en(INT), .Q(register_11_q), .clk(CLK), .clr(RST));
  Decoder #(.select(2), .tristate("false"), .disabled("Z"), .enable("false")) decoder_1 (
    .out1(decoder_1_out1), .out2(decoder_1_out2), .out3(decoder_1_out3), .sel(register_11_q));  // open: out0
  and and_15 (clear1, decoder_1_out1, IF_uret);
  and and_16 (clear2, decoder_1_out2, IF_uret);
  and and_17 (clear3, decoder_1_out3, IF_uret);
  Multiplexer #(.select(3), .width(32), .disabled("Z"), .enable("false")) multiplexer_19 (
    .in0(EX_PC), .in1(IF_PC), .in2(ID_PC), .in4(ID_PC), .out(save_PC),
    .sel({loadUseBefore1, BTBefore2, BTBefore1}));  // open: in3, in5, in6, in7

  // Other names for the same wires on the sheet: WB_RegWrite = RegWrite

  // Notes on the sheet:
  //   中断源
  //   中断等待指示
  //   总复位信号应将除ROM以外所有存储组件全部清零
  //   单级中断测试信号模拟器
  //   时空图监测，可删除
  //   数码管输出
  //   数码管输出应该用寄存器锁存，否则显示数据只能一闪而过
  //   为方便自动评测，需要输出PC，IR，寄存器堆写如数据RDin
  //   指令探针
  //   指令存储器
  //   RAM写使能MemWrite、RAM写入数据MDin等信号
  //   contents of rom_1 (hex, n*v repeats v):
  //   7d000113 100413 1f41993 41f9d993 433 c00913 800b13 140413 f47413 800293 100313 499993 89e9b3 1300533
  //   2200893 73 406282b3 fe0294e3 140413 f00f93 1f47433 1c41413 800293 100313 49d993 89e9b3 1300533
  //   2200893 73 406282b3 fe0294e3 1c45413 406b0b33 b0463 f95ff06f 2b3 fff2c293 1029293 fff2e293 500533
  //   2200893 73 f5dff06f 1112023 410113 a12023 410113 812023 410113 1312023 410113 1412023 410113 1512023
  //   410113 1612023 410113 100b13 300a13 100a93 1600433 441413 14469b3 1300533 2200893 73 fe0416e3
  //   415a0a33 fe0a10e3 ffc10113 12b03 ffc10113 12a83 ffc10113 12a03 ffc10113 12983 ffc10113 12403
  //   ffc10113 12503 ffc10113 12883 200073 1112023 410113 a12023 410113 812023 410113 1312023 410113
  //   1412023 410113 1512023 410113 1612023 410113 200b13 300a13 100a93 1600433 441413 14469b3 1300533
  //   2200893 73 fe0416e3 415a0a33 fe0a10e3 ffc10113 12b03 ffc10113 12a83 ffc10113 12a03 ffc10113 12983
  //   ffc10113 12403 ffc10113 12503 ffc10113 12883 200073 1112023 410113 a12023 410113 812023 410113
  //   1312023 410113 1412023 410113 1512023 410113 1612023 410113 300b13 300a13 100a93 1600433 441413
  //   14469b3 1300533 2200893 73 fe0416e3 415a0a33 fe0a10e3 ffc10113 12b03 ffc10113 12a83 ffc10113 12a03
  //   ffc10113 12983 ffc10113 12403 ffc10113 12503 ffc10113 12883 200073
  //   指令字
  //   Beq,Bne,Bltu
  //   JAL
  //   AUIPC
  //   JAL
  //   JALR
  //   Beq
  //   Bne
  //   AluOP
  //   AluSrcB
  //   RegWrite
  //   MemToReg
  //   MemWrite
  //   数据存储器
  //   LHU
  //   AUIPC
  //   JAL,JALR
endmodule

module \分支预测  (
  output RegWrite,
  output MemWrite,
  output [31:0] IF_PC,
  output [31:0] ID_PC,
  output [31:0] EX_PC,
  output [31:0] M_PC,
  output [31:0] WB_PC,
  output [31:0] RDin,
  output [31:0] MDin,
  output [31:0] LedData
);

  wire alu_1_equal, alu_1_out_6, and_1_out, and_2_out, and_3_out, and_4_out, and_5_out, and_6_out, and_8_out,
       branchTaken, CLK, clock_1_out, clock_2_out, comparator_1_eq, comparator_1_lt, comparator_2_eq,
       d_ff_1_q, EX_Beq, EX_Bltu, EX_Bne, EX_Branch, EX_ecall, EX_halt, Ex_isBubble, EX_JAL, EX_JALR,
       ex_mem_1_auipc_2, ex_mem_1_halt_2, ex_mem_1_jal_2, ex_mem_1_jalr_2, ex_mem_1_lhu_2,
       ex_mem_1_memtoreg_2, EX_MemToReg, EX_predictJump, EX_RegWrite, Go, halt, id_ex_1_alusrcb_2,
       id_ex_1_auipc_2, id_ex_1_lhu_2, id_ex_1_memwrite_2, if_id_1_isbubble_2, if_id_1_predictjump_2, IF_JAL,
       IF_JALR, IF_predictJump, IR1, IR2, IR3, isBranch, loadUse, MEM_RegWrite, mem_wb_1_auipc_2,
       mem_wb_1_jal_2, mem_wb_1_jalr_2, mem_wb_1_lhu_2, mem_wb_1_memtoreg_2, nand_1_out, not_1_out,
       not_2_out, not_3_out, not_4_out, or_1_out, or_2_out, or_3_out, or_4_out, or_5_out, or_8_out,
       or_10_out, or_11_out, predictError, RST, W1, W2, W3, \单周期硬布线控制器_1_alu_src , \单周期硬布线控制器_1_auipc ,
       \单周期硬布线控制器_1_beq , \单周期硬布线控制器_1_bltu , \单周期硬布线控制器_1_bne , \单周期硬布线控制器_1_ecall , \单周期硬布线控制器_1_lhu ,
       \单周期硬布线控制器_1_memtoreg , \单周期硬布线控制器_1_memwrite , \单周期硬布线控制器_1_regwrite , \单周期硬布线控制器_1_rs1_used ,
       \单周期硬布线控制器_1_rs2_used , \单周期硬布线控制器_1_s_type , \单周期硬布线控制器_1_uret ;
  wire [1:0] id_ex_1_rs1_redirect_2, id_ex_1_rs2_redirect_2, redirect_1_rs1_redirect, redirect_1_rs2_redirect;
  wire [3:0] id_ex_1_aluop_2, \单周期硬布线控制器_1_alu_op ;
  wire [4:0] EX_rd, MEM_rd, rs1, rs2, WB_rd;
  wire [11:0] multiplexer_5_out;
  wire [12:0] CNT_num;
  wire [15:0] \LoadUse次数 , multiplexer_15_out, multiplexer_17_out, multiplexer_17_out_2, \总周期数 , \插入气泡数 ,
       \无条件分支数 , \条件分支成功数 ;
  wire [31:0] adder_2_out, adder_3_out, alu_1_result, and_7_out, bit_extender_1_out, bit_extender_2_out,
       bit_extender_3_out, bit_extender_4_out, bit_extender_5_out, branchAddr, btb_1_jumpaddr, EX_IR,
       ex_mem_1_aluresult_2, ex_mem_1_auipc_addr_2, ex_mem_1_pc_4_2, EX_PC_4, id_ex_1_imm1_2, id_ex_1_imm2_2,
       id_ex_1_imm_20_2, id_ex_1_r1_2, id_ex_1_r2_2, ID_IR, if_id_1_pc_4_out, IF_IR, IF_PC_4, MEM_AluRes,
       MEM_IR, mem_wb_1_aluresult_2, mem_wb_1_auipc_addr_2, mem_wb_1_pc_4_2, mem_wb_1_readdata_2,
       multiplexer_1_out, multiplexer_2_out, multiplexer_7_out, multiplexer_9_out, multiplexer_14_out,
       multiplexer_16_out, predictAddr, R1, R2, ram_1_data, regifile_1_r1, regifile_1_r2, shifter_1_out,
       shifter_2_out, WB_IR;

  Button \u_总复位  (.out(RST));
  Button _1 (.out(IR1));
  Button _2 (.out(IR2));
  Button _3 (.out(IR3));
  // Probe on \总周期数 
  // Probe on \总周期数 
  Button \u_继续运行  (.out(Go));
  LED #(.active("true")) led_1 (.in(W1));
  LED #(.active("true")) led_2 (.in(W2));
  LED #(.active("true")) led_3 (.in(W3));
  Hex_Digit_Display hex_digit_display_1 (.value(LedData[31:28]));  // open: dp
  // Probe on IF_PC[19:0]
  // RiscV_Probe riscv_probe_1: pin names not known; wires that end beside it: IF_IR
  Hex_Digit_Display hex_digit_display_2 (.value(LedData[23:20]));  // open: dp
  Hex_Digit_Display hex_digit_display_3 (.value(LedData[27:24]));  // open: dp
  // Probe on ID_PC[19:0]
  // RiscV_Probe riscv_probe_2: pin names not known; wires that end beside it: ID_IR
  Hex_Digit_Display hex_digit_display_4 (.value(LedData[19:16]));  // open: dp
  Hex_Digit_Display hex_digit_display_5 (.value(LedData[15:12]));  // open: dp
  Multiplexer #(.select(1), .width(32), .disabled("Z"), .enable("false")) multiplexer_1 (
    .in0(EX_PC_4), .in1(branchAddr), .out(multiplexer_1_out), .sel(branchTaken));
  Hex_Digit_Display hex_digit_display_6 (.value(LedData[11:8]));  // open: dp
  Hex_Digit_Display hex_digit_display_7 (.value(LedData[7:4]));  // open: dp
  Clock #(.highDuration(1), .lowDuration(1)) clock_1 (.out(clock_1_out));
  // Probe on EX_PC[19:0]
  // RiscV_Probe riscv_probe_3: pin names not known; wires that end beside it: clock_1_out, EX_IR, CLK
  Multiplexer #(.select(1), .width(32), .disabled("Z"), .enable("false")) multiplexer_2 (
    .in0(predictAddr), .in1(multiplexer_1_out), .out(multiplexer_2_out), .sel(predictError));
  Hex_Digit_Display hex_digit_display_8 (.value(LedData[3:0]));  // open: dp
  // Probe on \总周期数 
  // Probe on M_PC[19:0]
  // RiscV_Probe riscv_probe_4: pin names not known; wires that end beside it: MEM_IR
  or or_1 (or_1_out, and_1_out, Go);
  and and_1 (and_1_out, not_1_out, not_2_out);
  not not_1 (not_1_out, loadUse);
  not not_2 (not_2_out, halt);
  // Probe on \总周期数 
  // Probe on \无条件分支数 
  // Probe on \条件分支成功数 
  // Probe on \插入气泡数 
  // Probe on \LoadUse次数 
  // Probe on IF_PC[11:0]
  // Probe on WB_PC[19:0]
  // RiscV_Probe riscv_probe_5: pin names not known; wires that end beside it: WB_IR
  Register #(.width(32), .trigger("rising"), .Select("low")) PC (
    .D(multiplexer_2_out), .en(or_1_out), .Q(IF_PC), .clk(CLK), .clr(RST));
  // Probe on EX_PC[11:0]
  // Probe on ID_PC[11:0]
  not not_3 (not_3_out, halt);
  Adder #(.width(32)) adder_1 (.a(IF_PC), .b(32'h4), .out(IF_PC_4));  // open: cin, cout
  // Probe on M_PC[11:0]
  D_Flip_Flop #(.trigger("high"), .Pre_Clr_Positions("LEGACY"), .NegatePresetClear("false"), .enable("true"), .NewFFLayout("false")) d_ff_1 (.Q(d_ff_1_q));  // open: clk, D, Qn, preset, en, reset
  // Probe on 13'hc
  Counter #(.width(16), .max('hffff), .ongoal("wrap"), .trigger("rising"), .behavior("new")) counter_1 (
    .count(not_3_out), .Q(\总周期数 ), .clk(CLK));  // open: load, D, carry, clr, preset, down
  // RiscV_Probe riscv_probe_6: pin names not known; wires that end beside it: IF_IR
  // Probe on WB_PC[11:0]
  Comparator #(.width(13), .mode("twosComplement")) comparator_1 (
    .a(CNT_num), .b(13'hc), .eq(comparator_1_eq), .lt(comparator_1_lt));  // open: gt
  Clock #(.highDuration(1), .lowDuration(1)) clock_2 (.out(clock_2_out));
  ROM #(.addrWidth(10), .dataWidth(32), .Select("high")) rom_1 (.addr(IF_PC[11:2]), .data(IF_IR));
  or or_2 (or_2_out, ~halt, Go);  // OR_Gate
  nand nand_1 (nand_1_out, d_ff_1_q, comparator_1_eq);
  Counter #(.width(13), .max('h1fff), .ongoal("stay"), .trigger("rising"), .behavior("old")) counter_2 (
    .count(comparator_1_lt), .Q(CNT_num), .clk(clock_2_out));  // open: load, D, carry, clr, preset
  and and_2 (and_2_out, ~loadUse, or_2_out);  // AND_Gate
  assign CLK = nand_1_out ? clock_2_out : 1'bz;  // Controlled_Buffer controlled_buffer_1
  IF_ID if_id_1 (
    .IR_in(IF_IR), .PC_in(IF_PC), .PC_4_in(IF_PC_4), .IR_out(ID_IR), .PC_out(ID_PC),
    .PC_4_out(if_id_1_pc_4_out), .RST(RST), .branchTaken(predictError), .en(and_2_out), .clk(CLK),
    .predictJump(IF_predictJump), .predictJump_2(if_id_1_predictjump_2), .isBubble(1'b0),
    .isBubble_2(if_id_1_isbubble_2));
  Pull_Resistor #(.pull(1)) pull_resistor_1 (.node(CLK));
  \单周期硬布线控制器  \u_单周期硬布线控制器_1  (
    .Funct({ID_IR[30], ID_IR[25], ID_IR[14:12]}), .OP(ID_IR[6:2]), .ALU_OP(\单周期硬布线控制器_1_alu_op ),
    .MemToReg(\单周期硬布线控制器_1_memtoreg ), .MemWrite(\单周期硬布线控制器_1_memwrite ), .ALU_SRC(\单周期硬布线控制器_1_alu_src ),
    .RegWrite(\单周期硬布线控制器_1_regwrite ), .ecall(\单周期硬布线控制器_1_ecall ), .S_type(\单周期硬布线控制器_1_s_type ),
    .Jalr(IF_JALR), .Beq(\单周期硬布线控制器_1_beq ), .JAL(IF_JAL), .Bne(\单周期硬布线控制器_1_bne ), .in_3(ID_IR[21]),
    .uret(\单周期硬布线控制器_1_uret ), .AUIPC(\单周期硬布线控制器_1_auipc ), .LHU(\单周期硬布线控制器_1_lhu ),
    .BLTU(\单周期硬布线控制器_1_bltu ), .rs1_used(\单周期硬布线控制器_1_rs1_used ), .rs2_used(\单周期硬布线控制器_1_rs2_used ));  // open: CSRRSI, CSRRCI
  Multiplexer #(.select(1), .width(5), .disabled("Z"), .enable("false")) multiplexer_3 (
    .in0(ID_IR[19:15]), .in1(5'b10001), .out(rs1), .sel(\单周期硬布线控制器_1_ecall ));
  Multiplexer #(.select(1), .width(5), .disabled("Z"), .enable("false")) multiplexer_4 (
    .in0(ID_IR[24:20]), .in1(5'b01010), .out(rs2), .sel(\单周期硬布线控制器_1_ecall ));
  assign bit_extender_1_out = {{12{ID_IR[31]}}, ID_IR[31:12]};  // Bit_Extender bit_extender_1
  BTB btb_1 (
    .clk(CLK), .PredictJump(IF_predictJump), .EX_PC(EX_PC), .PC(IF_PC), .EX_branch(EX_Branch),
    .JumpAddr(btb_1_jumpaddr), .EX_BranchAddr(branchAddr), .EX_BranchTaken(branchTaken));
  or or_3 (or_3_out, EX_JAL, EX_JALR);
  redirect redirect_1 (
    .rs1(rs1), .EX_RegWrite(EX_RegWrite), .ecall(\单周期硬布线控制器_1_ecall ), .rs2(rs2),
    .MEM_RegWrite(MEM_RegWrite), .EX_MemToReg(EX_MemToReg), .EX_rd(EX_rd), .rs1_used(\单周期硬布线控制器_1_rs1_used ),
    .rs2_used(\单周期硬布线控制器_1_rs2_used ), .MEM_rd(MEM_rd), .loadUse(loadUse),
    .rs1_redirect(redirect_1_rs1_redirect), .rs2_redirect(redirect_1_rs2_redirect));
  Multiplexer #(.select(1), .width(12), .disabled("Z"), .enable("false")) multiplexer_5 (
    .in0(ID_IR[31:20]), .in1({ID_IR[31:25], ID_IR[11:7]}), .out(multiplexer_5_out), .sel(\单周期硬布线控制器_1_s_type ));
  Shifter #(.width(32), .shift("ll")) shifter_1 (.in(bit_extender_1_out), .\dist (5'b01100), .out(shifter_1_out));
  Counter #(.width(16), .max('hffff), .ongoal("wrap"), .trigger("rising"), .behavior("new")) counter_3 (
    .count(or_3_out), .Q(\无条件分支数 ), .clk(CLK));  // open: load, D, carry, clr, preset, down
  assign bit_extender_2_out = {{20{multiplexer_5_out[11]}}, multiplexer_5_out};  // Bit_Extender bit_extender_2
  assign bit_extender_3_out = {{20{ID_IR[31]}}, {ID_IR[31], ID_IR[7], ID_IR[30:25], ID_IR[11:8]}};  // Bit_Extender bit_extender_3
  assign bit_extender_4_out = {{12{ID_IR[31]}}, {ID_IR[31], ID_IR[19:12], ID_IR[20], ID_IR[30:21]}};  // Bit_Extender bit_extender_4
  Multiplexer #(.select(1), .width(32), .disabled("Z"), .enable("false")) multiplexer_6 (
    .in0(IF_PC_4), .in1(btb_1_jumpaddr), .out(predictAddr), .sel(IF_predictJump));
  not not_4 (not_4_out, CLK);
  Regifile regifile_1 (
    .Din(RDin), .Clk(not_4_out), .R1(regifile_1_r1), .R2(regifile_1_r2), .WE(RegWrite), .W_num(WB_rd),
    .R1_num(rs1), .R2_num(rs2));
  Multiplexer #(.select(1), .width(32), .disabled("Z"), .enable("false")) multiplexer_7 (
    .in0(bit_extender_3_out), .in1(bit_extender_4_out), .out(multiplexer_7_out), .sel(IF_JAL));
  or or_4 (or_4_out, ~halt, Go);  // OR_Gate
  or or_5 (or_5_out, loadUse, predictError);
  ID_EX id_ex_1 (
    .Beq(\单周期硬布线控制器_1_beq ), .JAL(IF_JAL), .Bne(\单周期硬布线控制器_1_bne ), .JALR(IF_JALR),
    .MemToReg(\单周期硬布线控制器_1_memtoreg ), .AUIPC(\单周期硬布线控制器_1_auipc ), .AluOp(\单周期硬布线控制器_1_alu_op ),
    .LHU(\单周期硬布线控制器_1_lhu ), .AluSrcB(\单周期硬布线控制器_1_alu_src ), .BLTU(\单周期硬布线控制器_1_bltu ),
    .RegWrie(\单周期硬布线控制器_1_regwrite ), .ecall(\单周期硬布线控制器_1_ecall ), .uret(\单周期硬布线控制器_1_uret ),
    .R1(regifile_1_r1), .R2(regifile_1_r2), .rd(ID_IR[11:7]), .imm1(bit_extender_2_out),
    .imm2(multiplexer_7_out), .IR(ID_IR), .PC(ID_PC), .PC_4(if_id_1_pc_4_out), .Beq_2(EX_Beq),
    .JAL_2(EX_JAL), .Bne_2(EX_Bne), .JALR_2(EX_JALR), .MemToReg_2(EX_MemToReg), .AUIPC_2(id_ex_1_auipc_2),
    .AluOp_2(id_ex_1_aluop_2), .LHU_2(id_ex_1_lhu_2), .AluSrcB_2(id_ex_1_alusrcb_2), .BLTU_2(EX_Bltu),
    .RegWrie_2(EX_RegWrite), .ecall_2(EX_ecall), .R1_2(id_ex_1_r1_2), .R2_2(id_ex_1_r2_2), .rd_2(EX_rd),
    .imm1_2(id_ex_1_imm1_2), .imm2_2(id_ex_1_imm2_2), .IR_2(EX_IR), .PC_2(EX_PC), .PC_4_2(EX_PC_4),
    .reset(RST), .flush(or_5_out), .enable(or_4_out), .clk(CLK), .MemWrite(\单周期硬布线控制器_1_memwrite ),
    .MemWrite_2(id_ex_1_memwrite_2), .imm_20(shifter_1_out), .imm_20_2(id_ex_1_imm_20_2),
    .rs1_redirect(redirect_1_rs1_redirect), .rs1_redirect_2(id_ex_1_rs1_redirect_2),
    .rs2_redirect_2(id_ex_1_rs2_redirect_2), .rs2_redirect(redirect_1_rs2_redirect),
    .predictJump(if_id_1_predictjump_2), .predictJump_2(EX_predictJump), .isBubblet(if_id_1_isbubble_2),
    .isBubble(Ex_isBubble));  // open: uret_2
  and and_3 (and_3_out, branchTaken, ~predictError);  // AND_Gate
  Multiplexer #(.select(2), .width(32), .disabled("Z"), .enable("false")) multiplexer_8 (
    .in0(id_ex_1_r1_2), .in1(RDin), .in2(MEM_AluRes), .out(R1), .sel(id_ex_1_rs1_redirect_2));  // open: in3
  Multiplexer #(.select(2), .width(32), .disabled("Z"), .enable("false")) multiplexer_9 (
    .in0(id_ex_1_r2_2), .in1(RDin), .in2(MEM_AluRes), .out(multiplexer_9_out), .sel(id_ex_1_rs2_redirect_2));  // open: in3
  Shifter #(.width(32), .shift("ll")) shifter_2 (.in(id_ex_1_imm2_2), .\dist (5'b00001), .out(shifter_2_out));
  Counter #(.width(16), .max('hffff), .ongoal("wrap"), .trigger("rising"), .behavior("new")) counter_4 (
    .count(and_3_out), .Q(\条件分支成功数 ), .clk(CLK));  // open: load, D, carry, clr, preset, down
  and and_4 (and_4_out, EX_Bltu, alu_1_out_6);
  Multiplexer #(.select(1), .width(32), .disabled("Z"), .enable("false")) multiplexer_10 (
    .in0(multiplexer_9_out), .in1(id_ex_1_imm1_2), .out(R2), .sel(id_ex_1_alusrcb_2));
  xor xor_1 (predictError, branchTaken, EX_predictJump);
  or or_6 (isBranch, and_4_out, and_6_out, and_5_out);
  and and_5 (and_5_out, ~alu_1_equal, EX_Bne);  // AND_Gate
  and and_6 (and_6_out, EX_Beq, alu_1_equal);
  ALU alu_1 (
    .X(R1), .Y(R2), .AluOP(id_ex_1_aluop_2), .Equal(alu_1_equal), .Result(alu_1_result), .out_6(alu_1_out_6));  // open: Result_2, out_4
  Adder #(.width(32)) adder_2 (.a(shifter_2_out), .b(EX_PC), .out(adder_2_out));  // open: cin, cout
  Comparator #(.width(32), .mode("twosComplement")) comparator_2 (
    .a(R1), .b(32'h22), .eq(comparator_2_eq));  // open: gt, lt
  assign and_7_out = alu_1_result & 32'hfffffffe;  // AND_Gate and_7, 32 bits wide
  and and_8 (and_8_out, EX_ecall, comparator_2_eq);
  or or_7 (branchTaken, EX_JALR, EX_JAL, isBranch);
  Adder #(.width(32)) adder_3 (.a(EX_PC), .b(id_ex_1_imm_20_2), .out(adder_3_out));  // open: cin, cout
  and and_9 (EX_halt, EX_ecall, ~comparator_2_eq);  // AND_Gate
  Register #(.width(32), .trigger("rising"), .Select("low")) register_1 (
    .D(R2), .en(and_8_out), .Q(LedData), .clk(CLK));  // open: clr
  Counter #(.width(16), .max('hffff), .ongoal("wrap"), .trigger("rising"), .behavior("new")) counter_5 (
    .count(Ex_isBubble), .Q(\插入气泡数 ), .clk(CLK));  // open: load, D, carry, clr, preset, down
  Multiplexer #(.select(1), .width(32), .disabled("Z"), .enable("false")) multiplexer_11 (
    .in0(adder_2_out), .in1(and_7_out), .out(branchAddr), .sel(EX_JALR));
  or or_8 (or_8_out, ~halt, Go);  // OR_Gate
  EX_MEM ex_mem_1 (
    .JAL(EX_JAL), .JALR(EX_JALR), .MemToReg(EX_MemToReg), .AUIPC(id_ex_1_auipc_2),
    .MemWrite(id_ex_1_memwrite_2), .LHU(id_ex_1_lhu_2), .RegWrie(EX_RegWrite), .halt(EX_halt),
    .ALUResult(alu_1_result), .Write(multiplexer_9_out), .rd(EX_rd), .IR(EX_IR), .PC(EX_PC), .PC_4(EX_PC_4),
    .JAL_2(ex_mem_1_jal_2), .JALR_2(ex_mem_1_jalr_2), .MemToReg_2(ex_mem_1_memtoreg_2),
    .AUIPC_2(ex_mem_1_auipc_2), .MemWrite_2(MemWrite), .LHU_2(ex_mem_1_lhu_2), .RegWrie_2(MEM_RegWrite),
    .halt_2(ex_mem_1_halt_2), .ALUResult_2(ex_mem_1_aluresult_2), .Write_2(MDin), .rd_2(MEM_rd),
    .IR_2(MEM_IR), .PC_2(M_PC), .PC_4_2(ex_mem_1_pc_4_2), .reset(RST), .enable(or_8_out), .clk(CLK),
    .AUIPC_addr(adder_3_out), .AUIPC_addr_2(ex_mem_1_auipc_addr_2));
  or or_9 (EX_Branch, EX_JAL, EX_JALR, EX_Bne, EX_Beq, EX_Bltu);
  Counter #(.width(16), .max('hffff), .ongoal("wrap"), .trigger("rising"), .behavior("new")) counter_6 (
    .count(loadUse), .Q(\LoadUse次数 ), .clk(CLK));  // open: load, D, carry, clr, preset, down
  Multiplexer #(.select(1), .width(32), .disabled("Z"), .enable("false")) multiplexer_12 (
    .in0(ex_mem_1_aluresult_2), .in1(ex_mem_1_auipc_addr_2), .out(MEM_AluRes), .sel(ex_mem_1_auipc_2));
  RAM #(.addrWidth(10), .dataWidth(32), .bus("separate"), .Select("high")) ram_1 (
    .addr(ex_mem_1_aluresult_2[11:2]), .din(MDin), .data(ram_1_data), .str(MemWrite), .sel(1'b1), .clk(CLK),
    .ld(1'b1), .clr(RST));
  MEM_WB mem_wb_1 (
    .JAL(ex_mem_1_jal_2), .JALR(ex_mem_1_jalr_2), .MemToReg(ex_mem_1_memtoreg_2), .AUIPC(ex_mem_1_auipc_2),
    .LHU(ex_mem_1_lhu_2), .RegWrie(MEM_RegWrite), .halt(ex_mem_1_halt_2), .ALUResult(ex_mem_1_aluresult_2),
    .ReadData(ram_1_data), .IR(MEM_IR), .PC(M_PC), .PC_4(ex_mem_1_pc_4_2), .JAL_2(mem_wb_1_jal_2),
    .JALR_2(mem_wb_1_jalr_2), .MemToReg_2(mem_wb_1_memtoreg_2), .AUIPC_2(mem_wb_1_auipc_2),
    .LHU_2(mem_wb_1_lhu_2), .RegWrie_2(RegWrite), .halt_2(halt), .ALUResult_2(mem_wb_1_aluresult_2),
    .ReadData_2(mem_wb_1_readdata_2), .IR_2(WB_IR), .PC_2(WB_PC), .PC_4_2(mem_wb_1_pc_4_2), .reset(RST),
    .enable(or_10_out), .clk(CLK), .AUIPC_addr(ex_mem_1_auipc_addr_2), .AUIPC_addr_2(mem_wb_1_auipc_addr_2),
    .rd(MEM_rd), .rd_2(WB_rd));
  or or_10 (or_10_out, ~halt, Go);  // OR_Gate
  Multiplexer #(.select(1), .width(32), .disabled("Z"), .enable("false")) multiplexer_13 (
    .in0(multiplexer_14_out), .in1(bit_extender_5_out), .out(RDin), .sel(mem_wb_1_lhu_2));
  assign bit_extender_5_out = {{16{1'b0}}, multiplexer_15_out};  // Bit_Extender bit_extender_5
  Multiplexer #(.select(1), .width(32), .disabled("Z"), .enable("false")) multiplexer_14 (
    .in0(multiplexer_16_out), .in1(mem_wb_1_auipc_addr_2), .out(multiplexer_14_out), .sel(mem_wb_1_auipc_2));
  Multiplexer #(.select(1), .width(16), .disabled("Z"), .enable("false")) multiplexer_15 (
    .in0(multiplexer_17_out), .in1(multiplexer_17_out_2), .out(multiplexer_15_out),
    .sel(mem_wb_1_aluresult_2[1]));
  or or_11 (or_11_out, mem_wb_1_jalr_2, mem_wb_1_jal_2);
  Multiplexer #(.select(1), .width(32), .disabled("Z"), .enable("false")) multiplexer_16 (
    .in0({multiplexer_17_out_2, multiplexer_17_out}), .in1(mem_wb_1_pc_4_2), .out(multiplexer_16_out),
    .sel(or_11_out));
  Multiplexer #(.select(1), .width(32), .disabled("Z"), .enable("false")) multiplexer_17 (
    .in0(mem_wb_1_aluresult_2), .in1(mem_wb_1_readdata_2), .out({multiplexer_17_out_2, multiplexer_17_out}),
    .sel(mem_wb_1_memtoreg_2));

  // Other names for the same wires on the sheet: MEM_PC[31:0] = M_PC; WB_RegWrite = RegWrite

  // Notes on the sheet:
  //   中断源
  //   时空图监测，可删除
  //   中断等待指示
  //   数码管输出
  //   控制位
  //   流水调试日志用
  //   暂停节拍，不能为0
  //   指令探针
  //   指令存储器
  //   戳工具置1进入计数暂停模式，ctrl+k时钟自动运行到对应节拍暂停
  //   ctrl+k关闭时钟连续运行，将控制位置零，进入单步调试模式调试
  //   contents of rom_1 (hex, n*v repeats v):
  //   100493 100006f 100493 200913 300993 100006f 100493 200913 300993 100006f 100493 200913 300993
  //   100006f 100493 200913 300993 29c000ef 100413 100493 1f49493 900533 2200893 73 24d493 48463 fedff06f
  //   900533 2200893 73 100493 249493 900533 2200893 73 48463 fedff06f 100493 1f49493 900533 2200893 73
  //   4034d493 900533 2200893 73 4044d493 900533 2200893 73 4044d493 900533 2200893 73 4044d493 900533
  //   2200893 73 4044d493 900533 2200893 73 4044d493 900533 2200893 73 4044d493 900533 2200893 73 4044d493
  //   900533 2200893 73 100413 1f41993 41f9d993 433 c00913 300b13 140413 f47413 800293 100313 499993
  //   89e9b3 1300533 2200893 73 406282b3 fe0294e3 140413 f00f93 1f47433 1c41413 800293 100313 49d993
  //   89e9b3 1300533 2200893 73 406282b3 fe0294e3 1c45413 406b0b33 b0463 f95ff06f 2b3 fff2c293 829293
  //   ff2e293 500533 2200893 73 fff00413 493 84a023 140413 448493 84a023 140413 448493 84a023 140413
  //   448493 84a023 140413 448493 84a023 140413 448493 84a023 140413 448493 84a023 140413 448493 84a023
  //   140413 448493 84a023 140413 448493 84a023 140413 448493 84a023 140413 448493 84a023 140413 448493
  //   84a023 140413 448493 84a023 140413 448493 84a023 140413 448493 84a023 140413 448493 140413 433
  //   3c00493 42983 4aa03 149a2b3 28663 134a023 1442023 ffc48493 fe9412e3 800533 2200893 73 440413 3c00493
  //   fc9416e3 a00893 73 413 140413 800533 2200893 73 240413 800533 2200893 73 340413 800533 2200893 73
  //   440413 800533 2200893 73 540413 800533 2200893 73 640413 800533 2200893 73 740413 800533 2200893 73
  //   840413 800533 2200893 2200893 73 8067
  //   可计数暂停的时钟源
  //   指令字
  //   Beq,Bne,Bltu
  //   JAL
  //   AUIPC
  //   JAL
  //   JALR
  //   Beq
  //   Bne
  //   AluOP
  //   AluSrcB
  //   RegWrite
  //   为方便自动评测，需要输出流水线各段保存的PC值，注意是PC不是PC+4，另外ID段寄存器写入信息，Mem段内存写入信息也要输出
  //   MemToReg
  //   MemWrite
  //   数据存储器
  //   LHU
  //   AUIPC
  //   JAL,JALR
endmodule
module IF_ID (
  input  [31:0] IR_in,
  input  [31:0] PC_in,
  input  [31:0] PC_4_in,
  input  predictJump,
  input  isBubble,
  input  en,
  input  clk,
  input  RST,
  input  branchTaken,
  output [31:0] IR_out,
  output [31:0] PC_out,
  output [31:0] PC_4_out,
  output predictJump_2,
  output isBubble_2
);

  wire multiplexer_4_out, multiplexer_5_out, or_1_out;
  wire [31:0] multiplexer_1_out, multiplexer_2_out, multiplexer_3_out;

  Multiplexer #(.select(1), .width(32), .disabled("Z"), .enable("false")) multiplexer_1 (
    .in0(IR_in), .in1({32{1'b0}}), .out(multiplexer_1_out), .sel(or_1_out));
  Multiplexer #(.select(1), .width(32), .disabled("Z"), .enable("false")) multiplexer_2 (
    .in0(PC_in), .in1({32{1'b0}}), .out(multiplexer_2_out), .sel(or_1_out));
  Multiplexer #(.select(1), .width(32), .disabled("Z"), .enable("false")) multiplexer_3 (
    .in0(PC_4_in), .in1({32{1'b0}}), .out(multiplexer_3_out), .sel(or_1_out));
  Multiplexer #(.select(1), .width(1), .disabled("Z"), .enable("false")) multiplexer_4 (
    .in0(predictJump), .in1(1'b0), .out(multiplexer_4_out), .sel(or_1_out));
  Multiplexer #(.select(1), .width(1), .disabled("Z"), .enable("false")) multiplexer_5 (
    .in0(isBubble), .in1(1'b1), .out(multiplexer_5_out), .sel(branchTaken));
  or or_1 (or_1_out, RST, branchTaken);
  Register #(.width(32), .trigger("rising"), .Select("low")) register_1 (
    .D(multiplexer_1_out), .en(en), .Q(IR_out), .clk(clk));  // open: clr
  Register #(.width(32), .trigger("rising"), .Select("low")) register_2 (
    .D(multiplexer_2_out), .en(en), .Q(PC_out), .clk(clk));  // open: clr
  Register #(.width(32), .trigger("rising"), .Select("low")) register_3 (
    .D(multiplexer_3_out), .en(en), .Q(PC_4_out), .clk(clk));  // open: clr
  Register #(.width(1), .trigger("rising"), .Select("low")) register_4 (
    .D(multiplexer_4_out), .en(en), .Q(predictJump_2), .clk(clk));  // open: clr
  Register #(.width(1), .trigger("rising"), .Select("low")) register_5 (
    .D(multiplexer_5_out), .en(en), .Q(isBubble_2), .clk(clk));  // open: clr
endmodule

module ID_EX (
  input  Beq,
  input  [1:0] rs1_redirect,
  input  [1:0] rs2_redirect,
  input  JAL,
  input  Bne,
  input  JALR,
  input  MemToReg,
  input  AUIPC,
  input  MemWrite,
  input  [3:0] AluOp,
  input  LHU,
  input  AluSrcB,
  input  BLTU,
  input  RegWrie,
  input  predictJump,
  input  ecall,
  input  uret,
  input  [31:0] R1,
  input  [31:0] R2,
  input  [4:0] rd,
  input  [31:0] imm1,
  input  [31:0] imm2,
  input  [31:0] IR,
  input  [31:0] PC,
  input  [31:0] PC_4,
  input  [31:0] imm_20,
  input  isBubblet,
  input  enable,
  input  reset,
  input  clk,
  input  flush,
  output Beq_2,
  output [1:0] rs1_redirect_2,
  output [1:0] rs2_redirect_2,
  output JAL_2,
  output Bne_2,
  output JALR_2,
  output MemToReg_2,
  output AUIPC_2,
  output MemWrite_2,
  output [3:0] AluOp_2,
  output LHU_2,
  output AluSrcB_2,
  output BLTU_2,
  output RegWrie_2,
  output predictJump_2,
  output ecall_2,
  output uret_2,
  output [31:0] R1_2,
  output [31:0] R2_2,
  output [4:0] rd_2,
  output [31:0] imm1_2,
  output [31:0] imm2_2,
  output [31:0] IR_2,
  output [31:0] PC_2,
  output [31:0] PC_4_2,
  output [31:0] imm_20_2,
  output isBubble
);

  wire multiplexer_1_out, multiplexer_4_out, multiplexer_5_out, multiplexer_6_out, multiplexer_7_out,
       multiplexer_8_out, multiplexer_9_out, multiplexer_11_out, multiplexer_12_out, multiplexer_13_out,
       multiplexer_14_out, multiplexer_15_out, multiplexer_16_out, multiplexer_17_out, multiplexer_27_out,
       or_1_out;
  wire [1:0] multiplexer_2_out, multiplexer_3_out;
  wire [3:0] multiplexer_10_out;
  wire [4:0] multiplexer_20_out;
  wire [31:0] multiplexer_18_out, multiplexer_19_out, multiplexer_21_out, multiplexer_22_out,
       multiplexer_23_out, multiplexer_24_out, multiplexer_25_out, multiplexer_26_out;

  Multiplexer #(.select(1), .width(1), .disabled("Z"), .enable("false")) multiplexer_1 (
    .in0(Beq), .in1(1'b0), .out(multiplexer_1_out), .sel(or_1_out));
  Multiplexer #(.select(1), .width(2), .disabled("Z"), .enable("false")) multiplexer_2 (
    .in0(rs1_redirect), .in1(2'b00), .out(multiplexer_2_out), .sel(or_1_out));
  Multiplexer #(.select(1), .width(2), .disabled("Z"), .enable("false")) multiplexer_3 (
    .in0(rs2_redirect), .in1(2'b00), .out(multiplexer_3_out), .sel(or_1_out));
  Multiplexer #(.select(1), .width(1), .disabled("Z"), .enable("false")) multiplexer_4 (
    .in0(JAL), .in1(1'b0), .out(multiplexer_4_out), .sel(or_1_out));
  Multiplexer #(.select(1), .width(1), .disabled("Z"), .enable("false")) multiplexer_5 (
    .in0(Bne), .in1(1'b0), .out(multiplexer_5_out), .sel(or_1_out));
  Multiplexer #(.select(1), .width(1), .disabled("Z"), .enable("false")) multiplexer_6 (
    .in0(JALR), .in1(1'b0), .out(multiplexer_6_out), .sel(or_1_out));
  Multiplexer #(.select(1), .width(1), .disabled("Z"), .enable("false")) multiplexer_7 (
    .in0(MemToReg), .in1(1'b0), .out(multiplexer_7_out), .sel(or_1_out));
  Multiplexer #(.select(1), .width(1), .disabled("Z"), .enable("false")) multiplexer_8 (
    .in0(AUIPC), .in1(1'b0), .out(multiplexer_8_out), .sel(or_1_out));
  Multiplexer #(.select(1), .width(1), .disabled("Z"), .enable("false")) multiplexer_9 (
    .in0(MemWrite), .in1(1'b0), .out(multiplexer_9_out), .sel(or_1_out));
  Multiplexer #(.select(1), .width(4), .disabled("Z"), .enable("false")) multiplexer_10 (
    .in0(AluOp), .in1(4'b0000), .out(multiplexer_10_out), .sel(or_1_out));
  Multiplexer #(.select(1), .width(1), .disabled("Z"), .enable("false")) multiplexer_11 (
    .in0(LHU), .in1(1'b0), .out(multiplexer_11_out), .sel(or_1_out));
  Multiplexer #(.select(1), .width(1), .disabled("Z"), .enable("false")) multiplexer_12 (
    .in0(AluSrcB), .in1(1'b0), .out(multiplexer_12_out), .sel(or_1_out));
  Multiplexer #(.select(1), .width(1), .disabled("Z"), .enable("false")) multiplexer_13 (
    .in0(BLTU), .in1(1'b0), .out(multiplexer_13_out), .sel(or_1_out));
  Multiplexer #(.select(1), .width(1), .disabled("Z"), .enable("false")) multiplexer_14 (
    .in0(RegWrie), .in1(1'b0), .out(multiplexer_14_out), .sel(or_1_out));
  Multiplexer #(.select(1), .width(1), .disabled("Z"), .enable("false")) multiplexer_15 (
    .in0(predictJump), .in1(1'b0), .out(multiplexer_15_out), .sel(or_1_out));
  Multiplexer #(.select(1), .width(1), .disabled("Z"), .enable("false")) multiplexer_16 (
    .in0(ecall), .in1(1'b0), .out(multiplexer_16_out), .sel(or_1_out));
  Multiplexer #(.select(1), .width(1), .disabled("Z"), .enable("false")) multiplexer_17 (
    .in0(uret), .in1(1'b0), .out(multiplexer_17_out), .sel(or_1_out));
  Multiplexer #(.select(1), .width(32), .disabled("Z"), .enable("false")) multiplexer_18 (
    .in0(R1), .in1({32{1'b0}}), .out(multiplexer_18_out), .sel(or_1_out));
  Multiplexer #(.select(1), .width(32), .disabled("Z"), .enable("false")) multiplexer_19 (
    .in0(R2), .in1({32{1'b0}}), .out(multiplexer_19_out), .sel(or_1_out));
  Multiplexer #(.select(1), .width(5), .disabled("Z"), .enable("false")) multiplexer_20 (
    .in0(rd), .in1({5{1'b0}}), .out(multiplexer_20_out), .sel(or_1_out));
  Multiplexer #(.select(1), .width(32), .disabled("Z"), .enable("false")) multiplexer_21 (
    .in0(imm1), .in1({32{1'b0}}), .out(multiplexer_21_out), .sel(or_1_out));
  Multiplexer #(.select(1), .width(32), .disabled("Z"), .enable("false")) multiplexer_22 (
    .in0(imm2), .in1({32{1'b0}}), .out(multiplexer_22_out), .sel(or_1_out));
  Multiplexer #(.select(1), .width(32), .disabled("Z"), .enable("false")) multiplexer_23 (
    .in0(IR), .in1({32{1'b0}}), .out(multiplexer_23_out), .sel(or_1_out));
  Multiplexer #(.select(1), .width(32), .disabled("Z"), .enable("false")) multiplexer_24 (
    .in0(PC), .in1({32{1'b0}}), .out(multiplexer_24_out), .sel(or_1_out));
  Multiplexer #(.select(1), .width(32), .disabled("Z"), .enable("false")) multiplexer_25 (
    .in0(PC_4), .in1({32{1'b0}}), .out(multiplexer_25_out), .sel(or_1_out));
  Multiplexer #(.select(1), .width(32), .disabled("Z"), .enable("false")) multiplexer_26 (
    .in0(imm_20), .in1({32{1'b0}}), .out(multiplexer_26_out), .sel(or_1_out));
  Multiplexer #(.select(1), .width(1), .disabled("Z"), .enable("false")) multiplexer_27 (
    .in0(isBubblet), .in1(1'b1), .out(multiplexer_27_out), .sel(flush));
  or or_1 (or_1_out, reset, flush);
  Register #(.width(32), .trigger("rising"), .Select("low")) register_1 (
    .D(multiplexer_23_out), .en(enable), .Q(IR_2), .clk(clk));  // open: clr
  Register #(.width(32), .trigger("rising"), .Select("low")) register_2 (
    .D(multiplexer_24_out), .en(enable), .Q(PC_2), .clk(clk));  // open: clr
  Register #(.width(1), .trigger("rising"), .Select("low")) register_3 (
    .D(multiplexer_1_out), .en(enable), .Q(Beq_2), .clk(clk));  // open: clr
  Register #(.width(2), .trigger("rising"), .Select("low")) register_4 (
    .D(multiplexer_2_out), .en(enable), .Q(rs1_redirect_2), .clk(clk));  // open: clr
  Register #(.width(2), .trigger("rising"), .Select("low")) register_5 (
    .D(multiplexer_3_out), .en(enable), .Q(rs2_redirect_2), .clk(clk));  // open: clr
  Register #(.width(1), .trigger("rising"), .Select("low")) register_6 (
    .D(multiplexer_4_out), .en(enable), .Q(JAL_2), .clk(clk));  // open: clr
  Register #(.width(1), .trigger("rising"), .Select("low")) register_7 (
    .D(multiplexer_5_out), .en(enable), .Q(Bne_2), .clk(clk));  // open: clr
  Register #(.width(1), .trigger("rising"), .Select("low")) register_8 (
    .D(multiplexer_6_out), .en(enable), .Q(JALR_2), .clk(clk));  // open: clr
  Register #(.width(1), .trigger("rising"), .Select("low")) register_9 (
    .D(multiplexer_7_out), .en(enable), .Q(MemToReg_2), .clk(clk));  // open: clr
  Register #(.width(1), .trigger("rising"), .Select("low")) register_10 (
    .D(multiplexer_8_out), .en(enable), .Q(AUIPC_2), .clk(clk));  // open: clr
  Register #(.width(1), .trigger("rising"), .Select("low")) register_11 (
    .D(multiplexer_9_out), .en(enable), .Q(MemWrite_2), .clk(clk));  // open: clr
  Register #(.width(4), .trigger("rising"), .Select("low")) register_12 (
    .D(multiplexer_10_out), .en(enable), .Q(AluOp_2), .clk(clk));  // open: clr
  Register #(.width(1), .trigger("rising"), .Select("low")) register_13 (
    .D(multiplexer_11_out), .en(enable), .Q(LHU_2), .clk(clk));  // open: clr
  Register #(.width(1), .trigger("rising"), .Select("low")) register_14 (
    .D(multiplexer_12_out), .en(enable), .Q(AluSrcB_2), .clk(clk));  // open: clr
  Register #(.width(1), .trigger("rising"), .Select("low")) register_15 (
    .D(multiplexer_13_out), .en(enable), .Q(BLTU_2), .clk(clk));  // open: clr
  Register #(.width(1), .trigger("rising"), .Select("low")) register_16 (
    .D(multiplexer_14_out), .en(enable), .Q(RegWrie_2), .clk(clk));  // open: clr
  Register #(.width(1), .trigger("rising"), .Select("low")) register_17 (
    .D(multiplexer_15_out), .en(enable), .Q(predictJump_2), .clk(clk));  // open: clr
  Register #(.width(1), .trigger("rising"), .Select("low")) register_18 (
    .D(multiplexer_16_out), .en(enable), .Q(ecall_2), .clk(clk));  // open: clr
  Register #(.width(1), .trigger("rising"), .Select("low")) register_19 (
    .D(multiplexer_17_out), .en(enable), .Q(uret_2), .clk(clk));  // open: clr
  Register #(.width(32), .trigger("rising"), .Select("low")) register_20 (
    .D(multiplexer_18_out), .en(enable), .Q(R1_2), .clk(clk));  // open: clr
  Register #(.width(32), .trigger("rising"), .Select("low")) register_21 (
    .D(multiplexer_19_out), .en(enable), .Q(R2_2), .clk(clk));  // open: clr
  Register #(.width(5), .trigger("rising"), .Select("low")) register_22 (
    .D(multiplexer_20_out), .en(enable), .Q(rd_2), .clk(clk));  // open: clr
  Register #(.width(32), .trigger("rising"), .Select("low")) register_23 (
    .D(multiplexer_21_out), .en(enable), .Q(imm1_2), .clk(clk));  // open: clr
  Register #(.width(32), .trigger("rising"), .Select("low")) register_24 (
    .D(multiplexer_22_out), .en(enable), .Q(imm2_2), .clk(clk));  // open: clr
  Register #(.width(32), .trigger("rising"), .Select("low")) register_25 (
    .D(multiplexer_25_out), .en(enable), .Q(PC_4_2), .clk(clk));  // open: clr
  Register #(.width(32), .trigger("rising"), .Select("low")) register_26 (
    .D(multiplexer_26_out), .en(enable), .Q(imm_20_2), .clk(clk));  // open: clr
  Register #(.width(1), .trigger("rising"), .Select("low")) register_27 (
    .D(multiplexer_27_out), .en(enable), .Q(isBubble), .clk(clk));  // open: clr
endmodule

module EX_MEM (
  input  JAL,
  input  JALR,
  input  MemToReg,
  input  AUIPC,
  input  MemWrite,
  input  LHU,
  input  RegWrie,
  input  halt,
  input  [31:0] ALUResult,
  input  [31:0] Write,
  input  [4:0] rd,
  input  [31:0] AUIPC_addr,
  input  [31:0] IR,
  input  [31:0] PC,
  input  [31:0] PC_4,
  input  reset,
  input  enable,
  input  clk,
  output JAL_2,
  output JALR_2,
  output MemToReg_2,
  output AUIPC_2,
  output MemWrite_2,
  output LHU_2,
  output RegWrie_2,
  output halt_2,
  output [31:0] ALUResult_2,
  output [31:0] Write_2,
  output [4:0] rd_2,
  output [31:0] AUIPC_addr_2,
  output [31:0] IR_2,
  output [31:0] PC_2,
  output [31:0] PC_4_2
);

  wire multiplexer_1_out, multiplexer_2_out, multiplexer_3_out, multiplexer_4_out, multiplexer_5_out,
       multiplexer_6_out, multiplexer_7_out, multiplexer_8_out;
  wire [4:0] multiplexer_11_out;
  wire [31:0] multiplexer_9_out, multiplexer_10_out, multiplexer_12_out, multiplexer_13_out,
       multiplexer_14_out, multiplexer_15_out;

  Multiplexer #(.select(1), .width(1), .disabled("Z"), .enable("false")) multiplexer_1 (
    .in0(JAL), .in1(1'b0), .out(multiplexer_1_out), .sel(reset));
  Multiplexer #(.select(1), .width(1), .disabled("Z"), .enable("false")) multiplexer_2 (
    .in0(JALR), .in1(1'b0), .out(multiplexer_2_out), .sel(reset));
  Multiplexer #(.select(1), .width(1), .disabled("Z"), .enable("false")) multiplexer_3 (
    .in0(MemToReg), .in1(1'b0), .out(multiplexer_3_out), .sel(reset));
  Multiplexer #(.select(1), .width(1), .disabled("Z"), .enable("false")) multiplexer_4 (
    .in0(AUIPC), .in1(1'b0), .out(multiplexer_4_out), .sel(reset));
  Multiplexer #(.select(1), .width(1), .disabled("Z"), .enable("false")) multiplexer_5 (
    .in0(MemWrite), .in1(1'b0), .out(multiplexer_5_out), .sel(reset));
  Multiplexer #(.select(1), .width(1), .disabled("Z"), .enable("false")) multiplexer_6 (
    .in0(LHU), .in1(1'b0), .out(multiplexer_6_out), .sel(reset));
  Multiplexer #(.select(1), .width(1), .disabled("Z"), .enable("false")) multiplexer_7 (
    .in0(RegWrie), .in1(1'b0), .out(multiplexer_7_out), .sel(reset));
  Multiplexer #(.select(1), .width(1), .disabled("Z"), .enable("false")) multiplexer_8 (
    .in0(halt), .in1(1'b0), .out(multiplexer_8_out), .sel(reset));
  Multiplexer #(.select(1), .width(32), .disabled("Z"), .enable("false")) multiplexer_9 (
    .in0(ALUResult), .in1({32{1'b0}}), .out(multiplexer_9_out), .sel(reset));
  Multiplexer #(.select(1), .width(32), .disabled("Z"), .enable("false")) multiplexer_10 (
    .in0(Write), .in1({32{1'b0}}), .out(multiplexer_10_out), .sel(reset));
  Multiplexer #(.select(1), .width(5), .disabled("Z"), .enable("false")) multiplexer_11 (
    .in0(rd), .in1({5{1'b0}}), .out(multiplexer_11_out), .sel(reset));
  Multiplexer #(.select(1), .width(32), .disabled("Z"), .enable("false")) multiplexer_12 (
    .in0(AUIPC_addr), .in1({32{1'b0}}), .out(multiplexer_12_out), .sel(reset));
  Multiplexer #(.select(1), .width(32), .disabled("Z"), .enable("false")) multiplexer_13 (
    .in0(IR), .in1({32{1'b0}}), .out(multiplexer_13_out), .sel(reset));
  Multiplexer #(.select(1), .width(32), .disabled("Z"), .enable("false")) multiplexer_14 (
    .in0(PC), .in1({32{1'b0}}), .out(multiplexer_14_out), .sel(reset));
  Multiplexer #(.select(1), .width(32), .disabled("Z"), .enable("false")) multiplexer_15 (
    .in0(PC_4), .in1({32{1'b0}}), .out(multiplexer_15_out), .sel(reset));
  Register #(.width(32), .trigger("rising"), .Select("low")) register_1 (
    .D(multiplexer_12_out), .en(enable), .Q(AUIPC_addr_2), .clk(clk));  // open: clr
  Register #(.width(32), .trigger("rising"), .Select("low")) register_2 (
    .D(multiplexer_13_out), .en(enable), .Q(IR_2), .clk(clk));  // open: clr
  Register #(.width(32), .trigger("rising"), .Select("low")) register_3 (
    .D(multiplexer_14_out), .en(enable), .Q(PC_2), .clk(clk));  // open: clr
  Register #(.width(1), .trigger("rising"), .Select("low")) register_4 (
    .D(multiplexer_1_out), .en(enable), .Q(JAL_2), .clk(clk));  // open: clr
  Register #(.width(1), .trigger("rising"), .Select("low")) register_5 (
    .D(multiplexer_2_out), .en(enable), .Q(JALR_2), .clk(clk));  // open: clr
  Register #(.width(1), .trigger("rising"), .Select("low")) register_6 (
    .D(multiplexer_3_out), .en(enable), .Q(MemToReg_2), .clk(clk));  // open: clr
  Register #(.width(1), .trigger("rising"), .Select("low")) register_7 (
    .D(multiplexer_4_out), .en(enable), .Q(AUIPC_2), .clk(clk));  // open: clr
  Register #(.width(1), .trigger("rising"), .Select("low")) register_8 (
    .D(multiplexer_5_out), .en(enable), .Q(MemWrite_2), .clk(clk));  // open: clr
  Register #(.width(1), .trigger("rising"), .Select("low")) register_9 (
    .D(multiplexer_6_out), .en(enable), .Q(LHU_2), .clk(clk));  // open: clr
  Register #(.width(1), .trigger("rising"), .Select("low")) register_10 (
    .D(multiplexer_7_out), .en(enable), .Q(RegWrie_2), .clk(clk));  // open: clr
  Register #(.width(1), .trigger("rising"), .Select("low")) register_11 (
    .D(multiplexer_8_out), .en(enable), .Q(halt_2), .clk(clk));  // open: clr
  Register #(.width(32), .trigger("rising"), .Select("low")) register_12 (
    .D(multiplexer_9_out), .en(enable), .Q(ALUResult_2), .clk(clk));  // open: clr
  Register #(.width(32), .trigger("rising"), .Select("low")) register_13 (
    .D(multiplexer_10_out), .en(enable), .Q(Write_2), .clk(clk));  // open: clr
  Register #(.width(5), .trigger("rising"), .Select("low")) register_14 (
    .D(multiplexer_11_out), .en(enable), .Q(rd_2), .clk(clk));  // open: clr
  Register #(.width(32), .trigger("rising"), .Select("low")) register_15 (
    .D(multiplexer_15_out), .en(enable), .Q(PC_4_2), .clk(clk));  // open: clr
endmodule

module MEM_WB (
  input  JAL,
  input  JALR,
  input  MemToReg,
  input  AUIPC,
  input  LHU,
  input  RegWrie,
  input  halt,
  input  [31:0] ALUResult,
  input  [31:0] ReadData,
  input  [4:0] rd,
  input  [31:0] AUIPC_addr,
  input  [31:0] IR,
  input  [31:0] PC,
  input  [31:0] PC_4,
  input  reset,
  input  enable,
  input  clk,
  output JAL_2,
  output JALR_2,
  output MemToReg_2,
  output AUIPC_2,
  output LHU_2,
  output RegWrie_2,
  output halt_2,
  output [31:0] ALUResult_2,
  output [31:0] ReadData_2,
  output [4:0] rd_2,
  output [31:0] AUIPC_addr_2,
  output [31:0] IR_2,
  output [31:0] PC_2,
  output [31:0] PC_4_2
);

  wire multiplexer_1_out, multiplexer_2_out, multiplexer_3_out, multiplexer_4_out, multiplexer_5_out,
       multiplexer_6_out, multiplexer_7_out;
  wire [4:0] multiplexer_10_out;
  wire [31:0] multiplexer_8_out, multiplexer_9_out, multiplexer_11_out, multiplexer_12_out,
       multiplexer_13_out, multiplexer_14_out;

  Multiplexer #(.select(1), .width(1), .disabled("Z"), .enable("false")) multiplexer_1 (
    .in0(JAL), .in1(1'b0), .out(multiplexer_1_out), .sel(reset));
  Multiplexer #(.select(1), .width(1), .disabled("Z"), .enable("false")) multiplexer_2 (
    .in0(JALR), .in1(1'b0), .out(multiplexer_2_out), .sel(reset));
  Multiplexer #(.select(1), .width(1), .disabled("Z"), .enable("false")) multiplexer_3 (
    .in0(MemToReg), .in1(1'b0), .out(multiplexer_3_out), .sel(reset));
  Multiplexer #(.select(1), .width(1), .disabled("Z"), .enable("false")) multiplexer_4 (
    .in0(AUIPC), .in1(1'b0), .out(multiplexer_4_out), .sel(reset));
  Multiplexer #(.select(1), .width(1), .disabled("Z"), .enable("false")) multiplexer_5 (
    .in0(LHU), .in1(1'b0), .out(multiplexer_5_out), .sel(reset));
  Multiplexer #(.select(1), .width(1), .disabled("Z"), .enable("false")) multiplexer_6 (
    .in0(RegWrie), .in1(1'b0), .out(multiplexer_6_out), .sel(reset));
  Multiplexer #(.select(1), .width(1), .disabled("Z"), .enable("false")) multiplexer_7 (
    .in0(halt), .in1(1'b0), .out(multiplexer_7_out), .sel(reset));
  Multiplexer #(.select(1), .width(32), .disabled("Z"), .enable("false")) multiplexer_8 (
    .in0(ALUResult), .in1({32{1'b0}}), .out(multiplexer_8_out), .sel(reset));
  Multiplexer #(.select(1), .width(32), .disabled("Z"), .enable("false")) multiplexer_9 (
    .in0(ReadData), .in1({32{1'b0}}), .out(multiplexer_9_out), .sel(reset));
  Multiplexer #(.select(1), .width(5), .disabled("Z"), .enable("false")) multiplexer_10 (
    .in0(rd), .in1({5{1'b0}}), .out(multiplexer_10_out), .sel(reset));
  Multiplexer #(.select(1), .width(32), .disabled("Z"), .enable("false")) multiplexer_11 (
    .in0(AUIPC_addr), .in1({32{1'b0}}), .out(multiplexer_11_out), .sel(reset));
  Multiplexer #(.select(1), .width(32), .disabled("Z"), .enable("false")) multiplexer_12 (
    .in0(IR), .in1({32{1'b0}}), .out(multiplexer_12_out), .sel(reset));
  Multiplexer #(.select(1), .width(32), .disabled("Z"), .enable("false")) multiplexer_13 (
    .in0(PC), .in1({32{1'b0}}), .out(multiplexer_13_out), .sel(reset));
  Multiplexer #(.select(1), .width(32), .disabled("Z"), .enable("false")) multiplexer_14 (
    .in0(PC_4), .in1({32{1'b0}}), .out(multiplexer_14_out), .sel(reset));
  Register #(.width(32), .trigger("rising"), .Select("low")) register_1 (
    .D(multiplexer_12_out), .en(enable), .Q(IR_2), .clk(clk));  // open: clr
  Register #(.width(32), .trigger("rising"), .Select("low")) register_2 (
    .D(multiplexer_13_out), .en(enable), .Q(PC_2), .clk(clk));  // open: clr
  Register #(.width(1), .trigger("rising"), .Select("low")) register_3 (
    .D(multiplexer_1_out), .en(enable), .Q(JAL_2), .clk(clk));  // open: clr
  Register #(.width(1), .trigger("rising"), .Select("low")) register_4 (
    .D(multiplexer_2_out), .en(enable), .Q(JALR_2), .clk(clk));  // open: clr
  Register #(.width(1), .trigger("rising"), .Select("low")) register_5 (
    .D(multiplexer_3_out), .en(enable), .Q(MemToReg_2), .clk(clk));  // open: clr
  Register #(.width(1), .trigger("rising"), .Select("low")) register_6 (
    .D(multiplexer_4_out), .en(enable), .Q(AUIPC_2), .clk(clk));  // open: clr
  Register #(.width(1), .trigger("rising"), .Select("low")) register_7 (
    .D(multiplexer_5_out), .en(enable), .Q(LHU_2), .clk(clk));  // open: clr
  Register #(.width(1), .trigger("rising"), .Select("low")) register_8 (
    .D(multiplexer_6_out), .en(enable), .Q(RegWrie_2), .clk(clk));  // open: clr
  Register #(.width(1), .trigger("rising"), .Select("low")) register_9 (
    .D(multiplexer_7_out), .en(enable), .Q(halt_2), .clk(clk));  // open: clr
  Register #(.width(32), .trigger("rising"), .Select("low")) register_10 (
    .D(multiplexer_8_out), .en(enable), .Q(ALUResult_2), .clk(clk));  // open: clr
  Register #(.width(32), .trigger("rising"), .Select("low")) register_11 (
    .D(multiplexer_9_out), .en(enable), .Q(ReadData_2), .clk(clk));  // open: clr
  Register #(.width(5), .trigger("rising"), .Select("low")) register_12 (
    .D(multiplexer_10_out), .en(enable), .Q(rd_2), .clk(clk));  // open: clr
  Register #(.width(32), .trigger("rising"), .Select("low")) register_13 (
    .D(multiplexer_11_out), .en(enable), .Q(AUIPC_addr_2), .clk(clk));  // open: clr
  Register #(.width(32), .trigger("rising"), .Select("low")) register_14 (
    .D(multiplexer_14_out), .en(enable), .Q(PC_4_2), .clk(clk));  // open: clr
endmodule

module R1_R2_used (
  input  OP2,
  input  OP3,
  input  OP4,
  input  OP5,
  input  OP6,
  input  F12,
  input  F13,
  input  F14,
  input  F25,
  input  F30,
  output R1_used,
  output R2_used
);

  wire and_1_out, and_2_out, and_3_out, and_4_out, and_5_out, and_6_out, and_7_out, and_8_out, and_9_out,
       and_10_out, and_11_out, and_12_out, and_13_out, and_14_out, and_15_out, and_16_out, and_17_out,
       and_18_out, and_19_out, and_20_out, and_21_out, and_22_out, and_23_out, and_24_out, and_25_out,
       and_26_out, and_27_out, and_28_out, and_29_out, and_30_out, and_31_out, and_32_out, and_33_out,
       not_1_out, not_2_out, not_3_out, not_4_out, not_5_out, not_6_out, not_7_out, not_8_out, not_9_out,
       not_10_out, not_11_out, not_12_out, not_13_out, not_14_out, not_15_out, not_16_out, not_17_out,
       not_18_out, not_19_out, not_20_out, not_21_out, not_22_out, not_23_out, not_24_out, not_25_out,
       not_26_out, not_27_out, not_28_out, not_29_out, not_30_out, not_31_out, not_32_out, not_33_out,
       not_34_out, not_35_out, not_36_out, not_37_out, not_38_out, not_39_out, not_40_out, not_41_out,
       not_42_out, not_43_out, not_44_out, not_45_out, not_46_out, not_47_out, not_48_out, not_49_out,
       not_50_out, not_51_out, not_52_out, not_53_out, not_54_out, not_55_out, not_56_out, not_57_out,
       not_58_out, not_59_out, not_60_out, not_61_out, not_62_out, not_63_out, not_64_out, not_65_out,
       not_66_out, not_67_out, not_68_out, not_69_out, not_70_out, not_71_out, not_72_out, not_73_out,
       not_74_out, not_75_out, not_76_out, not_77_out, not_78_out, not_79_out, not_80_out, not_81_out,
       not_82_out, not_83_out, not_84_out, not_85_out, not_86_out, not_87_out, not_88_out, not_89_out,
       not_90_out, not_91_out, not_92_out, not_93_out, not_94_out, not_95_out, not_96_out, not_97_out,
       not_98_out, not_99_out, not_100_out, not_101_out, not_102_out, not_103_out, not_104_out, not_105_out,
       not_106_out, not_107_out, not_108_out, not_109_out, not_110_out, not_111_out, not_112_out,
       not_113_out, not_114_out, not_115_out, not_116_out, not_117_out, not_118_out, not_119_out,
       not_120_out, not_121_out, not_122_out, not_123_out, not_124_out, not_125_out, not_126_out,
       not_127_out, not_128_out, not_129_out, not_130_out, not_131_out, not_132_out, not_133_out,
       not_134_out, not_135_out, not_136_out, not_137_out, not_138_out, not_139_out, not_140_out,
       not_141_out, not_142_out, not_143_out, not_144_out, not_145_out, not_146_out, not_147_out,
       not_148_out, not_149_out, not_150_out, not_151_out, not_152_out, not_153_out, not_154_out,
       not_155_out, not_156_out, not_157_out, not_158_out, not_159_out, not_160_out, not_161_out,
       not_162_out, not_163_out, not_164_out, not_165_out, not_166_out, not_167_out, not_168_out,
       not_169_out, not_170_out, not_171_out, not_172_out, not_173_out, not_174_out, not_175_out,
       not_176_out, not_177_out, not_178_out, not_179_out, not_180_out, not_181_out, not_182_out,
       not_183_out, not_184_out, not_185_out, not_186_out, not_187_out, not_188_out, not_189_out,
       not_190_out, not_191_out, not_192_out, not_193_out, not_194_out, not_195_out, not_196_out,
       not_197_out, not_198_out, not_199_out, not_200_out, not_201_out;

  not not_1 (not_1_out, F30);
  not not_2 (not_2_out, F25);
  not not_3 (not_3_out, F14);
  not not_4 (not_4_out, F13);
  not not_5 (not_5_out, F12);
  not not_6 (not_6_out, OP6);
  not not_7 (not_7_out, OP3);
  not not_8 (not_8_out, OP2);
  not not_9 (not_9_out, F25);
  not not_10 (not_10_out, F14);
  not not_11 (not_11_out, F13);
  not not_12 (not_12_out, F12);
  not not_13 (not_13_out, OP6);
  not not_14 (not_14_out, OP3);
  not not_15 (not_15_out, OP2);
  not not_16 (not_16_out, F30);
  not not_17 (not_17_out, F25);
  not not_18 (not_18_out, OP6);
  not not_19 (not_19_out, OP3);
  not not_20 (not_20_out, OP2);
  not not_21 (not_21_out, F30);
  not not_22 (not_22_out, F25);
  not not_23 (not_23_out, F12);
  not not_24 (not_24_out, OP6);
  not not_25 (not_25_out, OP3);
  not not_26 (not_26_out, OP2);
  not not_27 (not_27_out, F30);
  not not_28 (not_28_out, F25);
  not not_29 (not_29_out, F14);
  not not_30 (not_30_out, F12);
  not not_31 (not_31_out, OP6);
  not not_32 (not_32_out, OP3);
  not not_33 (not_33_out, OP2);
  not not_34 (not_34_out, F30);
  not not_35 (not_35_out, F25);
  not not_36 (not_36_out, F14);
  not not_37 (not_37_out, OP6);
  not not_38 (not_38_out, OP3);
  not not_39 (not_39_out, OP2);
  not not_40 (not_40_out, F14);
  not not_41 (not_41_out, F13);
  not not_42 (not_42_out, F12);
  not not_43 (not_43_out, OP6);
  not not_44 (not_44_out, OP5);
  not not_45 (not_45_out, OP3);
  not not_46 (not_46_out, OP2);
  not not_47 (not_47_out, OP6);
  not not_48 (not_48_out, OP5);
  not not_49 (not_49_out, OP3);
  not not_50 (not_50_out, OP2);
  not not_51 (not_51_out, F12);
  not not_52 (not_52_out, OP6);
  not not_53 (not_53_out, OP5);
  not not_54 (not_54_out, OP3);
  not not_55 (not_55_out, OP2);
  not not_56 (not_56_out, F13);
  not not_57 (not_57_out, F12);
  not not_58 (not_58_out, OP6);
  not not_59 (not_59_out, OP5);
  not not_60 (not_60_out, OP3);
  not not_61 (not_61_out, OP2);
  not not_62 (not_62_out, F14);
  not not_63 (not_63_out, F12);
  not not_64 (not_64_out, OP6);
  not not_65 (not_65_out, OP5);
  not not_66 (not_66_out, OP3);
  not not_67 (not_67_out, OP2);
  not not_68 (not_68_out, F30);
  not not_69 (not_69_out, F25);
  not not_70 (not_70_out, F14);
  not not_71 (not_71_out, F13);
  not not_72 (not_72_out, OP6);
  not not_73 (not_73_out, OP5);
  not not_74 (not_74_out, OP3);
  not not_75 (not_75_out, OP2);
  not not_76 (not_76_out, F30);
  not not_77 (not_77_out, F25);
  not not_78 (not_78_out, F13);
  not not_79 (not_79_out, OP6);
  not not_80 (not_80_out, OP5);
  not not_81 (not_81_out, OP3);
  not not_82 (not_82_out, OP2);
  not not_83 (not_83_out, F25);
  not not_84 (not_84_out, F13);
  not not_85 (not_85_out, OP6);
  not not_86 (not_86_out, OP5);
  not not_87 (not_87_out, OP3);
  not not_88 (not_88_out, OP2);
  not not_89 (not_89_out, F14);
  not not_90 (not_90_out, F12);
  not not_91 (not_91_out, OP6);
  not not_92 (not_92_out, OP5);
  not not_93 (not_93_out, OP4);
  not not_94 (not_94_out, OP3);
  not not_95 (not_95_out, OP2);
  not not_96 (not_96_out, F14);
  not not_97 (not_97_out, F12);
  not not_98 (not_98_out, OP6);
  not not_99 (not_99_out, OP4);
  not not_100 (not_100_out, OP3);
  not not_101 (not_101_out, OP2);
  not not_102 (not_102_out, F14);
  not not_103 (not_103_out, F13);
  not not_104 (not_104_out, F12);
  not not_105 (not_105_out, OP4);
  not not_106 (not_106_out, OP3);
  not not_107 (not_107_out, OP2);
  not not_108 (not_108_out, F14);
  not not_109 (not_109_out, F13);
  not not_110 (not_110_out, OP4);
  not not_111 (not_111_out, OP3);
  not not_112 (not_112_out, OP2);
  not not_113 (not_113_out, F14);
  not not_114 (not_114_out, F13);
  not not_115 (not_115_out, F12);
  not not_116 (not_116_out, OP4);
  not not_117 (not_117_out, OP3);
  not not_118 (not_118_out, F30);
  not not_119 (not_119_out, F25);
  not not_120 (not_120_out, F13);
  not not_121 (not_121_out, F12);
  not not_122 (not_122_out, OP6);
  not not_123 (not_123_out, OP3);
  not not_124 (not_124_out, OP2);
  not not_125 (not_125_out, F13);
  not not_126 (not_126_out, OP6);
  not not_127 (not_127_out, OP5);
  not not_128 (not_128_out, OP4);
  not not_129 (not_129_out, OP3);
  not not_130 (not_130_out, OP2);
  not not_131 (not_131_out, F12);
  not not_132 (not_132_out, OP4);
  not not_133 (not_133_out, OP3);
  not not_134 (not_134_out, OP2);
  not not_135 (not_135_out, F30);
  not not_136 (not_136_out, F25);
  not not_137 (not_137_out, F14);
  not not_138 (not_138_out, F13);
  not not_139 (not_139_out, F12);
  not not_140 (not_140_out, OP6);
  not not_141 (not_141_out, OP3);
  not not_142 (not_142_out, OP2);
  not not_143 (not_143_out, F25);
  not not_144 (not_144_out, F14);
  not not_145 (not_145_out, F13);
  not not_146 (not_146_out, F12);
  not not_147 (not_147_out, OP6);
  not not_148 (not_148_out, OP3);
  not not_149 (not_149_out, OP2);
  not not_150 (not_150_out, F30);
  not not_151 (not_151_out, F25);
  not not_152 (not_152_out, OP6);
  not not_153 (not_153_out, OP3);
  not not_154 (not_154_out, OP2);
  not not_155 (not_155_out, F30);
  not not_156 (not_156_out, F25);
  not not_157 (not_157_out, F12);
  not not_158 (not_158_out, OP6);
  not not_159 (not_159_out, OP3);
  not not_160 (not_160_out, OP2);
  not not_161 (not_161_out, F30);
  not not_162 (not_162_out, F25);
  not not_163 (not_163_out, F14);
  not not_164 (not_164_out, F12);
  not not_165 (not_165_out, OP6);
  not not_166 (not_166_out, OP3);
  not not_167 (not_167_out, OP2);
  not not_168 (not_168_out, F30);
  not not_169 (not_169_out, F25);
  not not_170 (not_170_out, F14);
  not not_171 (not_171_out, OP6);
  not not_172 (not_172_out, OP3);
  not not_173 (not_173_out, OP2);
  not not_174 (not_174_out, F14);
  not not_175 (not_175_out, F12);
  not not_176 (not_176_out, OP6);
  not not_177 (not_177_out, OP4);
  not not_178 (not_178_out, OP3);
  not not_179 (not_179_out, OP2);
  not not_180 (not_180_out, F14);
  not not_181 (not_181_out, F13);
  not not_182 (not_182_out, F12);
  not not_183 (not_183_out, OP4);
  not not_184 (not_184_out, OP3);
  not not_185 (not_185_out, OP2);
  not not_186 (not_186_out, F14);
  not not_187 (not_187_out, F13);
  not not_188 (not_188_out, OP4);
  not not_189 (not_189_out, OP3);
  not not_190 (not_190_out, OP2);
  not not_191 (not_191_out, F30);
  not not_192 (not_192_out, F25);
  not not_193 (not_193_out, F13);
  not not_194 (not_194_out, F12);
  not not_195 (not_195_out, OP6);
  not not_196 (not_196_out, OP3);
  not not_197 (not_197_out, OP2);
  not not_198 (not_198_out, F12);
  not not_199 (not_199_out, OP4);
  not not_200 (not_200_out, OP3);
  not not_201 (not_201_out, OP2);
  and and_1 (and_1_out, not_1_out, not_2_out, not_3_out, not_4_out, not_5_out, not_6_out, OP5, OP4, not_7_out, not_8_out);
  and and_2 (and_2_out, F30, not_9_out, not_10_out, not_11_out, not_12_out, not_13_out, OP5, OP4, not_14_out, not_15_out);
  and and_3 (and_3_out, not_16_out, not_17_out, F14, F13, F12, not_18_out, OP5, OP4, not_19_out, not_20_out);
  and and_4 (and_4_out, not_21_out, not_22_out, F14, F13, not_23_out, not_24_out, OP5, OP4, not_25_out, not_26_out);
  and and_5 (and_5_out, not_27_out, not_28_out, not_29_out, F13, not_30_out, not_31_out, OP5, OP4, not_32_out, not_33_out);
  and and_6 (and_6_out, not_34_out, not_35_out, not_36_out, F13, F12, not_37_out, OP5, OP4, not_38_out, not_39_out);
  and and_7 (and_7_out, not_40_out, not_41_out, not_42_out, not_43_out, not_44_out, OP4, not_45_out, not_46_out);
  and and_8 (and_8_out, F14, F13, F12, not_47_out, not_48_out, OP4, not_49_out, not_50_out);
  and and_9 (and_9_out, F14, F13, not_51_out, not_52_out, not_53_out, OP4, not_54_out, not_55_out);
  and and_10 (and_10_out, F14, not_56_out, not_57_out, not_58_out, not_59_out, OP4, not_60_out, not_61_out);
  and and_11 (and_11_out, not_62_out, F13, not_63_out, not_64_out, not_65_out, OP4, not_66_out, not_67_out);
  and and_12 (and_12_out, not_68_out, not_69_out, not_70_out, not_71_out, F12, not_72_out, not_73_out, OP4, not_74_out, not_75_out);
  and and_13 (and_13_out, not_76_out, not_77_out, F14, not_78_out, F12, not_79_out, not_80_out, OP4, not_81_out, not_82_out);
  and and_14 (and_14_out, F30, not_83_out, F14, not_84_out, F12, not_85_out, not_86_out, OP4, not_87_out, not_88_out);
  and and_15 (and_15_out, not_89_out, F13, not_90_out, not_91_out, not_92_out, not_93_out, not_94_out, not_95_out);
  and and_16 (and_16_out, not_96_out, F13, not_97_out, not_98_out, OP5, not_99_out, not_100_out, not_101_out);
  and and_17 (and_17_out, not_102_out, not_103_out, not_104_out, OP6, OP5, not_105_out, not_106_out, not_107_out);
  and and_18 (and_18_out, not_108_out, not_109_out, F12, OP6, OP5, not_110_out, not_111_out, not_112_out);
  and and_19 (and_19_out, not_113_out, not_114_out, not_115_out, OP6, OP5, not_116_out, not_117_out, OP2);
  and and_20 (and_20_out, not_118_out, not_119_out, F14, not_120_out, not_121_out, not_122_out, OP5, OP4, not_123_out, not_124_out);
  and and_21 (and_21_out, F14, not_125_out, F12, not_126_out, not_127_out, not_128_out, not_129_out, not_130_out);
  and and_22 (and_22_out, F14, F13, not_131_out, OP6, OP5, not_132_out, not_133_out, not_134_out);
  and and_23 (and_23_out, not_135_out, not_136_out, not_137_out, not_138_out, not_139_out, not_140_out, OP5, OP4, not_141_out, not_142_out);
  and and_24 (and_24_out, F30, not_143_out, not_144_out, not_145_out, not_146_out, not_147_out, OP5, OP4, not_148_out, not_149_out);
  and and_25 (and_25_out, not_150_out, not_151_out, F14, F13, F12, not_152_out, OP5, OP4, not_153_out, not_154_out);
  and and_26 (and_26_out, not_155_out, not_156_out, F14, F13, not_157_out, not_158_out, OP5, OP4, not_159_out, not_160_out);
  and and_27 (and_27_out, not_161_out, not_162_out, not_163_out, F13, not_164_out, not_165_out, OP5, OP4, not_166_out, not_167_out);
  and and_28 (and_28_out, not_168_out, not_169_out, not_170_out, F13, F12, not_171_out, OP5, OP4, not_172_out, not_173_out);
  and and_29 (and_29_out, not_174_out, F13, not_175_out, not_176_out, OP5, not_177_out, not_178_out, not_179_out);
  and and_30 (and_30_out, not_180_out, not_181_out, not_182_out, OP6, OP5, not_183_out, not_184_out, not_185_out);
  and and_31 (and_31_out, not_186_out, not_187_out, F12, OP6, OP5, not_188_out, not_189_out, not_190_out);
  and and_32 (and_32_out, not_191_out, not_192_out, F14, not_193_out, not_194_out, not_195_out, OP5, OP4, not_196_out, not_197_out);
  and and_33 (and_33_out, F14, F13, not_198_out, OP6, OP5, not_199_out, not_200_out, not_201_out);
  or or_1 (R2_used, and_23_out, and_24_out, and_25_out, and_26_out, and_27_out, and_28_out, and_29_out, and_30_out, and_31_out, and_32_out, and_33_out);
  or or_2 (R1_used, and_1_out, and_2_out, and_3_out, and_4_out, and_5_out, and_6_out, and_7_out, and_8_out, and_9_out, and_10_out, and_11_out, and_12_out, and_13_out, and_14_out, and_15_out, and_16_out, and_17_out, and_18_out, and_19_out, and_20_out, and_21_out, and_22_out);
endmodule

module data_check (
  input  [4:0] rs1,
  input  EX_RegWrite,
  input  ecall,
  input  [4:0] rs2,
  input  MEM_RegWrite,
  input  [4:0] EX_rd,
  input  rs1_used,
  input  rs2_used,
  input  [4:0] MEM_rd,
  output hazzard
);

  wire and_1_out, and_2_out, and_3_out, and_4_out, and_5_out, and_6_out, comparator_1_eq, comparator_2_eq,
       comparator_3_eq, comparator_4_eq, comparator_5_eq, comparator_6_eq, comparator_7_eq, comparator_8_eq,
       comparator_9_eq, comparator_10_eq, comparator_11_eq, comparator_12_eq, or_1_out, or_2_out;

  Comparator #(.width(5), .mode("twosComplement")) comparator_1 (
    .a(5'b01010), .b(EX_rd), .eq(comparator_1_eq));  // open: gt, lt
  Comparator #(.width(5), .mode("twosComplement")) comparator_2 (
    .a(EX_rd), .b(5'b10001), .eq(comparator_2_eq));  // open: gt, lt
  Comparator #(.width(5), .mode("twosComplement")) comparator_3 (
    .a(5'b01010), .b(MEM_rd), .eq(comparator_3_eq));  // open: gt, lt
  Comparator #(.width(5), .mode("twosComplement")) comparator_4 (
    .a(MEM_rd), .b(5'b10001), .eq(comparator_4_eq));  // open: gt, lt
  Comparator #(.width(5), .mode("twosComplement")) comparator_5 (
    .a({5{1'b0}}), .b(rs1), .eq(comparator_5_eq));  // open: gt, lt
  Comparator #(.width(5), .mode("twosComplement")) comparator_6 (
    .a(rs1), .b(EX_rd), .eq(comparator_6_eq));  // open: gt, lt
  Comparator #(.width(5), .mode("twosComplement")) comparator_7 (
    .a({5{1'b0}}), .b(rs2), .eq(comparator_7_eq));  // open: gt, lt
  Comparator #(.width(5), .mode("twosComplement")) comparator_8 (
    .a(rs2), .b(EX_rd), .eq(comparator_8_eq));  // open: gt, lt
  Comparator #(.width(5), .mode("twosComplement")) comparator_9 (
    .a({5{1'b0}}), .b(rs1), .eq(comparator_9_eq));  // open: gt, lt
  Comparator #(.width(5), .mode("twosComplement")) comparator_10 (
    .a(rs1), .b(MEM_rd), .eq(comparator_10_eq));  // open: gt, lt
  Comparator #(.width(5), .mode("twosComplement")) comparator_11 (
    .a({5{1'b0}}), .b(rs2), .eq(comparator_11_eq));  // open: gt, lt
  Comparator #(.width(5), .mode("twosComplement")) comparator_12 (
    .a(rs2), .b(MEM_rd), .eq(comparator_12_eq));  // open: gt, lt
  or or_1 (or_1_out, comparator_1_eq, comparator_2_eq);
  or or_2 (or_2_out, comparator_3_eq, comparator_4_eq);
  and and_1 (and_1_out, ~comparator_5_eq, comparator_6_eq, EX_RegWrite, rs1_used);  // AND_Gate
  and and_2 (and_2_out, ~comparator_7_eq, comparator_8_eq, EX_RegWrite, rs2_used);  // AND_Gate
  and and_3 (and_3_out, ~comparator_9_eq, comparator_10_eq, MEM_RegWrite, rs1_used);  // AND_Gate
  and and_4 (and_4_out, ~comparator_11_eq, comparator_12_eq, MEM_RegWrite, rs2_used);  // AND_Gate
  and and_5 (and_5_out, ecall, EX_RegWrite, or_1_out);
  and and_6 (and_6_out, ecall, MEM_RegWrite, or_2_out);
  or or_3 (hazzard, and_1_out, and_2_out, and_3_out, and_4_out, and_5_out, and_6_out);
endmodule

module redirect (
  input  [4:0] rs1,
  input  EX_RegWrite,
  input  ecall,
  input  [4:0] rs2,
  input  MEM_RegWrite,
  input  EX_MemToReg,
  input  [4:0] EX_rd,
  input  rs1_used,
  input  rs2_used,
  input  [4:0] MEM_rd,
  output loadUse,
  output [1:0] rs1_redirect,
  output [1:0] rs2_redirect
);

  wire and_1_out, and_2_out, and_3_out, and_4_out, and_5_out, and_6_out, and_7_out, and_8_out, and_11_out,
       and_12_out, comparator_1_eq, comparator_2_eq, comparator_3_eq, comparator_4_eq, comparator_5_eq,
       comparator_6_eq, comparator_7_eq, comparator_8_eq, comparator_9_eq, comparator_10_eq,
       comparator_11_eq, comparator_12_eq, comparator_13_eq, comparator_14_eq, comparator_15_eq,
       comparator_16_eq, not_1_out, not_2_out, or_2_out, or_4_out;

  Comparator #(.width(5), .mode("twosComplement")) comparator_1 (
    .a({5{1'b0}}), .b(rs1), .eq(comparator_1_eq));  // open: gt, lt
  Comparator #(.width(5), .mode("twosComplement")) comparator_2 (
    .a(rs1), .b(EX_rd), .eq(comparator_2_eq));  // open: gt, lt
  Comparator #(.width(5), .mode("twosComplement")) comparator_3 (
    .a({5{1'b0}}), .b(rs1), .eq(comparator_3_eq));  // open: gt, lt
  Comparator #(.width(5), .mode("twosComplement")) comparator_4 (
    .a(rs1), .b(MEM_rd), .eq(comparator_4_eq));  // open: gt, lt
  Comparator #(.width(5), .mode("twosComplement")) comparator_5 (
    .a({5{1'b0}}), .b(rs2), .eq(comparator_5_eq));  // open: gt, lt
  Comparator #(.width(5), .mode("twosComplement")) comparator_6 (
    .a(rs2), .b(EX_rd), .eq(comparator_6_eq));  // open: gt, lt
  Comparator #(.width(5), .mode("twosComplement")) comparator_7 (
    .a({5{1'b0}}), .b(rs2), .eq(comparator_7_eq));  // open: gt, lt
  Comparator #(.width(5), .mode("twosComplement")) comparator_8 (
    .a(rs2), .b(MEM_rd), .eq(comparator_8_eq));  // open: gt, lt
  and and_1 (and_1_out, ~comparator_1_eq, comparator_2_eq, EX_RegWrite, rs1_used);  // AND_Gate
  and and_2 (and_2_out, ~comparator_3_eq, comparator_4_eq, MEM_RegWrite, rs1_used);  // AND_Gate
  and and_3 (and_3_out, ~comparator_5_eq, comparator_6_eq, EX_RegWrite, rs2_used);  // AND_Gate
  and and_4 (and_4_out, ~comparator_7_eq, comparator_8_eq, MEM_RegWrite, rs2_used);  // AND_Gate
  Comparator #(.width(5), .mode("twosComplement")) comparator_9 (
    .a(EX_rd), .b(5'b10001), .eq(comparator_9_eq));  // open: gt, lt
  Comparator #(.width(5), .mode("twosComplement")) comparator_10 (
    .a(5'b10001), .b(MEM_rd), .eq(comparator_10_eq));  // open: gt, lt
  Comparator #(.width(5), .mode("twosComplement")) comparator_11 (
    .a(5'b01010), .b(EX_rd), .eq(comparator_11_eq));  // open: gt, lt
  and and_5 (and_5_out, ecall, EX_RegWrite, comparator_9_eq);
  Comparator #(.width(5), .mode("twosComplement")) comparator_12 (
    .a(5'b01010), .b(MEM_rd), .eq(comparator_12_eq));  // open: gt, lt
  and and_6 (and_6_out, ecall, MEM_RegWrite, comparator_10_eq);
  and and_7 (and_7_out, ecall, EX_RegWrite, comparator_11_eq);
  and and_8 (and_8_out, ecall, MEM_RegWrite, comparator_12_eq);
  or or_1 (rs1_redirect[1], and_1_out, and_5_out);
  or or_2 (or_2_out, and_2_out, and_6_out);
  or or_3 (rs2_redirect[1], and_3_out, and_7_out);
  or or_4 (or_4_out, and_4_out, and_8_out);
  and and_9 (rs1_redirect[0], ~rs1_redirect[1], or_2_out);  // AND_Gate
  and and_10 (rs2_redirect[0], ~rs2_redirect[1], or_4_out);  // AND_Gate
  Comparator #(.width(5), .mode("twosComplement")) comparator_13 (
    .a({5{1'b0}}), .b(rs1), .eq(comparator_13_eq));  // open: gt, lt
  not not_1 (not_1_out, comparator_13_eq);
  Comparator #(.width(5), .mode("twosComplement")) comparator_14 (
    .a(rs1), .b(EX_rd), .eq(comparator_14_eq));  // open: gt, lt
  Comparator #(.width(5), .mode("twosComplement")) comparator_15 (
    .a(EX_rd), .b(rs2), .eq(comparator_15_eq));  // open: gt, lt
  Comparator #(.width(5), .mode("twosComplement")) comparator_16 (
    .a(rs2), .b({5{1'b0}}), .eq(comparator_16_eq));  // open: gt, lt
  not not_2 (not_2_out, comparator_16_eq);
  and and_11 (and_11_out, rs1_used, not_1_out, comparator_14_eq, EX_MemToReg);
  and and_12 (and_12_out, EX_MemToReg, comparator_15_eq, not_2_out, rs2_used);
  or or_5 (loadUse, and_11_out, and_12_out);
endmodule

module \中断相关指令  (
  input  OP2,
  input  OP3,
  input  OP4,
  input  OP5,
  input  OP6,
  input  F12,
  input  F13,
  input  F14,
  input  F25,
  input  F30,
  output CSRRSI,
  output CSRRCI
);

  wire not_1_out, not_2_out, not_3_out, not_4_out, not_5_out;

  not not_1 (not_1_out, F12);
  not not_2 (not_2_out, OP3);
  not not_3 (not_3_out, OP2);
  not not_4 (not_4_out, OP3);
  not not_5 (not_5_out, OP2);
  and and_1 (CSRRSI, F14, F13, not_1_out, OP6, OP5, OP4, not_2_out, not_3_out);
  and and_2 (CSRRCI, F14, F13, F12, OP6, OP5, OP4, not_4_out, not_5_out);
endmodule

module BTB (
  input  clk,
  input  [31:0] EX_PC,
  input  [31:0] PC,
  input  EX_branch,
  input  [31:0] EX_BranchAddr,
  input  EX_BranchTaken,
  output PredictJump,
  output [31:0] JumpAddr
);

  wire and_17_out, and_18_out, and_19_out, and_20_out, and_21_out, and_22_out, and_23_out, and_24_out,
       comparator_1_eq, comparator_2_eq, comparator_3_eq, comparator_4_eq, comparator_5_eq, comparator_6_eq,
       comparator_7_eq, comparator_8_eq, comparator_9_eq, comparator_10_eq, comparator_11_eq,
       comparator_12_eq, comparator_13_eq, comparator_14_eq, comparator_15_eq, comparator_16_eq, d_ff_1_q,
       d_ff_2_q, d_ff_3_q, d_ff_4_q, d_ff_5_q, d_ff_6_q, d_ff_7_q, d_ff_8_q, decoder_1_out0, decoder_1_out1,
       decoder_1_out2, decoder_1_out3, decoder_1_out4, decoder_1_out5, decoder_1_out6, decoder_1_out7,
       decoder_2_out0, decoder_2_out1, decoder_2_out2, decoder_2_out3, decoder_2_out4, decoder_2_out5,
       decoder_2_out6, decoder_2_out7, Hit, hit0, hit1, hit2, hit3, hit4, hit5, hit6, hit7, isFull, L0, L1,
       L2, L3, L4, L5, L6, L7, Miss, not_1_out, not_2_out, not_3_out, not_4_out, not_5_out, not_6_out,
       not_7_out, not_8_out, or_1_out, or_2_out, or_3_out, or_4_out, or_5_out, or_6_out, or_7_out, or_8_out,
       or_9_out, or_10_out, or_11_out, or_12_out, or_13_out, or_14_out, or_15_out, or_16_out,
       priority_encoder_1_gs, v0, v1, v2, v3, v4, v5, v6, v7, w0, w1, w2, w3, w4, w5, w6, w7;
  wire [1:0] fsm_1_nextlow, fsm_2_nextlow, fsm_3_nextlow, fsm_4_nextlow, fsm_5_nextlow, fsm_6_nextlow,
       fsm_7_nextlow, fsm_8_nextlow, predict0, predict1, predict2, predict3, predict4, predict5, predict6,
       predict7;
  wire [2:0] LRUIndex, max_1_maxindex, max_2_maxindex, max_3_maxindex, max_4_maxindex, max_5_maxindex,
       max_7_maxindex, priority_encoder_1_out;
  wire [15:0] c0, c1, c2, c3, c4, c5, c6, c7, max_1_max, max_2_max, max_3_max, max_4_max, max_5_max,
       max_7_max;
  wire [31:0] EX_PC0, EX_PC1, EX_PC2, EX_PC3, EX_PC4, EX_PC5, EX_PC6, EX_PC7, register_17_q, register_18_q,
       register_19_q, register_20_q, register_21_q, register_22_q, register_23_q, register_24_q;

  Register #(.width(1), .trigger("rising"), .Select("low")) register_1 (
    .D(1'b1), .en(w2), .Q(v2), .clk(clk));  // open: clr
  Register #(.width(1), .trigger("rising"), .Select("low")) register_2 (
    .D(1'b1), .en(w3), .Q(v3), .clk(clk));  // open: clr
  Register #(.width(1), .trigger("rising"), .Select("low")) register_3 (
    .D(1'b1), .en(w6), .Q(v6), .clk(clk));  // open: clr
  Register #(.width(1), .trigger("rising"), .Select("low")) register_4 (
    .D(1'b1), .en(w7), .Q(v7), .clk(clk));  // open: clr
  Register #(.width(1), .trigger("rising"), .Select("low")) register_5 (
    .D(1'b1), .en(w0), .Q(v0), .clk(clk));  // open: clr
  Register #(.width(1), .trigger("rising"), .Select("low")) register_6 (
    .D(1'b1), .en(w1), .Q(v1), .clk(clk));  // open: clr
  Register #(.width(1), .trigger("rising"), .Select("low")) register_7 (
    .D(1'b1), .en(w4), .Q(v4), .clk(clk));  // open: clr
  Register #(.width(1), .trigger("rising"), .Select("low")) register_8 (
    .D(1'b1), .en(w5), .Q(v5), .clk(clk));  // open: clr
  Register #(.width(32), .trigger("rising"), .Select("low")) register_9 (
    .D(EX_PC), .en(w0), .Q(EX_PC0), .clk(clk));  // open: clr
  Register #(.width(32), .trigger("rising"), .Select("low")) register_10 (
    .D(EX_PC), .en(w1), .Q(EX_PC1), .clk(clk));  // open: clr
  Register #(.width(32), .trigger("rising"), .Select("low")) register_11 (
    .D(EX_PC), .en(w2), .Q(EX_PC2), .clk(clk));  // open: clr
  Register #(.width(32), .trigger("rising"), .Select("low")) register_12 (
    .D(EX_PC), .en(w3), .Q(EX_PC3), .clk(clk));  // open: clr
  Register #(.width(32), .trigger("rising"), .Select("low")) register_13 (
    .D(EX_PC), .en(w4), .Q(EX_PC4), .clk(clk));  // open: clr
  Register #(.width(32), .trigger("rising"), .Select("low")) register_14 (
    .D(EX_PC), .en(w5), .Q(EX_PC5), .clk(clk));  // open: clr
  Register #(.width(32), .trigger("rising"), .Select("low")) register_15 (
    .D(EX_PC), .en(w6), .Q(EX_PC6), .clk(clk));  // open: clr
  Register #(.width(32), .trigger("rising"), .Select("low")) register_16 (
    .D(EX_PC), .en(w7), .Q(EX_PC7), .clk(clk));  // open: clr
  Counter #(.width(16), .max('hffff), .ongoal("wrap"), .trigger("rising"), .behavior("new")) counter_1 (
    .Q(c0), .clk(clk), .clr(d_ff_1_q));  // open: load, D, count, carry, preset, down
  D_Flip_Flop #(.trigger("rising"), .Pre_Clr_Positions("ABOVE_BELOW"), .NegatePresetClear("false"), .enable("false"), .NewFFLayout("false")) d_ff_1 (
    .clk(clk), .D(or_1_out), .Q(d_ff_1_q));  // open: Qn, preset, reset
  or or_1 (or_1_out, w0, L0);
  Counter #(.width(16), .max('hffff), .ongoal("wrap"), .trigger("rising"), .behavior("new")) counter_2 (
    .Q(c1), .clk(clk), .clr(d_ff_2_q));  // open: load, D, count, carry, preset, down
  D_Flip_Flop #(.trigger("rising"), .Pre_Clr_Positions("ABOVE_BELOW"), .NegatePresetClear("false"), .enable("false"), .NewFFLayout("false")) d_ff_2 (
    .clk(clk), .D(or_2_out), .Q(d_ff_2_q));  // open: Qn, preset, reset
  or or_2 (or_2_out, w1, L1);
  Counter #(.width(16), .max('hffff), .ongoal("wrap"), .trigger("rising"), .behavior("new")) counter_3 (
    .Q(c2), .clk(clk), .clr(d_ff_3_q));  // open: load, D, count, carry, preset, down
  D_Flip_Flop #(.trigger("rising"), .Pre_Clr_Positions("ABOVE_BELOW"), .NegatePresetClear("false"), .enable("false"), .NewFFLayout("false")) d_ff_3 (
    .clk(clk), .D(or_3_out), .Q(d_ff_3_q));  // open: Qn, preset, reset
  or or_3 (or_3_out, w2, L2);
  Counter #(.width(16), .max('hffff), .ongoal("wrap"), .trigger("rising"), .behavior("new")) counter_4 (
    .Q(c3), .clk(clk), .clr(d_ff_4_q));  // open: load, D, count, carry, preset, down
  D_Flip_Flop #(.trigger("rising"), .Pre_Clr_Positions("ABOVE_BELOW"), .NegatePresetClear("false"), .enable("false"), .NewFFLayout("false")) d_ff_4 (
    .clk(clk), .D(or_4_out), .Q(d_ff_4_q));  // open: Qn, preset, reset
  or or_4 (or_4_out, w3, L3);
  Counter #(.width(16), .max('hffff), .ongoal("wrap"), .trigger("rising"), .behavior("new")) counter_5 (
    .Q(c4), .clk(clk), .clr(d_ff_5_q));  // open: load, D, count, carry, preset, down
  D_Flip_Flop #(.trigger("rising"), .Pre_Clr_Positions("ABOVE_BELOW"), .NegatePresetClear("false"), .enable("false"), .NewFFLayout("false")) d_ff_5 (
    .clk(clk), .D(or_5_out), .Q(d_ff_5_q));  // open: Qn, preset, reset
  or or_5 (or_5_out, w4, L4);
  Counter #(.width(16), .max('hffff), .ongoal("wrap"), .trigger("rising"), .behavior("new")) counter_6 (
    .Q(c5), .clk(clk), .clr(d_ff_6_q));  // open: load, D, count, carry, preset, down
  D_Flip_Flop #(.trigger("rising"), .Pre_Clr_Positions("ABOVE_BELOW"), .NegatePresetClear("false"), .enable("false"), .NewFFLayout("false")) d_ff_6 (
    .clk(clk), .D(or_6_out), .Q(d_ff_6_q));  // open: Qn, preset, reset
  or or_6 (or_6_out, w5, L5);
  Counter #(.width(16), .max('hffff), .ongoal("wrap"), .trigger("rising"), .behavior("new")) counter_7 (
    .Q(c6), .clk(clk), .clr(d_ff_7_q));  // open: load, D, count, carry, preset, down
  D_Flip_Flop #(.trigger("rising"), .Pre_Clr_Positions("ABOVE_BELOW"), .NegatePresetClear("false"), .enable("false"), .NewFFLayout("false")) d_ff_7 (
    .clk(clk), .D(or_7_out), .Q(d_ff_7_q));  // open: Qn, preset, reset
  or or_7 (or_7_out, w6, L6);
  Counter #(.width(16), .max('hffff), .ongoal("wrap"), .trigger("rising"), .behavior("new")) counter_8 (
    .Q(c7), .clk(clk), .clr(d_ff_8_q));  // open: load, D, count, carry, preset, down
  D_Flip_Flop #(.trigger("rising"), .Pre_Clr_Positions("ABOVE_BELOW"), .NegatePresetClear("false"), .enable("false"), .NewFFLayout("false")) d_ff_8 (
    .clk(clk), .D(or_8_out), .Q(d_ff_8_q));  // open: Qn, preset, reset
  or or_8 (or_8_out, w7, L7);
  Register #(.width(32), .trigger("rising"), .Select("low")) register_17 (
    .D(EX_BranchAddr), .en(w0), .Q(register_17_q), .clk(clk));  // open: clr
  assign JumpAddr = L0 ? register_17_q : 32'bz;  // Controlled_Buffer controlled_buffer_1
  Register #(.width(32), .trigger("rising"), .Select("low")) register_18 (
    .D(EX_BranchAddr), .en(w1), .Q(register_18_q), .clk(clk));  // open: clr
  assign JumpAddr = L1 ? register_18_q : 32'bz;  // Controlled_Buffer controlled_buffer_2
  assign JumpAddr = L2 ? register_19_q : 32'bz;  // Controlled_Buffer controlled_buffer_3
  Register #(.width(32), .trigger("rising"), .Select("low")) register_19 (
    .D(EX_BranchAddr), .en(w2), .Q(register_19_q), .clk(clk));  // open: clr
  Register #(.width(32), .trigger("rising"), .Select("low")) register_20 (
    .D(EX_BranchAddr), .en(w3), .Q(register_20_q), .clk(clk));  // open: clr
  assign JumpAddr = L3 ? register_20_q : 32'bz;  // Controlled_Buffer controlled_buffer_4
  Register #(.width(32), .trigger("rising"), .Select("low")) register_21 (
    .D(EX_BranchAddr), .en(w4), .Q(register_21_q), .clk(clk));  // open: clr
  assign JumpAddr = L4 ? register_21_q : 32'bz;  // Controlled_Buffer controlled_buffer_5
  Register #(.width(32), .trigger("rising"), .Select("low")) register_22 (
    .D(EX_BranchAddr), .en(w5), .Q(register_22_q), .clk(clk));  // open: clr
  assign JumpAddr = L5 ? register_22_q : 32'bz;  // Controlled_Buffer controlled_buffer_6
  assign JumpAddr = L6 ? register_23_q : 32'bz;  // Controlled_Buffer controlled_buffer_7
  Register #(.width(32), .trigger("rising"), .Select("low")) register_23 (
    .D(EX_BranchAddr), .en(w6), .Q(register_23_q), .clk(clk));  // open: clr
  Register #(.width(32), .trigger("rising"), .Select("low")) register_24 (
    .D(EX_BranchAddr), .en(w7), .Q(register_24_q), .clk(clk));  // open: clr
  assign JumpAddr = L7 ? register_24_q : 32'bz;  // Controlled_Buffer controlled_buffer_8
  Comparator #(.width(32), .mode("unsigned")) comparator_1 (.a(EX_PC0), .b(PC), .eq(comparator_1_eq));  // open: gt, lt
  Comparator #(.width(32), .mode("unsigned")) comparator_2 (.a(EX_PC1), .b(PC), .eq(comparator_2_eq));  // open: gt, lt
  Comparator #(.width(32), .mode("unsigned")) comparator_3 (.a(EX_PC2), .b(PC), .eq(comparator_3_eq));  // open: gt, lt
  Comparator #(.width(32), .mode("unsigned")) comparator_4 (.a(EX_PC3), .b(PC), .eq(comparator_4_eq));  // open: gt, lt
  Comparator #(.width(32), .mode("unsigned")) comparator_5 (.a(EX_PC4), .b(PC), .eq(comparator_5_eq));  // open: gt, lt
  and and_1 (L0, v0, comparator_1_eq);
  and and_2 (L1, v1, comparator_2_eq);
  and and_3 (L2, v2, comparator_3_eq);
  and and_4 (L3, v3, comparator_4_eq);
  and and_5 (L4, v4, comparator_5_eq);
  and and_6 (L5, v5, comparator_6_eq);
  Comparator #(.width(32), .mode("unsigned")) comparator_6 (.a(EX_PC5), .b(PC), .eq(comparator_6_eq));  // open: gt, lt
  Comparator #(.width(32), .mode("unsigned")) comparator_7 (.a(EX_PC6), .b(PC), .eq(comparator_7_eq));  // open: gt, lt
  Comparator #(.width(32), .mode("unsigned")) comparator_8 (.a(EX_PC7), .b(PC), .eq(comparator_8_eq));  // open: gt, lt
  and and_7 (L6, v6, comparator_7_eq);
  and and_8 (L7, v7, comparator_8_eq);
  Comparator #(.width(32), .mode("unsigned")) comparator_9 (
    .a(EX_PC), .b(EX_PC0), .eq(comparator_9_eq));  // open: gt, lt
  Comparator #(.width(32), .mode("unsigned")) comparator_10 (
    .a(EX_PC), .b(EX_PC1), .eq(comparator_10_eq));  // open: gt, lt
  and and_9 (hit0, v0, comparator_9_eq);
  and and_10 (hit1, v1, comparator_10_eq);
  Comparator #(.width(32), .mode("unsigned")) comparator_11 (
    .a(EX_PC), .b(EX_PC2), .eq(comparator_11_eq));  // open: gt, lt
  Comparator #(.width(32), .mode("unsigned")) comparator_12 (
    .a(EX_PC), .b(EX_PC3), .eq(comparator_12_eq));  // open: gt, lt
  Comparator #(.width(32), .mode("unsigned")) comparator_13 (
    .a(EX_PC), .b(EX_PC4), .eq(comparator_13_eq));  // open: gt, lt
  Comparator #(.width(32), .mode("unsigned")) comparator_14 (
    .a(EX_PC), .b(EX_PC5), .eq(comparator_14_eq));  // open: gt, lt
  Comparator #(.width(32), .mode("unsigned")) comparator_15 (
    .a(EX_PC), .b(EX_PC6), .eq(comparator_15_eq));  // open: gt, lt
  Comparator #(.width(32), .mode("unsigned")) comparator_16 (
    .a(EX_PC), .b(EX_PC7), .eq(comparator_16_eq));  // open: gt, lt
  and and_11 (hit2, v2, comparator_11_eq);
  and and_12 (hit3, v3, comparator_12_eq);
  and and_13 (hit4, v4, comparator_13_eq);
  and and_14 (hit5, v5, comparator_14_eq);
  and and_15 (hit6, v6, comparator_15_eq);
  and and_16 (hit7, v7, comparator_16_eq);
  FSM fsm_1 (
    .high(predict0[1]), .low(predict0[0]), .jump(EX_BranchTaken), .NextHigh(fsm_1_nextlow[1]),
    .NextLow(fsm_1_nextlow[0]));
  FSM fsm_2 (
    .high(predict1[1]), .low(predict1[0]), .jump(EX_BranchTaken), .NextHigh(fsm_2_nextlow[1]),
    .NextLow(fsm_2_nextlow[0]));
  FSM fsm_3 (
    .high(predict2[1]), .low(predict2[0]), .jump(EX_BranchTaken), .NextHigh(fsm_3_nextlow[1]),
    .NextLow(fsm_3_nextlow[0]));
  FSM fsm_4 (
    .high(predict3[1]), .low(predict3[0]), .jump(EX_BranchTaken), .NextHigh(fsm_4_nextlow[1]),
    .NextLow(fsm_4_nextlow[0]));
  and and_17 (and_17_out, EX_branch, hit0);
  and and_18 (and_18_out, EX_branch, hit1);
  and and_19 (and_19_out, EX_branch, hit2);
  and and_20 (and_20_out, EX_branch, hit3);
  FSM fsm_5 (
    .high(predict4[1]), .low(predict4[0]), .jump(EX_BranchTaken), .NextHigh(fsm_5_nextlow[1]),
    .NextLow(fsm_5_nextlow[0]));
  FSM fsm_6 (
    .high(predict5[1]), .low(predict5[0]), .jump(EX_BranchTaken), .NextHigh(fsm_6_nextlow[1]),
    .NextLow(fsm_6_nextlow[0]));
  FSM fsm_7 (
    .high(predict6[1]), .low(predict6[0]), .jump(EX_BranchTaken), .NextHigh(fsm_7_nextlow[1]),
    .NextLow(fsm_7_nextlow[0]));
  FSM fsm_8 (
    .high(predict7[1]), .low(predict7[0]), .jump(EX_BranchTaken), .NextHigh(fsm_8_nextlow[1]),
    .NextLow(fsm_8_nextlow[0]));
  Register #(.width(2), .trigger("rising"), .Select("low")) register_25 (
    .D(fsm_1_nextlow), .en(and_17_out), .Q(predict0), .clk(clk));  // open: clr
  Register #(.width(2), .trigger("rising"), .Select("low")) register_26 (
    .D(fsm_2_nextlow), .en(and_18_out), .Q(predict1), .clk(clk));  // open: clr
  Register #(.width(2), .trigger("rising"), .Select("low")) register_27 (
    .D(fsm_3_nextlow), .en(and_19_out), .Q(predict2), .clk(clk));  // open: clr
  Register #(.width(2), .trigger("rising"), .Select("low")) register_28 (
    .D(fsm_4_nextlow), .en(and_20_out), .Q(predict3), .clk(clk));  // open: clr
  and and_21 (and_21_out, EX_branch, hit4);
  and and_22 (and_22_out, EX_branch, hit5);
  and and_23 (and_23_out, EX_branch, hit6);
  and and_24 (and_24_out, EX_branch, hit7);
  Register #(.width(2), .trigger("rising"), .Select("low")) register_29 (
    .D(fsm_5_nextlow), .en(and_21_out), .Q(predict4), .clk(clk));  // open: clr
  Register #(.width(2), .trigger("rising"), .Select("low")) register_30 (
    .D(fsm_6_nextlow), .en(and_22_out), .Q(predict5), .clk(clk));  // open: clr
  Register #(.width(2), .trigger("rising"), .Select("low")) register_31 (
    .D(fsm_7_nextlow), .en(and_23_out), .Q(predict6), .clk(clk));  // open: clr
  Register #(.width(2), .trigger("rising"), .Select("low")) register_32 (
    .D(fsm_8_nextlow), .en(and_24_out), .Q(predict7), .clk(clk));  // open: clr
  MAX max_1 (.X(c0), .Y(c1), .xIndex(3'b000), .yIndex(3'b001), .MAX(max_1_max), .maxIndex(max_1_maxindex));
  MAX max_2 (.X(c2), .Y(c3), .xIndex(3'b010), .yIndex(3'b011), .MAX(max_2_max), .maxIndex(max_2_maxindex));
  MAX max_3 (.X(c4), .Y(c5), .xIndex(3'b100), .yIndex(3'b101), .MAX(max_3_max), .maxIndex(max_3_maxindex));
  MAX max_4 (.X(c6), .Y(c7), .xIndex(3'b110), .yIndex(3'b111), .MAX(max_4_max), .maxIndex(max_4_maxindex));
  not not_1 (not_1_out, v0);
  not not_2 (not_2_out, v1);
  not not_3 (not_3_out, v2);
  not not_4 (not_4_out, v3);
  not not_5 (not_5_out, v4);
  not not_6 (not_6_out, v5);
  not not_7 (not_7_out, v6);
  not not_8 (not_8_out, v7);
  MAX max_5 (
    .X(max_1_max), .Y(max_2_max), .xIndex(max_1_maxindex), .yIndex(max_2_maxindex), .MAX(max_5_max),
    .maxIndex(max_5_maxindex));
  Decoder #(.select(3), .tristate("false"), .disabled(0), .enable("true")) decoder_1 (
    .out0(decoder_1_out0), .out1(decoder_1_out1), .out2(decoder_1_out2), .out3(decoder_1_out3),
    .out4(decoder_1_out4), .out5(decoder_1_out5), .out6(decoder_1_out6), .out7(decoder_1_out7),
    .sel(LRUIndex), .en(isFull));
  Priority_Encoder #(.select(3), .disabled("Z")) priority_encoder_1 (
    .in0(not_1_out), .in1(not_2_out), .in2(not_3_out), .in3(not_4_out), .in4(not_5_out), .in5(not_6_out),
    .in6(not_7_out), .in7(not_8_out), .out(priority_encoder_1_out), .gs(priority_encoder_1_gs));  // open: en_out, en_in
  and and_25 (isFull, v1, v0, v2, v3, v6, v4, v7, v5);
  MAX max_6 (
    .X(max_5_max), .Y(max_7_max), .xIndex(max_5_maxindex), .yIndex(max_7_maxindex), .maxIndex(LRUIndex));  // open: MAX
  MAX max_7 (
    .X(max_3_max), .Y(max_4_max), .xIndex(max_3_maxindex), .yIndex(max_4_maxindex), .MAX(max_7_max),
    .maxIndex(max_7_maxindex));
  Decoder #(.select(3), .tristate("false"), .disabled(0), .enable("true")) decoder_2 (
    .out0(decoder_2_out0), .out1(decoder_2_out1), .out2(decoder_2_out2), .out3(decoder_2_out3),
    .out4(decoder_2_out4), .out5(decoder_2_out5), .out6(decoder_2_out6), .out7(decoder_2_out7),
    .sel(priority_encoder_1_out), .en(priority_encoder_1_gs));
  assign PredictJump = L0 ? predict0[1] : 1'bz;  // Controlled_Buffer controlled_buffer_9
  assign PredictJump = L1 ? predict1[1] : 1'bz;  // Controlled_Buffer controlled_buffer_10
  assign PredictJump = L2 ? predict2[1] : 1'bz;  // Controlled_Buffer controlled_buffer_11
  assign PredictJump = L3 ? predict3[1] : 1'bz;  // Controlled_Buffer controlled_buffer_12
  assign PredictJump = L4 ? predict4[1] : 1'bz;  // Controlled_Buffer controlled_buffer_13
  assign PredictJump = L5 ? predict5[1] : 1'bz;  // Controlled_Buffer controlled_buffer_14
  assign PredictJump = L6 ? predict6[1] : 1'bz;  // Controlled_Buffer controlled_buffer_15
  assign PredictJump = L7 ? predict7[1] : 1'bz;  // Controlled_Buffer controlled_buffer_16
  Pull_Resistor #(.pull(0)) pull_resistor_1 (.node(PredictJump));
  or or_9 (or_9_out, decoder_1_out0, decoder_2_out0);
  or or_10 (or_10_out, decoder_1_out1, decoder_2_out1);
  or or_11 (or_11_out, decoder_1_out2, decoder_2_out2);
  or or_12 (or_12_out, decoder_1_out3, decoder_2_out3);
  or or_13 (or_13_out, decoder_1_out4, decoder_2_out4);
  or or_14 (or_14_out, decoder_1_out5, decoder_2_out5);
  or or_15 (or_15_out, decoder_1_out6, decoder_2_out6);
  or or_16 (or_16_out, decoder_1_out7, decoder_2_out7);
  and and_26 (w0, Miss, or_9_out, EX_branch);
  and and_27 (w1, Miss, or_10_out, EX_branch);
  and and_28 (w2, Miss, or_11_out, EX_branch);
  and and_29 (w3, Miss, or_12_out, EX_branch);
  and and_30 (w4, Miss, or_13_out, EX_branch);
  and and_31 (w5, Miss, or_14_out, EX_branch);
  and and_32 (w6, Miss, or_15_out, EX_branch);
  and and_33 (w7, Miss, or_16_out, EX_branch);
  or or_17 (Hit, hit0, hit1, hit2, hit3, hit5, hit4, hit6, hit7);
  not not_9 (Miss, Hit);
endmodule

module FSM (
  input  high,
  input  low,
  input  jump,
  output NextHigh,
  output NextLow
);

  wire and_1_out, and_2_out, and_3_out, and_4_out, not_1_out, not_2_out, not_3_out, not_4_out, not_5_out;

  not not_1 (not_1_out, low);
  not not_2 (not_2_out, high);
  not not_3 (not_3_out, low);
  not not_4 (not_4_out, low);
  not not_5 (not_5_out, jump);
  and and_1 (and_1_out, low, jump);
  and and_2 (and_2_out, high, not_1_out);
  and and_3 (and_3_out, not_2_out, not_3_out, jump);
  and and_4 (and_4_out, high, not_4_out, not_5_out);
  or or_1 (NextHigh, and_1_out, and_2_out);
  or or_2 (NextLow, and_3_out, and_4_out);
endmodule

module MAX (
  input  [15:0] X,
  input  [15:0] Y,
  input  [2:0] yIndex,
  input  [2:0] xIndex,
  output [15:0] MAX,
  output [2:0] maxIndex
);

  wire comparator_1_eq, comparator_1_gt, or_1_out;

  Comparator #(.width(16), .mode("unsigned")) comparator_1 (
    .a(X), .b(Y), .gt(comparator_1_gt), .eq(comparator_1_eq));  // open: lt
  Multiplexer #(.select(1), .width(16), .disabled("Z"), .enable("false")) multiplexer_1 (
    .in0(X), .in1(Y), .out(MAX), .sel(or_1_out));
  or or_1 (or_1_out, comparator_1_gt, comparator_1_eq);
  Multiplexer #(.select(1), .width(3), .disabled("Z"), .enable("false")) multiplexer_2 (
    .in0(yIndex), .in1(xIndex), .out(maxIndex), .sel(or_1_out));
endmodule
